// Logisim project CBRLAB4.circ as structural Verilog: 13 circuits, main circuit main
module Half_Adder (
  input  A,
  input  B,
  output SUM,
  output Carry
);

  xor xor_1 (SUM, A, B);
  and and_1 (Carry, A, B);
endmodule

module Full_Adder (
  input  in_1,
  input  in_2,
  input  in_3,
  output out_4,
  output out_5
);

  wire Half_Adder_2_carry, Half_Adder_carry, Half_Adder_sum;

  Half_Adder Half_Adder (.A(in_2), .B(in_3), .SUM(Half_Adder_sum), .Carry(Half_Adder_carry));
  Half_Adder Half_Adder_2 (.A(in_1), .B(Half_Adder_sum), .SUM(out_4), .Carry(Half_Adder_2_carry));
  or or_1 (out_5, Half_Adder_2_carry, Half_Adder_carry);
endmodule

module _4_Bit_Adder_by_FA (
  input  [3:0] in_1,
  input  [3:0] in_2,
  input  in_3,
  output out_4,
  output [3:0] out_5
);

  wire full_adder_2_out_5, full_adder_3_out_5, full_adder_4_out_5;

  Full_Adder full_adder_1 (.in_2(in_1[3]), .in_3(in_2[3]), .in_1(full_adder_2_out_5), .out_4(out_5[3]), .out_5(out_4));
  Full_Adder full_adder_2 (
    .in_2(in_1[2]), .in_3(in_2[2]), .in_1(full_adder_3_out_5), .out_4(out_5[2]), .out_5(full_adder_2_out_5));
  Full_Adder full_adder_3 (
    .in_2(in_1[1]), .in_3(in_2[1]), .in_1(full_adder_4_out_5), .out_4(out_5[1]), .out_5(full_adder_3_out_5));
  Full_Adder full_adder_4 (.in_2(in_1[0]), .in_3(in_2[0]), .in_1(in_3), .out_4(out_5[0]), .out_5(full_adder_4_out_5));
endmodule

module _2_Bit_Adder_by_TT (
  input  in_1,
  input  in_2,
  input  in_3,
  input  in_4,
  output out_5,
  output out_6,
  output out_7
);

  f0 f0_1 (.in_1(in_2), .in_2(in_4), .out_3(out_6));
  f1 f1_1 (.in_1(in_1), .in_2(in_2), .in_3(in_3), .in_4(in_4), .out_5(out_5));
  f2 f2_1 (.in_1(in_1), .in_2(in_2), .in_3(in_3), .in_4(in_4), .out_5(out_7));
endmodule

module main (
  input  [3:0] in_1,
  input  [3:0] in_2,
  input  in_3,
  input  in_4,
  input  in_5,
  input  in_6,
  input  [7:0] in_7,
  input  [7:0] in_8,
  input  in_9,
  input  [7:0] in_10,
  input  [7:0] in_11,
  input  [3:0] in_12,
  input  [3:0] in_13,
  input  in_14,
  output out_15,
  output out_16,
  output out_17,
  output out_18,
  output [3:0] out_19,
  output out_20,
  output [7:0] out_21,
  output out_22,
  output [7:0] out_23,
  output out_24,
  output [7:0] out_25
);

  // Probe on in_1
  // Probe on in_10
  _4_Bit_Adder_by_FA u_4_bit_adder_by_fa_1 (.out_4(out_18), .in_1(in_1), .in_2(in_2), .out_5(out_19), .in_3(1'b0));
  // Probe on out_19
  // Probe on in_2
  _8_Bit_Adder_by_FA u_8_bit_adder_by_fa_1 (.out_4(out_22), .in_3(1'b0), .in_1(in_10), .in_2(in_11), .out_5(out_23));
  // Probe on out_23
  _2_Bit_Adder_by_TT u_2_bit_adder_by_tt_1 (
    .in_1(in_3), .in_2(in_4), .in_3(in_5), .in_4(in_6), .out_7(out_15), .out_5(out_16), .out_6(out_17));
  // Probe on in_11
  // Probe on in_7
  // Probe on in_12
  Markiplier markiplier_1 (.in_1(in_12), .in_2(in_13), .in_3(in_14), .out_5(out_25), .out_4(out_24));
  // Probe on out_25
  // Probe on out_25
  Subtracting_Adder subtracting_adder_1 (.in_3(in_9), .in_1(in_7), .in_2(in_8), .out_4(out_20), .out_5(out_21));
  // Probe on in_13
  // Probe on in_8
  // Probe on out_21
  // Probe on out_21

  // Notes on the sheet:
  //   Вычитатор попросили назвать креативно.
  //   Так что этого вычитатора зовут Андрей
endmodule

module f0 (
  input  in_1,
  input  in_2,
  output out_3
);

  wire and_1_out, and_2_out, not_1_out, not_2_out;

  not not_1 (not_1_out, in_2);
  not not_2 (not_2_out, in_1);
  and and_1 (and_1_out, in_1, not_1_out);
  and and_2 (and_2_out, not_2_out, in_2);
  or or_1 (out_3, and_1_out, and_2_out);
endmodule

module f1 (
  input  in_1,
  input  in_2,
  input  in_3,
  input  in_4,
  output out_5
);

  wire and_1_out, and_2_out, and_3_out, and_4_out, and_5_out, and_6_out, not_1_out, not_2_out, not_3_out,
       not_4_out, not_5_out, not_6_out, not_7_out, not_8_out, not_9_out, not_10_out;

  not not_1 (not_1_out, in_3);
  and and_1 (and_1_out, in_1, not_1_out, not_2_out);
  not not_2 (not_2_out, in_4);
  not not_3 (not_3_out, in_2);
  and and_2 (and_2_out, in_1, not_3_out, not_4_out);
  not not_4 (not_4_out, in_3);
  not not_5 (not_5_out, in_1);
  and and_3 (and_3_out, not_5_out, not_6_out, in_3);
  not not_6 (not_6_out, in_2);
  not not_7 (not_7_out, in_1);
  and and_4 (and_4_out, not_7_out, in_3, not_8_out);
  not not_8 (not_8_out, in_4);
  not not_9 (not_9_out, in_1);
  and and_5 (and_5_out, not_9_out, in_2, not_10_out, in_4);
  not not_10 (not_10_out, in_3);
  and and_6 (and_6_out, in_1, in_2, in_3, in_4);
  or or_1 (out_5, and_1_out, and_2_out, and_3_out, and_4_out, and_5_out, and_6_out);
endmodule

module f2 (
  input  in_1,
  input  in_2,
  input  in_3,
  input  in_4,
  output out_5
);

  wire and_1_out, and_2_out, and_3_out, and_4_out, and_5_out;

  and and_1 (and_1_out, in_1, in_3);
  and and_2 (and_2_out, in_1, in_3, in_4);
  and and_3 (and_3_out, in_2, in_3, in_4);
  and and_4 (and_4_out, in_1, in_2, in_3);
  and and_5 (and_5_out, in_1, in_2, in_4);
  or or_1 (out_5, and_1_out, and_2_out, and_3_out, and_4_out, and_5_out);
endmodule

module _8_Bit_Adder_by_FA (
  input  [7:0] in_1,
  input  [7:0] in_2,
  input  in_3,
  output out_4,
  output [7:0] out_5
);

  wire full_adder_2_out_5, full_adder_3_out_5, full_adder_4_out_5, full_adder_5_out_5, full_adder_6_out_5,
       full_adder_7_out_5, full_adder_8_out_5;

  Full_Adder full_adder_1 (.in_2(in_1[7]), .in_3(in_2[7]), .in_1(full_adder_2_out_5), .out_4(out_5[7]), .out_5(out_4));
  Full_Adder full_adder_2 (
    .in_2(in_1[6]), .in_3(in_2[6]), .in_1(full_adder_3_out_5), .out_4(out_5[6]), .out_5(full_adder_2_out_5));
  Full_Adder full_adder_3 (
    .in_2(in_1[5]), .in_3(in_2[5]), .in_1(full_adder_4_out_5), .out_4(out_5[5]), .out_5(full_adder_3_out_5));
  Full_Adder full_adder_4 (
    .in_2(in_1[4]), .in_3(in_2[4]), .in_1(full_adder_5_out_5), .out_4(out_5[4]), .out_5(full_adder_4_out_5));
  Full_Adder full_adder_5 (
    .in_2(in_1[3]), .in_3(in_2[3]), .in_1(full_adder_6_out_5), .out_4(out_5[3]), .out_5(full_adder_5_out_5));
  Full_Adder full_adder_6 (
    .in_2(in_1[2]), .in_3(in_2[2]), .in_1(full_adder_7_out_5), .out_4(out_5[2]), .out_5(full_adder_6_out_5));
  Full_Adder full_adder_7 (
    .in_2(in_1[1]), .in_3(in_2[1]), .in_1(full_adder_8_out_5), .out_4(out_5[1]), .out_5(full_adder_7_out_5));
  Full_Adder full_adder_8 (.in_2(in_1[0]), .in_3(in_2[0]), .in_1(in_3), .out_4(out_5[0]), .out_5(full_adder_8_out_5));
endmodule

module Subtracting_Adder (
  input  [7:0] in_1,
  input  [7:0] in_2,
  input  in_3,
  output out_4,
  output [7:0] out_5
);

  wire n8_bit_adder_by_fa_1_out_4;
  wire [7:0] togglable_invertor_1_out_3;

  xor xor_1 (out_4, in_3, n8_bit_adder_by_fa_1_out_4);
  // Probe on in_1
  // Probe on in_1
  _8_Bit_Adder_by_FA u_8_bit_adder_by_fa_1 (
    .out_4(n8_bit_adder_by_fa_1_out_4), .in_3(in_3), .in_1(in_1), .in_2(togglable_invertor_1_out_3),
    .out_5(out_5));
  // Probe on out_5
  // Probe on out_5
  Togglable_Invertor togglable_invertor_1 (.in_2(in_3), .in_1(in_2), .out_3(togglable_invertor_1_out_3));
  // Probe on togglable_invertor_1_out_3
  // Probe on togglable_invertor_1_out_3
endmodule

module Togglable_Invertor (
  input  [7:0] in_1,
  input  in_2,
  output [7:0] out_3
);

  xor xor_1 (out_3[7], in_1[7], in_2);
  xor xor_2 (out_3[6], in_1[6], in_2);
  xor xor_3 (out_3[5], in_1[5], in_2);
  xor xor_4 (out_3[4], in_1[4], in_2);
  xor xor_5 (out_3[3], in_1[3], in_2);
  xor xor_6 (out_3[2], in_1[2], in_2);
  xor xor_7 (out_3[0], in_1[0], in_2);
  xor xor_8 (out_3[1], in_1[1], in_2);
endmodule

module Markiplier (
  input  [3:0] in_1,
  input  [3:0] in_2,
  input  in_3,
  output out_4,
  output [7:0] out_5
);

  wire [0:0] markiplier_subcircuit_4_out_3, n4_bit_adder_by_fa_2_out_5_2, n4_bit_adder_by_fa_3_out_5_2;
  wire [2:0] markiplier_subcircuit_4_out_3_2;
  wire [3:0] markiplier_subcircuit_1_out_3, markiplier_subcircuit_2_out_3, markiplier_subcircuit_3_out_3,
       n4_bit_adder_by_fa_1_out_5, n4_bit_adder_by_fa_2_out_5, n4_bit_adder_by_fa_3_out_5;
  wire [7:0] togglable_invertor_1_out_3;

  // Probe on in_1
  // Probe on in_2
  Markiplier_subcircuit markiplier_subcircuit_1 (.in_2(in_2[3]), .in_1(in_1), .out_3(markiplier_subcircuit_1_out_3));
  Markiplier_subcircuit markiplier_subcircuit_2 (.in_2(in_2[2]), .in_1(in_1), .out_3(markiplier_subcircuit_2_out_3));
  _4_Bit_Adder_by_FA u_4_bit_adder_by_fa_1 (
    .out_4(out_4), .in_1(markiplier_subcircuit_1_out_3), .in_2(n4_bit_adder_by_fa_2_out_5),
    .out_5(n4_bit_adder_by_fa_1_out_5), .in_3(1'b0));
  Markiplier_subcircuit markiplier_subcircuit_3 (.in_2(in_2[1]), .in_1(in_1), .out_3(markiplier_subcircuit_3_out_3));
  _4_Bit_Adder_by_FA u_4_bit_adder_by_fa_2 (
    .out_4(n4_bit_adder_by_fa_2_out_5[3]), .in_1(markiplier_subcircuit_2_out_3),
    .in_2(n4_bit_adder_by_fa_3_out_5),
    .out_5({n4_bit_adder_by_fa_2_out_5[2:0], n4_bit_adder_by_fa_2_out_5_2[0]}), .in_3(1'b0));
  _8_Bit_Adder_by_FA u_8_bit_adder_by_fa_1 (
    .in_3(in_3), .in_1({8{1'b0}}), .in_2(togglable_invertor_1_out_3), .out_5(out_5));  // open: out_4
  // Probe on out_5
  // Probe on out_5
  _4_Bit_Adder_by_FA u_4_bit_adder_by_fa_3 (
    .out_4(n4_bit_adder_by_fa_3_out_5[3]), .in_1(markiplier_subcircuit_3_out_3),
    .in_2({1'b0, markiplier_subcircuit_4_out_3_2}),
    .out_5({n4_bit_adder_by_fa_3_out_5[2:0], n4_bit_adder_by_fa_3_out_5_2[0]}), .in_3(1'b0));
  // Probe on {out_4, n4_bit_adder_by_fa_1_out_5, n4_bit_adder_by_fa_2_out_5_2[0], n4_bit_adder_by_fa_3_out_5_2[0], markiplier_subcircuit_4_out_3[0]}
  Togglable_Invertor togglable_invertor_1 (
    .in_2(in_3),
    .in_1({out_4, n4_bit_adder_by_fa_1_out_5, n4_bit_adder_by_fa_2_out_5_2[0], n4_bit_adder_by_fa_3_out_5_2[0], markiplier_subcircuit_4_out_3[0]}),
    .out_3(togglable_invertor_1_out_3));
  Markiplier_subcircuit markiplier_subcircuit_4 (
    .in_2(in_2[0]), .in_1(in_1), .out_3({markiplier_subcircuit_4_out_3_2, markiplier_subcircuit_4_out_3[0]}));
endmodule

module Markiplier_subcircuit (
  input  [3:0] in_1,
  input  in_2,
  output [3:0] out_3
);

  and and_1 (out_3[2], in_1[2], in_2);
  and and_2 (out_3[3], in_1[3], in_2);
  and and_3 (out_3[0], in_1[0], in_2);
  and and_4 (out_3[1], in_1[1], in_2);
endmodule
