// Logisim project CBRLAB5++.circ as structural Verilog: 8 circuits, main circuit main
module main (
);

  wire _0_out, _1_out, _2_out, _3_out, _4_out, _5_out, _6_out, _7_out, _8_out, _9_out, A_out, B_out, C_out,
       Clear_out, D_out, E_out, F_out, n16btn_to_hex_1_out_17, not_2_out, or_1_out, Reboot_Display_out;
  wire [3:0] and_1_out, n4bit_mem_1_out_4, n4bit_mem_2_out_4, n4bit_mem_3_out_4, n4bit_mem_4_out_4,
       n4bit_mem_5_out_4, n4bit_mem_6_out_4, n4bit_mem_7_out_4, n4bit_mem_8_out_4, n16btn_to_hex_1_out_16;
  wire [3:3] not_1_out;
  wire [7:0] hex_to_7seg_1_out_3, hex_to_7seg_2_out_3, hex_to_7seg_3_out_3, hex_to_7seg_4_out_3,
       hex_to_7seg_5_out_3, hex_to_7seg_6_out_3, hex_to_7seg_7_out_3, hex_to_7seg_8_out_3;

  Button _0 (.out(_0_out));
  Button _1 (.out(_1_out));
  Button _5 (.out(_5_out));
  Button _4 (.out(_4_out));
  Button _9 (.out(_9_out));
  Button _8 (.out(_8_out));
  Button C (.out(C_out));
  Button D (.out(D_out));
  Button Clear (.out(Clear_out));
  Button _2 (.out(_2_out));
  Button _3 (.out(_3_out));
  Button _7 (.out(_7_out));
  Button _6 (.out(_6_out));
  Button B (.out(B_out));
  Button A (.out(A_out));
  Button F (.out(F_out));
  Button E (.out(E_out));
  not not_1 (not_1_out[3], _0_out);
  _16btn_to_hex u_16btn_to_hex_1 (
    ._1(_1_out), ._2(_2_out), ._3(_3_out), ._4(_4_out), ._5(_5_out), ._6(_6_out), ._7(_7_out), ._8(_8_out),
    ._9(_9_out), .A(A_out), .B(B_out), .C(C_out), .D(D_out), .E(E_out), .F(F_out),
    .out_16(n16btn_to_hex_1_out_16), .out_17(n16btn_to_hex_1_out_17));
  Button Reboot_Display (.out(Reboot_Display_out));
  hex_to_7seg hex_to_7seg_1 (.in_1(n4bit_mem_8_out_4), .out_3(hex_to_7seg_1_out_3), .in_2(Reboot_Display_out));
  assign and_1_out = {4{not_1_out[3]}} & n16btn_to_hex_1_out_16;  // AND_Gate and_1, 4 bits wide
  or or_1 (or_1_out, _0_out, n16btn_to_hex_1_out_17);
  _7_Segment_Display u_7_segment_display_1 (
    .g(hex_to_7seg_1_out_3[0]), .f(hex_to_7seg_1_out_3[1]), .a(hex_to_7seg_1_out_3[2]),
    .b(hex_to_7seg_1_out_3[3]), .e(hex_to_7seg_1_out_3[4]), .d(hex_to_7seg_1_out_3[5]),
    .c(hex_to_7seg_1_out_3[6]), .dp(hex_to_7seg_1_out_3[7]));
  hex_to_7seg hex_to_7seg_2 (.in_1(n4bit_mem_7_out_4), .out_3(hex_to_7seg_2_out_3), .in_2(Reboot_Display_out));
  not not_2 (not_2_out, or_1_out);
  _7_Segment_Display u_7_segment_display_2 (
    .g(hex_to_7seg_2_out_3[0]), .f(hex_to_7seg_2_out_3[1]), .a(hex_to_7seg_2_out_3[2]),
    .b(hex_to_7seg_2_out_3[3]), .e(hex_to_7seg_2_out_3[4]), .d(hex_to_7seg_2_out_3[5]),
    .c(hex_to_7seg_2_out_3[6]), .dp(hex_to_7seg_2_out_3[7]));
  _4bit_MEM u_4bit_mem_1 (.in_1(and_1_out), .in_2(Clear_out), .in_3(not_2_out), .out_4(n4bit_mem_1_out_4));
  // Probe on n4bit_mem_1_out_4
  _4bit_MEM u_4bit_mem_2 (.in_1(n4bit_mem_1_out_4), .in_2(Clear_out), .in_3(not_2_out), .out_4(n4bit_mem_2_out_4));
  // Probe on n4bit_mem_2_out_4
  // Probe on n4bit_mem_3_out_4
  _4bit_MEM u_4bit_mem_3 (.in_1(n4bit_mem_2_out_4), .in_2(Clear_out), .in_3(not_2_out), .out_4(n4bit_mem_3_out_4));
  _4bit_MEM u_4bit_mem_4 (.in_1(n4bit_mem_3_out_4), .in_2(Clear_out), .in_3(not_2_out), .out_4(n4bit_mem_4_out_4));
  // Probe on n4bit_mem_4_out_4
  _4bit_MEM u_4bit_mem_5 (.in_1(n4bit_mem_4_out_4), .in_2(Clear_out), .in_3(not_2_out), .out_4(n4bit_mem_5_out_4));
  // Probe on n4bit_mem_5_out_4
  _4bit_MEM u_4bit_mem_6 (.in_1(n4bit_mem_5_out_4), .in_2(Clear_out), .in_3(not_2_out), .out_4(n4bit_mem_6_out_4));
  // Probe on n4bit_mem_6_out_4
  _4bit_MEM u_4bit_mem_7 (.in_1(n4bit_mem_6_out_4), .in_2(Clear_out), .in_3(not_2_out), .out_4(n4bit_mem_7_out_4));
  // Probe on n4bit_mem_7_out_4
  _4bit_MEM u_4bit_mem_8 (.in_1(n4bit_mem_7_out_4), .in_2(Clear_out), .in_3(not_2_out), .out_4(n4bit_mem_8_out_4));
  // Probe on n4bit_mem_8_out_4
  _7_Segment_Display u_7_segment_display_3 (
    .g(hex_to_7seg_3_out_3[0]), .f(hex_to_7seg_3_out_3[1]), .a(hex_to_7seg_3_out_3[2]),
    .b(hex_to_7seg_3_out_3[3]), .e(hex_to_7seg_3_out_3[4]), .d(hex_to_7seg_3_out_3[5]),
    .c(hex_to_7seg_3_out_3[6]), .dp(hex_to_7seg_3_out_3[7]));
  hex_to_7seg hex_to_7seg_3 (.in_1(n4bit_mem_6_out_4), .out_3(hex_to_7seg_3_out_3), .in_2(Reboot_Display_out));
  _7_Segment_Display u_7_segment_display_4 (
    .g(hex_to_7seg_4_out_3[0]), .f(hex_to_7seg_4_out_3[1]), .a(hex_to_7seg_4_out_3[2]),
    .b(hex_to_7seg_4_out_3[3]), .e(hex_to_7seg_4_out_3[4]), .d(hex_to_7seg_4_out_3[5]),
    .c(hex_to_7seg_4_out_3[6]), .dp(hex_to_7seg_4_out_3[7]));
  hex_to_7seg hex_to_7seg_4 (.in_1(n4bit_mem_5_out_4), .out_3(hex_to_7seg_4_out_3), .in_2(Reboot_Display_out));
  _7_Segment_Display u_7_segment_display_5 (
    .g(hex_to_7seg_5_out_3[0]), .f(hex_to_7seg_5_out_3[1]), .a(hex_to_7seg_5_out_3[2]),
    .b(hex_to_7seg_5_out_3[3]), .e(hex_to_7seg_5_out_3[4]), .d(hex_to_7seg_5_out_3[5]),
    .c(hex_to_7seg_5_out_3[6]), .dp(hex_to_7seg_5_out_3[7]));
  hex_to_7seg hex_to_7seg_5 (.in_1(n4bit_mem_4_out_4), .out_3(hex_to_7seg_5_out_3), .in_2(Reboot_Display_out));
  hex_to_7seg hex_to_7seg_6 (.in_1(n4bit_mem_3_out_4), .out_3(hex_to_7seg_6_out_3), .in_2(Reboot_Display_out));
  _7_Segment_Display u_7_segment_display_6 (
    .g(hex_to_7seg_6_out_3[0]), .f(hex_to_7seg_6_out_3[1]), .a(hex_to_7seg_6_out_3[2]),
    .b(hex_to_7seg_6_out_3[3]), .e(hex_to_7seg_6_out_3[4]), .d(hex_to_7seg_6_out_3[5]),
    .c(hex_to_7seg_6_out_3[6]), .dp(hex_to_7seg_6_out_3[7]));
  hex_to_7seg hex_to_7seg_7 (.in_1(n4bit_mem_2_out_4), .out_3(hex_to_7seg_7_out_3), .in_2(Reboot_Display_out));
  _7_Segment_Display u_7_segment_display_7 (
    .g(hex_to_7seg_7_out_3[0]), .f(hex_to_7seg_7_out_3[1]), .a(hex_to_7seg_7_out_3[2]),
    .b(hex_to_7seg_7_out_3[3]), .e(hex_to_7seg_7_out_3[4]), .d(hex_to_7seg_7_out_3[5]),
    .c(hex_to_7seg_7_out_3[6]), .dp(hex_to_7seg_7_out_3[7]));
  hex_to_7seg hex_to_7seg_8 (.in_1(n4bit_mem_1_out_4), .out_3(hex_to_7seg_8_out_3), .in_2(Reboot_Display_out));
  _7_Segment_Display u_7_segment_display_8 (
    .g(hex_to_7seg_8_out_3[0]), .f(hex_to_7seg_8_out_3[1]), .a(hex_to_7seg_8_out_3[2]),
    .b(hex_to_7seg_8_out_3[3]), .e(hex_to_7seg_8_out_3[4]), .d(hex_to_7seg_8_out_3[5]),
    .c(hex_to_7seg_8_out_3[6]), .dp(hex_to_7seg_8_out_3[7]));
endmodule

module hex_to_7seg (
  input  [3:0] in_1,
  input  in_2,
  output [7:0] out_3
);

  wire and_1_out, and_2_out, and_3_out, and_4_out, and_5_out, and_6_out, and_7_out, and_8_out, and_9_out,
       and_10_out, and_11_out, and_12_out, and_13_out, and_14_out, and_15_out, and_16_out, and_17_out,
       and_18_out, and_19_out, and_20_out, and_21_out, and_22_out, and_23_out, and_24_out, and_25_out,
       and_26_out, and_27_out, and_28_out, and_29_out, and_30_out, and_31_out, and_32_out, and_33_out,
       and_34_out, and_35_out, not_1_out, not_2_out, not_3_out, not_4_out, not_5_out, not_6_out, not_7_out,
       not_8_out, not_9_out, not_10_out, not_11_out, not_12_out, not_13_out, not_14_out, not_15_out,
       not_16_out, not_17_out, not_18_out, not_19_out, not_20_out, not_21_out, not_22_out, not_23_out,
       not_24_out, not_25_out, not_26_out, not_27_out, not_28_out, not_29_out, not_30_out, not_31_out,
       not_32_out, not_33_out, not_34_out, not_35_out, not_36_out, not_37_out, not_38_out, not_39_out,
       not_40_out, not_41_out, not_42_out, not_43_out, xor_1_out, xor_2_out, xor_3_out, xor_4_out;

  xor xor_1 (xor_1_out, in_1[3], in_2);
  xor xor_2 (xor_2_out, in_1[2], in_2);
  xor xor_3 (xor_3_out, in_1[1], in_2);
  xor xor_4 (xor_4_out, in_1[0], in_2);
  not not_1 (not_1_out, xor_1_out);
  not not_2 (not_2_out, xor_3_out);
  not not_3 (not_3_out, xor_1_out);
  not not_4 (not_4_out, xor_3_out);
  not not_5 (not_5_out, xor_1_out);
  not not_6 (not_6_out, xor_2_out);
  not not_7 (not_7_out, xor_1_out);
  not not_8 (not_8_out, xor_2_out);
  not not_9 (not_9_out, xor_4_out);
  not not_10 (not_10_out, xor_2_out);
  not not_11 (not_11_out, xor_3_out);
  not not_12 (not_12_out, xor_4_out);
  not not_13 (not_13_out, xor_3_out);
  not not_14 (not_14_out, xor_2_out);
  not not_15 (not_15_out, xor_4_out);
  not not_16 (not_16_out, xor_4_out);
  not not_17 (not_17_out, xor_1_out);
  not not_18 (not_18_out, xor_2_out);
  not not_19 (not_19_out, xor_1_out);
  not not_20 (not_20_out, xor_3_out);
  not not_21 (not_21_out, xor_4_out);
  not not_22 (not_22_out, xor_2_out);
  not not_23 (not_23_out, xor_4_out);
  not not_24 (not_24_out, xor_1_out);
  not not_25 (not_25_out, xor_3_out);
  not not_26 (not_26_out, xor_2_out);
  not not_27 (not_27_out, xor_4_out);
  not not_28 (not_28_out, xor_1_out);
  not not_29 (not_29_out, xor_1_out);
  not not_30 (not_30_out, xor_2_out);
  not not_31 (not_31_out, xor_3_out);
  not not_32 (not_32_out, xor_4_out);
  not not_33 (not_33_out, xor_3_out);
  not not_34 (not_34_out, xor_4_out);
  not not_35 (not_35_out, xor_1_out);
  not not_36 (not_36_out, xor_3_out);
  not not_37 (not_37_out, xor_4_out);
  not not_38 (not_38_out, xor_2_out);
  not not_39 (not_39_out, xor_2_out);
  not not_40 (not_40_out, xor_4_out);
  not not_41 (not_41_out, xor_1_out);
  not not_42 (not_42_out, xor_3_out);
  not not_43 (not_43_out, xor_2_out);
  and and_1 (and_1_out, not_1_out, not_2_out);
  and and_2 (and_2_out, not_3_out, xor_4_out);
  and and_3 (and_3_out, not_4_out, xor_4_out);
  and and_4 (and_4_out, not_5_out, xor_2_out);
  and and_5 (and_5_out, xor_1_out, not_6_out);
  and and_6 (and_6_out, not_7_out, not_8_out, not_9_out);
  and and_7 (and_7_out, not_10_out, xor_3_out, xor_4_out);
  and and_8 (and_8_out, xor_2_out, not_11_out, xor_4_out);
  and and_9 (and_9_out, xor_2_out, xor_3_out, not_12_out);
  and and_10 (and_10_out, xor_1_out, not_13_out);
  and and_11 (and_11_out, not_14_out, not_15_out);
  and and_12 (and_12_out, xor_3_out, not_16_out);
  and and_13 (and_13_out, xor_1_out, xor_3_out);
  and and_14 (and_14_out, xor_1_out, xor_2_out);
  and and_15 (and_15_out, not_17_out, not_18_out);
  and and_16 (and_16_out, not_19_out, not_20_out, not_21_out);
  and and_17 (and_17_out, not_22_out, not_23_out);
  and and_18 (and_18_out, not_24_out, xor_3_out, xor_4_out);
  and and_19 (and_19_out, xor_1_out, not_25_out, xor_4_out);
  and and_20 (and_20_out, not_26_out, not_27_out);
  and and_21 (and_21_out, not_28_out, xor_3_out);
  and and_22 (and_22_out, not_29_out, xor_2_out, xor_4_out);
  and and_23 (and_23_out, xor_2_out, xor_3_out);
  and and_24 (and_24_out, xor_1_out, not_30_out, not_31_out);
  and and_25 (and_25_out, xor_1_out, not_32_out);
  and and_26 (and_26_out, not_33_out, not_34_out);
  and and_27 (and_27_out, not_35_out, xor_2_out, not_36_out);
  and and_28 (and_28_out, xor_2_out, not_37_out);
  and and_29 (and_29_out, xor_1_out, not_38_out);
  and and_30 (and_30_out, xor_1_out, xor_3_out);
  and and_31 (and_31_out, not_39_out, xor_3_out);
  and and_32 (and_32_out, xor_3_out, not_40_out);
  and and_33 (and_33_out, not_41_out, xor_2_out, not_42_out);
  and and_34 (and_34_out, xor_1_out, not_43_out);
  and and_35 (and_35_out, xor_1_out, xor_4_out);
  or or_1 (out_3[6], and_1_out, and_2_out, and_3_out, and_4_out, and_5_out);
  or or_2 (out_3[5], and_6_out, and_7_out, and_8_out, and_9_out, and_10_out);
  or or_3 (out_3[4], and_11_out, and_12_out, and_13_out, and_14_out);
  or or_4 (out_3[3], and_15_out, and_16_out, and_17_out, and_18_out, and_19_out);
  or or_5 (out_3[2], and_20_out, and_21_out, and_22_out, and_23_out, and_24_out, and_25_out);
  or or_6 (out_3[1], and_26_out, and_27_out, and_28_out, and_29_out, and_30_out);
  or or_7 (out_3[0], and_31_out, and_32_out, and_33_out, and_34_out, and_35_out);

  assign out_3[7] = 1'b0;
endmodule

module _16btn_to_hex (
  input  _1,
  input  _2,
  input  _3,
  input  _4,
  input  _5,
  input  _6,
  input  _7,
  input  _8,
  input  _9,
  input  A,
  input  B,
  input  C,
  input  D,
  input  E,
  input  F,
  output [3:0] out_16,
  output out_17
);

  _1f0 u_1f0_1 (.in_1({F, E, D, C, B, A, _9, _8, _7, _6, _5, _4, _3, _2, _1}), .out_2(out_16[3]));
  _1f1 u_1f1_1 (.in_1({F, E, D, C, B, A, _9, _8, _7, _6, _5, _4, _3, _2, _1}), .out_2(out_16[2]));
  _1f2 u_1f2_1 (.in_1({F, E, D, C, B, A, _9, _8, _7, _6, _5, _4, _3, _2, _1}), .out_2(out_16[1]));
  _1f3 u_1f3_1 (.in_1({F, E, D, C, B, A, _9, _8, _7, _6, _5, _4, _3, _2, _1}), .out_2(out_16[0]));
  or or_1 (out_17, _1, _2, _3, _4, _5, _6, _7, _8, _9, A, B, C, D, E, F);
endmodule

module _1f0 (
  input  [14:0] in_1,
  output out_2
);

  wire nor_1_out, nor_2_out, nor_3_out, nor_4_out, nor_5_out, nor_6_out, nor_7_out, nor_8_out;

  nor nor_1 (nor_1_out, in_1[0], in_1[1], in_1[2], in_1[3], in_1[4], in_1[5], in_1[6], ~in_1[7], in_1[8], in_1[9], in_1[10], in_1[11], in_1[12], in_1[13], in_1[14]);  // NOR_Gate
  nor nor_2 (nor_2_out, in_1[0], in_1[1], in_1[2], in_1[3], in_1[4], in_1[5], in_1[6], in_1[7], ~in_1[8], in_1[9], in_1[10], in_1[11], in_1[12], in_1[13], in_1[14]);  // NOR_Gate
  nor nor_3 (nor_3_out, in_1[0], in_1[1], in_1[2], in_1[3], in_1[4], in_1[5], in_1[6], in_1[7], in_1[8], ~in_1[9], in_1[10], in_1[11], in_1[12], in_1[13], in_1[14]);  // NOR_Gate
  nor nor_4 (nor_4_out, in_1[0], in_1[1], in_1[2], in_1[3], in_1[4], in_1[5], in_1[6], in_1[7], in_1[8], in_1[9], ~in_1[10], in_1[11], in_1[12], in_1[13], in_1[14]);  // NOR_Gate
  nor nor_5 (nor_5_out, in_1[0], in_1[1], in_1[2], in_1[3], in_1[4], in_1[5], in_1[6], in_1[7], in_1[8], in_1[9], in_1[10], ~in_1[11], in_1[12], in_1[13], in_1[14]);  // NOR_Gate
  nor nor_6 (nor_6_out, in_1[0], in_1[1], in_1[2], in_1[3], in_1[4], in_1[5], in_1[6], in_1[7], in_1[8], in_1[9], in_1[10], in_1[11], ~in_1[12], in_1[13], in_1[14]);  // NOR_Gate
  nor nor_7 (nor_7_out, in_1[0], in_1[1], in_1[2], in_1[3], in_1[4], in_1[5], in_1[6], in_1[7], in_1[8], in_1[9], in_1[10], in_1[11], in_1[12], ~in_1[13], in_1[14]);  // NOR_Gate
  nor nor_8 (nor_8_out, in_1[0], in_1[1], in_1[2], in_1[3], in_1[4], in_1[5], in_1[6], in_1[7], in_1[8], in_1[9], in_1[10], in_1[11], in_1[12], in_1[13], ~in_1[14]);  // NOR_Gate
  or or_1 (out_2, nor_1_out, nor_2_out, nor_3_out, nor_4_out, nor_5_out, nor_6_out, nor_7_out, nor_8_out);
endmodule

module _1f1 (
  input  [14:0] in_1,
  output out_2
);

  wire nor_1_out, nor_2_out, nor_3_out, nor_4_out, nor_5_out, nor_6_out, nor_7_out, nor_8_out;

  nor nor_1 (nor_1_out, in_1[0], in_1[1], in_1[2], ~in_1[3], in_1[4], in_1[5], in_1[6], in_1[7], in_1[8], in_1[9], in_1[10], in_1[11], in_1[12], in_1[13], in_1[14]);  // NOR_Gate
  nor nor_2 (nor_2_out, in_1[0], in_1[1], in_1[2], in_1[3], ~in_1[4], in_1[5], in_1[6], in_1[7], in_1[8], in_1[9], in_1[10], in_1[11], in_1[12], in_1[13], in_1[14]);  // NOR_Gate
  nor nor_3 (nor_3_out, in_1[0], in_1[1], in_1[2], in_1[3], in_1[4], ~in_1[5], in_1[6], in_1[7], in_1[8], in_1[9], in_1[10], in_1[11], in_1[12], in_1[13], in_1[14]);  // NOR_Gate
  nor nor_4 (nor_4_out, in_1[0], in_1[1], in_1[2], in_1[3], in_1[4], in_1[5], ~in_1[6], in_1[7], in_1[8], in_1[9], in_1[10], in_1[11], in_1[12], in_1[13], in_1[14]);  // NOR_Gate
  nor nor_5 (nor_5_out, in_1[0], in_1[1], in_1[2], in_1[3], in_1[4], in_1[5], in_1[6], in_1[7], in_1[8], in_1[9], in_1[10], ~in_1[11], in_1[12], in_1[13], in_1[14]);  // NOR_Gate
  nor nor_6 (nor_6_out, in_1[0], in_1[1], in_1[2], in_1[3], in_1[4], in_1[5], in_1[6], in_1[7], in_1[8], in_1[9], in_1[10], in_1[11], ~in_1[12], in_1[13], in_1[14]);  // NOR_Gate
  nor nor_7 (nor_7_out, in_1[0], in_1[1], in_1[2], in_1[3], in_1[4], in_1[5], in_1[6], in_1[7], in_1[8], in_1[9], in_1[10], in_1[11], in_1[12], ~in_1[13], in_1[14]);  // NOR_Gate
  nor nor_8 (nor_8_out, in_1[0], in_1[1], in_1[2], in_1[3], in_1[4], in_1[5], in_1[6], in_1[7], in_1[8], in_1[9], in_1[10], in_1[11], in_1[12], in_1[13], ~in_1[14]);  // NOR_Gate
  or or_1 (out_2, nor_1_out, nor_2_out, nor_3_out, nor_4_out, nor_5_out, nor_6_out, nor_7_out, nor_8_out);
endmodule

module _1f2 (
  input  [14:0] in_1,
  output out_2
);

  wire nor_1_out, nor_2_out, nor_3_out, nor_4_out, nor_5_out, nor_6_out, nor_7_out, nor_8_out;

  nor nor_1 (nor_1_out, in_1[0], ~in_1[1], in_1[2], in_1[3], in_1[4], in_1[5], in_1[6], in_1[7], in_1[8], in_1[9], in_1[10], in_1[11], in_1[12], in_1[13], in_1[14]);  // NOR_Gate
  nor nor_2 (nor_2_out, in_1[0], in_1[1], ~in_1[2], in_1[3], in_1[4], in_1[5], in_1[6], in_1[7], in_1[8], in_1[9], in_1[10], in_1[11], in_1[12], in_1[13], in_1[14]);  // NOR_Gate
  nor nor_3 (nor_3_out, in_1[0], in_1[1], in_1[2], in_1[3], in_1[4], ~in_1[5], in_1[6], in_1[7], in_1[8], in_1[9], in_1[10], in_1[11], in_1[12], in_1[13], in_1[14]);  // NOR_Gate
  nor nor_4 (nor_4_out, in_1[0], in_1[1], in_1[2], in_1[3], in_1[4], in_1[5], ~in_1[6], in_1[7], in_1[8], in_1[9], in_1[10], in_1[11], in_1[12], in_1[13], in_1[14]);  // NOR_Gate
  nor nor_5 (nor_5_out, in_1[0], in_1[1], in_1[2], in_1[3], in_1[4], in_1[5], in_1[6], in_1[7], in_1[8], ~in_1[9], in_1[10], in_1[11], in_1[12], in_1[13], in_1[14]);  // NOR_Gate
  nor nor_6 (nor_6_out, in_1[0], in_1[1], in_1[2], in_1[3], in_1[4], in_1[5], in_1[6], in_1[7], in_1[8], in_1[9], ~in_1[10], in_1[11], in_1[12], in_1[13], in_1[14]);  // NOR_Gate
  nor nor_7 (nor_7_out, in_1[0], in_1[1], in_1[2], in_1[3], in_1[4], in_1[5], in_1[6], in_1[7], in_1[8], in_1[9], in_1[10], in_1[11], in_1[12], ~in_1[13], in_1[14]);  // NOR_Gate
  nor nor_8 (nor_8_out, in_1[0], in_1[1], in_1[2], in_1[3], in_1[4], in_1[5], in_1[6], in_1[7], in_1[8], in_1[9], in_1[10], in_1[11], in_1[12], in_1[13], ~in_1[14]);  // NOR_Gate
  or or_1 (out_2, nor_1_out, nor_2_out, nor_3_out, nor_4_out, nor_5_out, nor_6_out, nor_7_out, nor_8_out);
endmodule

module _1f3 (
  input  [14:0] in_1,
  output out_2
);

  wire nor_1_out, nor_2_out, nor_3_out, nor_4_out, nor_5_out, nor_6_out, nor_7_out, nor_8_out;

  nor nor_1 (nor_1_out, ~in_1[0], in_1[1], in_1[2], in_1[3], in_1[4], in_1[5], in_1[6], in_1[7], in_1[8], in_1[9], in_1[10], in_1[11], in_1[12], in_1[13], in_1[14]);  // NOR_Gate
  nor nor_2 (nor_2_out, in_1[0], in_1[1], ~in_1[2], in_1[3], in_1[4], in_1[5], in_1[6], in_1[7], in_1[8], in_1[9], in_1[10], in_1[11], in_1[12], in_1[13], in_1[14]);  // NOR_Gate
  nor nor_3 (nor_3_out, in_1[0], in_1[1], in_1[2], in_1[3], ~in_1[4], in_1[5], in_1[6], in_1[7], in_1[8], in_1[9], in_1[10], in_1[11], in_1[12], in_1[13], in_1[14]);  // NOR_Gate
  nor nor_4 (nor_4_out, in_1[0], in_1[1], in_1[2], in_1[3], in_1[4], in_1[5], ~in_1[6], in_1[7], in_1[8], in_1[9], in_1[10], in_1[11], in_1[12], in_1[13], in_1[14]);  // NOR_Gate
  nor nor_5 (nor_5_out, in_1[0], in_1[1], in_1[2], in_1[3], in_1[4], in_1[5], in_1[6], in_1[7], ~in_1[8], in_1[9], in_1[10], in_1[11], in_1[12], in_1[13], in_1[14]);  // NOR_Gate
  nor nor_6 (nor_6_out, in_1[0], in_1[1], in_1[2], in_1[3], in_1[4], in_1[5], in_1[6], in_1[7], in_1[8], in_1[9], ~in_1[10], in_1[11], in_1[12], in_1[13], in_1[14]);  // NOR_Gate
  nor nor_7 (nor_7_out, in_1[0], in_1[1], in_1[2], in_1[3], in_1[4], in_1[5], in_1[6], in_1[7], in_1[8], in_1[9], in_1[10], in_1[11], ~in_1[12], in_1[13], in_1[14]);  // NOR_Gate
  nor nor_8 (nor_8_out, in_1[0], in_1[1], in_1[2], in_1[3], in_1[4], in_1[5], in_1[6], in_1[7], in_1[8], in_1[9], in_1[10], in_1[11], in_1[12], in_1[13], ~in_1[14]);  // NOR_Gate
  or or_1 (out_2, nor_1_out, nor_2_out, nor_3_out, nor_4_out, nor_5_out, nor_6_out, nor_7_out, nor_8_out);
endmodule

module _4bit_MEM (
  input  [3:0] in_1,
  input  in_2,
  input  in_3,
  output [3:0] out_4
);

  D_Flip_Flop d_ff_1 (.clk(in_3), .D(in_1[3]), .Q(out_4[3]), .en(in_3), .reset(in_2));  // open: Qn, preset
  D_Flip_Flop d_ff_2 (.clk(in_3), .D(in_1[2]), .Q(out_4[2]), .en(in_3), .reset(in_2));  // open: Qn, preset
  D_Flip_Flop d_ff_3 (.clk(in_3), .D(in_1[1]), .Q(out_4[1]), .en(in_3), .reset(in_2));  // open: Qn, preset
  D_Flip_Flop d_ff_4 (.clk(in_3), .D(in_1[0]), .Q(out_4[0]), .en(in_3), .reset(in_2));  // open: Qn, preset
endmodule
