// Logisim project CBRLAB5.circ as structural Verilog: 11 circuits, main circuit main
module main (
  input  _1,
  input  _2,
  input  _3,
  input  _4,
  input  _5,
  input  _6,
  input  _7,
  input  _8,
  input  _9,
  input  A,
  input  B,
  input  C,
  input  D,
  input  E,
  input  [3:0] in_15,
  input  F,
  input  [3:0] in_17,
  input  [3:0] in_18,
  input  [3:0] in_19,
  input  [3:0] in_20,
  input  [3:0] in_21,
  input  [3:0] in_22,
  input  [3:0] in_23,
  input  [2:0] in_24,
  input  [2:0] in_25,
  input  [3:0] in_26,
  output [3:0] out_27,
  output [3:0] out_28,
  output [3:0] out_29,
  output [3:0] out_30,
  output [3:0] out_31,
  output [3:0] out_32,
  output [3:0] out_33,
  output [3:0] out_34,
  output [3:0] out_35
);

  wire [3:0] n16btn_to_hex_1_out_16;
  wire [7:0] hex_to_7seg_1_out_2;

  // Probe on n16btn_to_hex_1_out_16
  _16btn_to_hex u_16btn_to_hex_1 (
    ._1(_1), ._2(_2), ._3(_3), ._4(_4), ._5(_5), ._6(_6), ._7(_7), ._8(_8), ._9(_9), .A(A), .B(B), .C(C),
    .D(D), .E(E), .F(F), .out_16(n16btn_to_hex_1_out_16));
  hex_to_7seg hex_to_7seg_1 (.in_1(n16btn_to_hex_1_out_16), .out_2(hex_to_7seg_1_out_2));
  _4bit_Demultiplexer u_4bit_demultiplexer_1 (
    .a(in_20), .c2(in_24[2]), .c1(in_24[1]), .c0(in_24[0]), .x(out_27), .x2(out_28), .x3(out_29),
    .x4(out_30), .x5(out_32), .x6(out_33), .x7(out_34), .x8(out_35));
  _7_Segment_Display u_7_segment_display_1 (
    .g(hex_to_7seg_1_out_2[0]), .f(hex_to_7seg_1_out_2[1]), .a(hex_to_7seg_1_out_2[2]),
    .b(hex_to_7seg_1_out_2[3]), .e(hex_to_7seg_1_out_2[4]), .d(hex_to_7seg_1_out_2[5]),
    .c(hex_to_7seg_1_out_2[6]), .dp(hex_to_7seg_1_out_2[7]));
  _4bit_Multiplexer u_4bit_multiplexer_1 (
    .in_1(in_15), .in_2(in_17), .in_3(in_18), .in_4(in_19), .in_5(in_21), .in_6(in_22), .in_7(in_23),
    .in_8(in_26), .out_12(out_31), .c2(in_25[2]), .c1(in_25[1]), .c0(in_25[0]));
endmodule

module hex_to_7seg (
  input  [3:0] in_1,
  output [7:0] out_2
);

  wire and_1_out, and_2_out, and_3_out, and_4_out, and_5_out, and_6_out, and_7_out, and_8_out, and_9_out,
       and_10_out, and_11_out, and_12_out, and_13_out, and_14_out, and_15_out, and_16_out, and_17_out,
       and_18_out, and_19_out, and_20_out, and_21_out, and_22_out, and_23_out, and_24_out, and_25_out,
       and_26_out, and_27_out, and_28_out, and_29_out, and_30_out, and_31_out, and_32_out, and_33_out,
       and_34_out, and_35_out, not_1_out, not_2_out, not_3_out, not_4_out, not_5_out, not_6_out, not_7_out,
       not_8_out, not_9_out, not_10_out, not_11_out, not_12_out, not_13_out, not_14_out, not_15_out,
       not_16_out, not_17_out, not_18_out, not_19_out, not_20_out, not_21_out, not_22_out, not_23_out,
       not_24_out, not_25_out, not_26_out, not_27_out, not_28_out, not_29_out, not_30_out, not_31_out,
       not_32_out, not_33_out, not_34_out, not_35_out, not_36_out, not_37_out, not_38_out, not_39_out,
       not_40_out, not_41_out, not_42_out, not_43_out;

  not not_1 (not_1_out, in_1[3]);
  not not_2 (not_2_out, in_1[1]);
  not not_3 (not_3_out, in_1[3]);
  not not_4 (not_4_out, in_1[1]);
  not not_5 (not_5_out, in_1[3]);
  not not_6 (not_6_out, in_1[2]);
  not not_7 (not_7_out, in_1[3]);
  not not_8 (not_8_out, in_1[2]);
  not not_9 (not_9_out, in_1[0]);
  not not_10 (not_10_out, in_1[2]);
  not not_11 (not_11_out, in_1[1]);
  not not_12 (not_12_out, in_1[0]);
  not not_13 (not_13_out, in_1[1]);
  not not_14 (not_14_out, in_1[2]);
  not not_15 (not_15_out, in_1[0]);
  not not_16 (not_16_out, in_1[0]);
  not not_17 (not_17_out, in_1[3]);
  not not_18 (not_18_out, in_1[2]);
  not not_19 (not_19_out, in_1[3]);
  not not_20 (not_20_out, in_1[1]);
  not not_21 (not_21_out, in_1[0]);
  not not_22 (not_22_out, in_1[2]);
  not not_23 (not_23_out, in_1[0]);
  not not_24 (not_24_out, in_1[3]);
  not not_25 (not_25_out, in_1[1]);
  not not_26 (not_26_out, in_1[2]);
  not not_27 (not_27_out, in_1[0]);
  not not_28 (not_28_out, in_1[3]);
  not not_29 (not_29_out, in_1[3]);
  not not_30 (not_30_out, in_1[2]);
  not not_31 (not_31_out, in_1[1]);
  not not_32 (not_32_out, in_1[0]);
  not not_33 (not_33_out, in_1[1]);
  not not_34 (not_34_out, in_1[0]);
  not not_35 (not_35_out, in_1[3]);
  not not_36 (not_36_out, in_1[1]);
  not not_37 (not_37_out, in_1[0]);
  not not_38 (not_38_out, in_1[2]);
  not not_39 (not_39_out, in_1[2]);
  not not_40 (not_40_out, in_1[0]);
  not not_41 (not_41_out, in_1[3]);
  not not_42 (not_42_out, in_1[1]);
  not not_43 (not_43_out, in_1[2]);
  and and_1 (and_1_out, not_1_out, not_2_out);
  and and_2 (and_2_out, not_3_out, in_1[0]);
  and and_3 (and_3_out, not_4_out, in_1[0]);
  and and_4 (and_4_out, not_5_out, in_1[2]);
  and and_5 (and_5_out, in_1[3], not_6_out);
  and and_6 (and_6_out, not_7_out, not_8_out, not_9_out);
  and and_7 (and_7_out, not_10_out, in_1[1], in_1[0]);
  and and_8 (and_8_out, in_1[2], not_11_out, in_1[0]);
  and and_9 (and_9_out, in_1[2], in_1[1], not_12_out);
  and and_10 (and_10_out, in_1[3], not_13_out);
  and and_11 (and_11_out, not_14_out, not_15_out);
  and and_12 (and_12_out, in_1[1], not_16_out);
  and and_13 (and_13_out, in_1[3], in_1[1]);
  and and_14 (and_14_out, in_1[3], in_1[2]);
  and and_15 (and_15_out, not_17_out, not_18_out);
  and and_16 (and_16_out, not_19_out, not_20_out, not_21_out);
  and and_17 (and_17_out, not_22_out, not_23_out);
  and and_18 (and_18_out, not_24_out, in_1[1], in_1[0]);
  and and_19 (and_19_out, in_1[3], not_25_out, in_1[0]);
  and and_20 (and_20_out, not_26_out, not_27_out);
  and and_21 (and_21_out, not_28_out, in_1[1]);
  and and_22 (and_22_out, not_29_out, in_1[2], in_1[0]);
  and and_23 (and_23_out, in_1[2], in_1[1]);
  and and_24 (and_24_out, in_1[3], not_30_out, not_31_out);
  and and_25 (and_25_out, in_1[3], not_32_out);
  and and_26 (and_26_out, not_33_out, not_34_out);
  and and_27 (and_27_out, not_35_out, in_1[2], not_36_out);
  and and_28 (and_28_out, in_1[2], not_37_out);
  and and_29 (and_29_out, in_1[3], not_38_out);
  and and_30 (and_30_out, in_1[3], in_1[1]);
  and and_31 (and_31_out, not_39_out, in_1[1]);
  and and_32 (and_32_out, in_1[1], not_40_out);
  and and_33 (and_33_out, not_41_out, in_1[2], not_42_out);
  and and_34 (and_34_out, in_1[3], not_43_out);
  and and_35 (and_35_out, in_1[3], in_1[0]);
  or or_1 (out_2[6], and_1_out, and_2_out, and_3_out, and_4_out, and_5_out);
  or or_2 (out_2[5], and_6_out, and_7_out, and_8_out, and_9_out, and_10_out);
  or or_3 (out_2[4], and_11_out, and_12_out, and_13_out, and_14_out);
  or or_4 (out_2[3], and_15_out, and_16_out, and_17_out, and_18_out, and_19_out);
  or or_5 (out_2[2], and_20_out, and_21_out, and_22_out, and_23_out, and_24_out, and_25_out);
  or or_6 (out_2[1], and_26_out, and_27_out, and_28_out, and_29_out, and_30_out);
  or or_7 (out_2[0], and_31_out, and_32_out, and_33_out, and_34_out, and_35_out);

  assign out_2[7] = 1'b0;
endmodule

module _16btn_to_hex (
  input  _1,
  input  _2,
  input  _3,
  input  _4,
  input  _5,
  input  _6,
  input  _7,
  input  _8,
  input  _9,
  input  A,
  input  B,
  input  C,
  input  D,
  input  E,
  input  F,
  output [3:0] out_16
);

  _1f0 u_1f0_1 (.in_1({F, E, D, C, B, A, _9, _8, _7, _6, _5, _4, _3, _2, _1}), .out_2(out_16[3]));
  _1f1 u_1f1_1 (.in_1({F, E, D, C, B, A, _9, _8, _7, _6, _5, _4, _3, _2, _1}), .out_2(out_16[2]));
  _1f2 u_1f2_1 (.in_1({F, E, D, C, B, A, _9, _8, _7, _6, _5, _4, _3, _2, _1}), .out_2(out_16[1]));
  _1f3 u_1f3_1 (.in_1({F, E, D, C, B, A, _9, _8, _7, _6, _5, _4, _3, _2, _1}), .out_2(out_16[0]));
endmodule

module _1f0 (
  input  [14:0] in_1,
  output out_2
);

  wire nor_1_out, nor_2_out, nor_3_out, nor_4_out, nor_5_out, nor_6_out, nor_7_out, nor_8_out;

  nor nor_1 (nor_1_out, in_1[0], in_1[1], in_1[2], in_1[3], in_1[4], in_1[5], in_1[6], ~in_1[7], in_1[8], in_1[9], in_1[10], in_1[11], in_1[12], in_1[13], in_1[14]);  // NOR_Gate
  nor nor_2 (nor_2_out, in_1[0], in_1[1], in_1[2], in_1[3], in_1[4], in_1[5], in_1[6], in_1[7], ~in_1[8], in_1[9], in_1[10], in_1[11], in_1[12], in_1[13], in_1[14]);  // NOR_Gate
  nor nor_3 (nor_3_out, in_1[0], in_1[1], in_1[2], in_1[3], in_1[4], in_1[5], in_1[6], in_1[7], in_1[8], ~in_1[9], in_1[10], in_1[11], in_1[12], in_1[13], in_1[14]);  // NOR_Gate
  nor nor_4 (nor_4_out, in_1[0], in_1[1], in_1[2], in_1[3], in_1[4], in_1[5], in_1[6], in_1[7], in_1[8], in_1[9], ~in_1[10], in_1[11], in_1[12], in_1[13], in_1[14]);  // NOR_Gate
  nor nor_5 (nor_5_out, in_1[0], in_1[1], in_1[2], in_1[3], in_1[4], in_1[5], in_1[6], in_1[7], in_1[8], in_1[9], in_1[10], ~in_1[11], in_1[12], in_1[13], in_1[14]);  // NOR_Gate
  nor nor_6 (nor_6_out, in_1[0], in_1[1], in_1[2], in_1[3], in_1[4], in_1[5], in_1[6], in_1[7], in_1[8], in_1[9], in_1[10], in_1[11], ~in_1[12], in_1[13], in_1[14]);  // NOR_Gate
  nor nor_7 (nor_7_out, in_1[0], in_1[1], in_1[2], in_1[3], in_1[4], in_1[5], in_1[6], in_1[7], in_1[8], in_1[9], in_1[10], in_1[11], in_1[12], ~in_1[13], in_1[14]);  // NOR_Gate
  nor nor_8 (nor_8_out, in_1[0], in_1[1], in_1[2], in_1[3], in_1[4], in_1[5], in_1[6], in_1[7], in_1[8], in_1[9], in_1[10], in_1[11], in_1[12], in_1[13], ~in_1[14]);  // NOR_Gate
  or or_1 (out_2, nor_1_out, nor_2_out, nor_3_out, nor_4_out, nor_5_out, nor_6_out, nor_7_out, nor_8_out);
endmodule

module _1f1 (
  input  [14:0] in_1,
  output out_2
);

  wire nor_1_out, nor_2_out, nor_3_out, nor_4_out, nor_5_out, nor_6_out, nor_7_out, nor_8_out;

  nor nor_1 (nor_1_out, in_1[0], in_1[1], in_1[2], ~in_1[3], in_1[4], in_1[5], in_1[6], in_1[7], in_1[8], in_1[9], in_1[10], in_1[11], in_1[12], in_1[13], in_1[14]);  // NOR_Gate
  nor nor_2 (nor_2_out, in_1[0], in_1[1], in_1[2], in_1[3], ~in_1[4], in_1[5], in_1[6], in_1[7], in_1[8], in_1[9], in_1[10], in_1[11], in_1[12], in_1[13], in_1[14]);  // NOR_Gate
  nor nor_3 (nor_3_out, in_1[0], in_1[1], in_1[2], in_1[3], in_1[4], ~in_1[5], in_1[6], in_1[7], in_1[8], in_1[9], in_1[10], in_1[11], in_1[12], in_1[13], in_1[14]);  // NOR_Gate
  nor nor_4 (nor_4_out, in_1[0], in_1[1], in_1[2], in_1[3], in_1[4], in_1[5], ~in_1[6], in_1[7], in_1[8], in_1[9], in_1[10], in_1[11], in_1[12], in_1[13], in_1[14]);  // NOR_Gate
  nor nor_5 (nor_5_out, in_1[0], in_1[1], in_1[2], in_1[3], in_1[4], in_1[5], in_1[6], in_1[7], in_1[8], in_1[9], in_1[10], ~in_1[11], in_1[12], in_1[13], in_1[14]);  // NOR_Gate
  nor nor_6 (nor_6_out, in_1[0], in_1[1], in_1[2], in_1[3], in_1[4], in_1[5], in_1[6], in_1[7], in_1[8], in_1[9], in_1[10], in_1[11], ~in_1[12], in_1[13], in_1[14]);  // NOR_Gate
  nor nor_7 (nor_7_out, in_1[0], in_1[1], in_1[2], in_1[3], in_1[4], in_1[5], in_1[6], in_1[7], in_1[8], in_1[9], in_1[10], in_1[11], in_1[12], ~in_1[13], in_1[14]);  // NOR_Gate
  nor nor_8 (nor_8_out, in_1[0], in_1[1], in_1[2], in_1[3], in_1[4], in_1[5], in_1[6], in_1[7], in_1[8], in_1[9], in_1[10], in_1[11], in_1[12], in_1[13], ~in_1[14]);  // NOR_Gate
  or or_1 (out_2, nor_1_out, nor_2_out, nor_3_out, nor_4_out, nor_5_out, nor_6_out, nor_7_out, nor_8_out);
endmodule

module _1f2 (
  input  [14:0] in_1,
  output out_2
);

  wire nor_1_out, nor_2_out, nor_3_out, nor_4_out, nor_5_out, nor_6_out, nor_7_out, nor_8_out;

  nor nor_1 (nor_1_out, in_1[0], ~in_1[1], in_1[2], in_1[3], in_1[4], in_1[5], in_1[6], in_1[7], in_1[8], in_1[9], in_1[10], in_1[11], in_1[12], in_1[13], in_1[14]);  // NOR_Gate
  nor nor_2 (nor_2_out, in_1[0], in_1[1], ~in_1[2], in_1[3], in_1[4], in_1[5], in_1[6], in_1[7], in_1[8], in_1[9], in_1[10], in_1[11], in_1[12], in_1[13], in_1[14]);  // NOR_Gate
  nor nor_3 (nor_3_out, in_1[0], in_1[1], in_1[2], in_1[3], in_1[4], ~in_1[5], in_1[6], in_1[7], in_1[8], in_1[9], in_1[10], in_1[11], in_1[12], in_1[13], in_1[14]);  // NOR_Gate
  nor nor_4 (nor_4_out, in_1[0], in_1[1], in_1[2], in_1[3], in_1[4], in_1[5], ~in_1[6], in_1[7], in_1[8], in_1[9], in_1[10], in_1[11], in_1[12], in_1[13], in_1[14]);  // NOR_Gate
  nor nor_5 (nor_5_out, in_1[0], in_1[1], in_1[2], in_1[3], in_1[4], in_1[5], in_1[6], in_1[7], in_1[8], ~in_1[9], in_1[10], in_1[11], in_1[12], in_1[13], in_1[14]);  // NOR_Gate
  nor nor_6 (nor_6_out, in_1[0], in_1[1], in_1[2], in_1[3], in_1[4], in_1[5], in_1[6], in_1[7], in_1[8], in_1[9], ~in_1[10], in_1[11], in_1[12], in_1[13], in_1[14]);  // NOR_Gate
  nor nor_7 (nor_7_out, in_1[0], in_1[1], in_1[2], in_1[3], in_1[4], in_1[5], in_1[6], in_1[7], in_1[8], in_1[9], in_1[10], in_1[11], in_1[12], ~in_1[13], in_1[14]);  // NOR_Gate
  nor nor_8 (nor_8_out, in_1[0], in_1[1], in_1[2], in_1[3], in_1[4], in_1[5], in_1[6], in_1[7], in_1[8], in_1[9], in_1[10], in_1[11], in_1[12], in_1[13], ~in_1[14]);  // NOR_Gate
  or or_1 (out_2, nor_1_out, nor_2_out, nor_3_out, nor_4_out, nor_5_out, nor_6_out, nor_7_out, nor_8_out);
endmodule

module _1f3 (
  input  [14:0] in_1,
  output out_2
);

  wire nor_1_out, nor_2_out, nor_3_out, nor_4_out, nor_5_out, nor_6_out, nor_7_out, nor_8_out;

  nor nor_1 (nor_1_out, ~in_1[0], in_1[1], in_1[2], in_1[3], in_1[4], in_1[5], in_1[6], in_1[7], in_1[8], in_1[9], in_1[10], in_1[11], in_1[12], in_1[13], in_1[14]);  // NOR_Gate
  nor nor_2 (nor_2_out, in_1[0], in_1[1], ~in_1[2], in_1[3], in_1[4], in_1[5], in_1[6], in_1[7], in_1[8], in_1[9], in_1[10], in_1[11], in_1[12], in_1[13], in_1[14]);  // NOR_Gate
  nor nor_3 (nor_3_out, in_1[0], in_1[1], in_1[2], in_1[3], ~in_1[4], in_1[5], in_1[6], in_1[7], in_1[8], in_1[9], in_1[10], in_1[11], in_1[12], in_1[13], in_1[14]);  // NOR_Gate
  nor nor_4 (nor_4_out, in_1[0], in_1[1], in_1[2], in_1[3], in_1[4], in_1[5], ~in_1[6], in_1[7], in_1[8], in_1[9], in_1[10], in_1[11], in_1[12], in_1[13], in_1[14]);  // NOR_Gate
  nor nor_5 (nor_5_out, in_1[0], in_1[1], in_1[2], in_1[3], in_1[4], in_1[5], in_1[6], in_1[7], ~in_1[8], in_1[9], in_1[10], in_1[11], in_1[12], in_1[13], in_1[14]);  // NOR_Gate
  nor nor_6 (nor_6_out, in_1[0], in_1[1], in_1[2], in_1[3], in_1[4], in_1[5], in_1[6], in_1[7], in_1[8], in_1[9], ~in_1[10], in_1[11], in_1[12], in_1[13], in_1[14]);  // NOR_Gate
  nor nor_7 (nor_7_out, in_1[0], in_1[1], in_1[2], in_1[3], in_1[4], in_1[5], in_1[6], in_1[7], in_1[8], in_1[9], in_1[10], in_1[11], ~in_1[12], in_1[13], in_1[14]);  // NOR_Gate
  nor nor_8 (nor_8_out, in_1[0], in_1[1], in_1[2], in_1[3], in_1[4], in_1[5], in_1[6], in_1[7], in_1[8], in_1[9], in_1[10], in_1[11], in_1[12], in_1[13], ~in_1[14]);  // NOR_Gate
  or or_1 (out_2, nor_1_out, nor_2_out, nor_3_out, nor_4_out, nor_5_out, nor_6_out, nor_7_out, nor_8_out);
endmodule

module _4bit_Multiplexer (
  input  [3:0] in_1,
  input  [3:0] in_2,
  input  [3:0] in_3,
  input  [3:0] in_4,
  input  [3:0] in_5,
  input  [3:0] in_6,
  input  [3:0] in_7,
  input  [3:0] in_8,
  input  c2,
  input  c1,
  input  c0,
  output [3:0] out_12
);

  wire [3:0] transistor_1_out, transistor_2_out, transistor_3_out, transistor_4_out, transistor_5_out,
       transistor_6_out, transistor_7_out, transistor_8_out, transistor_9_out, transistor_12_out,
       transistor_13_out, transistor_16_out, transistor_17_out, transistor_20_out, transistor_22_out,
       transistor_23_out;

  Transistor #(.gate("br"), .width(4)) transistor_1 (.in(in_1), .out(transistor_1_out), .gate(c2));
  Transistor #(.gate("br"), .width(4)) transistor_2 (.in(in_2), .out(transistor_2_out), .gate(c2));
  Transistor #(.gate("br"), .width(4)) transistor_3 (.in(in_3), .out(transistor_3_out), .gate(c2));
  Transistor #(.gate("br"), .width(4)) transistor_4 (.in(in_4), .out(transistor_4_out), .gate(c2));
  Transistor #(.\type ("n"), .gate("br"), .width(4)) transistor_5 (.in(in_5), .out(transistor_5_out), .gate(c2));
  Transistor #(.\type ("n"), .gate("br"), .width(4)) transistor_6 (.in(in_6), .out(transistor_6_out), .gate(c2));
  Transistor #(.\type ("n"), .gate("br"), .width(4)) transistor_7 (.in(in_7), .out(transistor_7_out), .gate(c2));
  Transistor #(.\type ("n"), .gate("br"), .width(4)) transistor_8 (.in(in_8), .out(transistor_8_out), .gate(c2));
  Transistor #(.gate("br"), .width(4)) transistor_9 (.in(transistor_1_out), .out(transistor_9_out), .gate(c1));
  Transistor #(.gate("br"), .width(4)) transistor_10 (.in(transistor_9_out), .out(out_12), .gate(c0));
  Transistor #(.\type ("n"), .gate("br"), .width(4)) transistor_11 (.in(transistor_12_out), .out(out_12), .gate(c0));
  Transistor #(.gate("br"), .width(4)) transistor_12 (.in(transistor_2_out), .out(transistor_12_out), .gate(c1));
  Transistor #(.\type ("n"), .gate("br"), .width(4)) transistor_13 (
    .in(transistor_3_out), .out(transistor_13_out), .gate(c1));
  Transistor #(.gate("br"), .width(4)) transistor_14 (.in(transistor_13_out), .out(out_12), .gate(c0));
  Transistor #(.\type ("n"), .gate("br"), .width(4)) transistor_15 (.in(transistor_16_out), .out(out_12), .gate(c0));
  Transistor #(.\type ("n"), .gate("br"), .width(4)) transistor_16 (
    .in(transistor_4_out), .out(transistor_16_out), .gate(c1));
  Transistor #(.gate("br"), .width(4)) transistor_17 (.in(transistor_5_out), .out(transistor_17_out), .gate(c1));
  Transistor #(.gate("br"), .width(4)) transistor_18 (.in(transistor_17_out), .out(out_12), .gate(c0));
  Transistor #(.\type ("n"), .gate("br"), .width(4)) transistor_19 (.in(transistor_20_out), .out(out_12), .gate(c0));
  Transistor #(.gate("br"), .width(4)) transistor_20 (.in(transistor_6_out), .out(transistor_20_out), .gate(c1));
  Transistor #(.gate("br"), .width(4)) transistor_21 (.in(transistor_22_out), .out(out_12), .gate(c0));
  Transistor #(.\type ("n"), .gate("br"), .width(4)) transistor_22 (
    .in(transistor_7_out), .out(transistor_22_out), .gate(c1));
  Transistor #(.\type ("n"), .gate("br"), .width(4)) transistor_23 (
    .in(transistor_8_out), .out(transistor_23_out), .gate(c1));
  Transistor #(.\type ("n"), .gate("br"), .width(4)) transistor_24 (.in(transistor_23_out), .out(out_12), .gate(c0));
endmodule

module _4bit_Demultiplexer (
  input  [3:0] a,
  input  c2,
  input  c1,
  input  c0,
  output [3:0] x,
  output [3:0] x2,
  output [3:0] x3,
  output [3:0] x4,
  output [3:0] x5,
  output [3:0] x6,
  output [3:0] x7,
  output [3:0] x8
);

  wire [3:0] not_1_out, not_2_out, not_3_out, not_4_out, not_5_out, not_6_out, not_7_out, not_8_out,
       not_9_out, not_10_out, not_11_out, not_12_out;

  assign not_1_out = ~{4{c2}};  // NOT_Gate not_1, 4 bits wide
  assign not_2_out = ~{4{c1}};  // NOT_Gate not_2, 4 bits wide
  assign not_3_out = ~{4{c0}};  // NOT_Gate not_3, 4 bits wide
  assign not_4_out = ~{4{c2}};  // NOT_Gate not_4, 4 bits wide
  assign not_5_out = ~{4{c1}};  // NOT_Gate not_5, 4 bits wide
  assign not_6_out = ~{4{c2}};  // NOT_Gate not_6, 4 bits wide
  assign not_7_out = ~{4{c0}};  // NOT_Gate not_7, 4 bits wide
  assign not_8_out = ~{4{c2}};  // NOT_Gate not_8, 4 bits wide
  assign not_9_out = ~{4{c1}};  // NOT_Gate not_9, 4 bits wide
  assign not_10_out = ~{4{c0}};  // NOT_Gate not_10, 4 bits wide
  assign not_11_out = ~{4{c1}};  // NOT_Gate not_11, 4 bits wide
  assign not_12_out = ~{4{c0}};  // NOT_Gate not_12, 4 bits wide
  assign x8 = a & {4{c2}} & {4{c1}} & {4{c0}};  // AND_Gate and_1, 4 bits wide
  assign x = a & not_1_out & not_2_out & not_3_out;  // AND_Gate and_2, 4 bits wide
  assign x2 = a & not_4_out & not_5_out & {4{c0}};  // AND_Gate and_3, 4 bits wide
  assign x3 = a & not_6_out & {4{c1}} & not_7_out;  // AND_Gate and_4, 4 bits wide
  assign x4 = a & not_8_out & {4{c1}} & {4{c0}};  // AND_Gate and_5, 4 bits wide
  assign x5 = a & {4{c2}} & not_9_out & not_10_out;  // AND_Gate and_6, 4 bits wide
  assign x6 = a & {4{c2}} & not_11_out & {4{c0}};  // AND_Gate and_7, 4 bits wide
  assign x7 = a & {4{c2}} & {4{c1}} & not_12_out;  // AND_Gate and_8, 4 bits wide
endmodule

module Multiplexer (
  input  in_1,
  input  in_2,
  input  in_3,
  input  in_4,
  input  in_5,
  input  in_6,
  input  in_7,
  input  in_8,
  input  c2,
  input  c1,
  input  c0,
  output out_12
);

  wire transistor_1_out, transistor_2_out, transistor_3_out, transistor_4_out, transistor_5_out,
       transistor_6_out, transistor_7_out, transistor_8_out, transistor_9_out, transistor_11_out,
       transistor_14_out, transistor_16_out, transistor_18_out, transistor_20_out, transistor_22_out,
       transistor_23_out;

  Transistor #(.gate("br")) transistor_1 (.in(in_1), .out(transistor_1_out), .gate(c2));
  Transistor #(.gate("br")) transistor_2 (.in(in_2), .out(transistor_2_out), .gate(c2));
  Transistor #(.gate("br")) transistor_3 (.in(in_3), .out(transistor_3_out), .gate(c2));
  Transistor #(.gate("br")) transistor_4 (.in(in_4), .out(transistor_4_out), .gate(c2));
  Transistor #(.\type ("n"), .gate("br")) transistor_5 (.in(in_5), .out(transistor_5_out), .gate(c2));
  Transistor #(.\type ("n"), .gate("br")) transistor_6 (.in(in_6), .out(transistor_6_out), .gate(c2));
  Transistor #(.\type ("n"), .gate("br")) transistor_7 (.in(in_7), .out(transistor_7_out), .gate(c2));
  Transistor #(.\type ("n"), .gate("br")) transistor_8 (.in(in_8), .out(transistor_8_out), .gate(c2));
  Transistor #(.gate("br")) transistor_9 (.in(transistor_1_out), .out(transistor_9_out), .gate(c1));
  Transistor #(.gate("br")) transistor_10 (.in(transistor_9_out), .out(out_12), .gate(c0));
  Transistor #(.gate("br")) transistor_11 (.in(transistor_2_out), .out(transistor_11_out), .gate(c1));
  Transistor #(.\type ("n"), .gate("br")) transistor_12 (.in(transistor_11_out), .out(out_12), .gate(c0));
  Transistor #(.gate("br")) transistor_13 (.in(transistor_14_out), .out(out_12), .gate(c0));
  Transistor #(.\type ("n"), .gate("br")) transistor_14 (.in(transistor_3_out), .out(transistor_14_out), .gate(c1));
  Transistor #(.\type ("n"), .gate("br")) transistor_15 (.in(transistor_16_out), .out(out_12), .gate(c0));
  Transistor #(.\type ("n"), .gate("br")) transistor_16 (.in(transistor_4_out), .out(transistor_16_out), .gate(c1));
  Transistor #(.gate("br")) transistor_17 (.in(transistor_18_out), .out(out_12), .gate(c0));
  Transistor #(.gate("br")) transistor_18 (.in(transistor_5_out), .out(transistor_18_out), .gate(c1));
  Transistor #(.\type ("n"), .gate("br")) transistor_19 (.in(transistor_20_out), .out(out_12), .gate(c0));
  Transistor #(.gate("br")) transistor_20 (.in(transistor_6_out), .out(transistor_20_out), .gate(c1));
  Transistor #(.gate("br")) transistor_21 (.in(transistor_22_out), .out(out_12), .gate(c0));
  Transistor #(.\type ("n"), .gate("br")) transistor_22 (.in(transistor_7_out), .out(transistor_22_out), .gate(c1));
  Transistor #(.\type ("n"), .gate("br")) transistor_23 (.in(transistor_8_out), .out(transistor_23_out), .gate(c1));
  Transistor #(.\type ("n"), .gate("br")) transistor_24 (.in(transistor_23_out), .out(out_12), .gate(c0));
endmodule

module Demultiplexer (
  input  a,
  input  c2,
  input  c1,
  input  c0,
  output x,
  output x2,
  output x3,
  output x4,
  output x5,
  output x6,
  output x7,
  output x8
);

  wire not_1_out, not_2_out, not_3_out, not_4_out, not_5_out, not_6_out, not_7_out, not_8_out, not_9_out,
       not_10_out, not_11_out, not_12_out;

  not not_1 (not_1_out, c2);
  not not_2 (not_2_out, c1);
  not not_3 (not_3_out, c0);
  not not_4 (not_4_out, c2);
  not not_5 (not_5_out, c1);
  not not_6 (not_6_out, c2);
  not not_7 (not_7_out, c0);
  not not_8 (not_8_out, c2);
  not not_9 (not_9_out, c1);
  not not_10 (not_10_out, c0);
  not not_11 (not_11_out, c1);
  not not_12 (not_12_out, c0);
  and and_1 (x8, a, c2, c1, c0);
  and and_2 (x, a, not_1_out, not_2_out, not_3_out);
  and and_3 (x2, a, not_4_out, not_5_out, c0);
  and and_4 (x3, a, not_6_out, c1, not_7_out);
  and and_5 (x4, a, not_8_out, c1, c0);
  and and_6 (x5, a, c2, not_9_out, not_10_out);
  and and_7 (x6, a, c2, not_11_out, c0);
  and and_8 (x7, a, c2, c1, not_12_out);
endmodule
