// Logisim project CBRLAB6.circ as structural Verilog: 8 circuits, main circuit main
module main (
  input  SR_Flip_Flop,
  input  Preset,
  input  in_3,
  input  in_4,
  input  Trigger,
  input  in_6,
  input  Preset_2,
  input  Preset_3,
  input  in_9,
  input  Clear,
  input  Clock,
  input  Data,
  input  Data_2,
  input  Clear_2,
  input  Clock_2,
  input  Preset_4,
  input  Clear_3,
  input  Clock_3,
  input  Clear_4,
  input  Clock_4,
  input  Toggle,
  input  Clock_5,
  input  Preset_5,
  input  Preset_6,
  input  Clear_5,
  input  Data_3,
  input  Data_4,
  input  Clear_6,
  input  Clear_7,
  input  Clock_6,
  input  Clock_7,
  output out_32,
  output out_33,
  output out_34,
  output out_35,
  output out_36,
  output out_37,
  output out_38,
  output out_39,
  output out_40,
  output out_41,
  output [3:0] out_42,
  output out_43,
  output out_44,
  output out_45,
  output out_46
);

  wire not_1_out, not_2_out, rising_edge_detector_1_out_2, rising_edge_detector_2_out_2;

  SR_Flip_Flop sr_ff_1 (.in_1(SR_Flip_Flop), .in_2(in_6), .in_3(in_4), .out_4(out_32), .out_5(out_35));
  Rising_Edge_Detector rising_edge_detector_1 (.in_1(Clock_6), .out_2(rising_edge_detector_1_out_2));
  D_Flip_Flop d_ff_1 (.in_2(Data), .in_3(Clock_3), .out_5(out_38), .out_6(out_40), .in_1(Preset_2), .in_4(Clear_3));
  D_Flip_Flop d_ff_2 (
    .in_2(Data_3), .in_3(rising_edge_detector_1_out_2), .out_5(out_43), .out_6(out_45), .in_1(Preset_5),
    .in_4(Clear_6));
  not not_1 (not_1_out, Clock_4);
  Rising_Edge_Detector rising_edge_detector_2 (.in_1(not_2_out), .out_2(rising_edge_detector_2_out_2));
  not not_2 (not_2_out, Clock_7);
  D_Flip_Flop d_ff_3 (.in_2(Data_2), .in_3(not_1_out), .out_5(out_39), .out_6(out_41), .in_1(Preset_3), .in_4(Clear_4));
  D_Flip_Flop d_ff_4 (
    .in_2(Data_4), .in_3(rising_edge_detector_2_out_2), .out_5(out_44), .out_6(out_46), .in_1(Preset_6),
    .in_4(Clear_7));
  T_Flip_Flop t_ff_1 (.in_2(Trigger), .out_5(out_33), .out_6(out_36), .in_1(Preset), .in_3(Clear), .in_4(Clock));
  Binary_Counter binary_counter_1 (.in_1(Toggle), .in_2(Clock_5), .in_3(Clear_5), .out_4(out_42));
  // Probe on out_42
  JK_Flip_Flop jk_ff_1 (
    .in_2(in_3), .in_3(Clock_2), .in_4(in_9), .out_6(out_34), .out_7(out_37), .in_1(Preset_4), .in_5(Clear_2));

  // Notes on the sheet:
  //   High Level
  //   Rising Edge
  //   D Flip-Flops
  //   Low Level
  //   Falling Edge
  //   T Flip-Flop
  //   Counter
  //   In loving memory of Jack Kilby
endmodule

module Rising_Edge_Detector (
  input  in_1,
  output out_2
);

  wire not_1_out, not_2_out, not_3_out;

  not not_1 (not_1_out, in_1);
  not not_2 (not_2_out, not_1_out);
  not not_3 (not_3_out, not_2_out);
  and and_1 (out_2, not_3_out, in_1);
endmodule

module SR_Flip_Flop (
  input  in_1,
  input  in_2,
  input  in_3,
  output out_4,
  output out_5
);

  wire bootstrapper_1_out_1, nand_1_out, nand_4_out;

  nand nand_1 (nand_1_out, in_1, in_2);
  nand nand_2 (out_4, nand_1_out, out_5);
  nand nand_3 (out_5, out_4, ~bootstrapper_1_out_1, nand_4_out);  // NAND_Gate
  nand nand_4 (nand_4_out, in_2, in_3);
  Bootstrapper bootstrapper_1 (.out_1(bootstrapper_1_out_1));
endmodule

module D_Flip_Flop (
  input  in_1,
  input  in_2,
  input  in_3,
  input  in_4,
  output out_5,
  output out_6
);

  wire bootstrapper_1_out_1, nand_1_out, nand_3_out, or_1_out;

  Bootstrapper bootstrapper_1 (.out_1(bootstrapper_1_out_1));
  nand nand_1 (nand_1_out, in_2, in_3);
  nand nand_2 (out_5, ~in_1, nand_1_out, out_6);  // NAND_Gate
  nand nand_3 (nand_3_out, in_3, ~in_2);  // NAND_Gate
  nand nand_4 (out_6, out_5, nand_3_out, ~or_1_out);  // NAND_Gate
  or or_1 (or_1_out, bootstrapper_1_out_1, in_4);
endmodule

module T_Flip_Flop (
  input  in_1,
  input  in_2,
  input  in_3,
  input  in_4,
  output out_5,
  output out_6
);

  wire rising_edge_detector_1_out_2, xor_1_out;

  xor xor_1 (xor_1_out, out_5, in_2);
  D_Flip_Flop d_ff_1 (
    .in_2(xor_1_out), .in_3(rising_edge_detector_1_out_2), .out_5(out_5), .out_6(out_6), .in_1(in_1),
    .in_4(in_3));
  Rising_Edge_Detector rising_edge_detector_1 (.in_1(in_4), .out_2(rising_edge_detector_1_out_2));
endmodule

module JK_Flip_Flop (
  input  in_1,
  input  in_2,
  input  in_3,
  input  in_4,
  input  in_5,
  output out_6,
  output out_7
);

  wire bootstrapper_1_out_1, nand_1_out, nand_2_out, nand_3_out, nand_4_out, not_1_out, or_1_out,
       rising_edge_detector_1_out_2;

  Rising_Edge_Detector rising_edge_detector_1 (.in_1(in_3), .out_2(rising_edge_detector_1_out_2));
  not not_1 (not_1_out, rising_edge_detector_1_out_2);
  nand nand_1 (nand_1_out, out_7, in_2, rising_edge_detector_1_out_2);
  nand nand_2 (nand_2_out, ~in_1, nand_1_out, nand_3_out);  // NAND_Gate
  nand nand_3 (nand_3_out, nand_2_out, nand_4_out, ~or_1_out);  // NAND_Gate
  nand nand_4 (nand_4_out, rising_edge_detector_1_out_2, in_4, out_6);
  or or_1 (or_1_out, bootstrapper_1_out_1, in_5);
  Bootstrapper bootstrapper_1 (.out_1(bootstrapper_1_out_1));
  SR_Flip_Flop sr_ff_1 (.in_1(nand_2_out), .in_2(not_1_out), .in_3(nand_3_out), .out_4(out_6), .out_5(out_7));
endmodule

module Binary_Counter (
  input  in_1,
  input  in_2,
  input  in_3,
  output [3:0] out_4
);

  wire bootstrapper_1_out_1, or_1_out, t_ff_1_out_6, t_ff_2_out_6, t_ff_3_out_6;

  or or_1 (or_1_out, in_3, bootstrapper_1_out_1);
  Bootstrapper bootstrapper_1 (.out_1(bootstrapper_1_out_1));
  T_Flip_Flop t_ff_1 (
    .in_2(in_1), .out_5(out_4[1]), .out_6(t_ff_1_out_6), .in_1(1'b0), .in_3(or_1_out), .in_4(t_ff_2_out_6));
  T_Flip_Flop t_ff_2 (.in_2(in_1), .out_5(out_4[0]), .out_6(t_ff_2_out_6), .in_1(1'b0), .in_3(or_1_out), .in_4(in_2));
  T_Flip_Flop t_ff_3 (
    .in_2(in_1), .out_5(out_4[2]), .out_6(t_ff_3_out_6), .in_1(1'b0), .in_3(or_1_out), .in_4(t_ff_1_out_6));
  T_Flip_Flop t_ff_4 (.in_2(in_1), .out_5(out_4[3]), .in_1(1'b0), .in_3(or_1_out), .in_4(t_ff_3_out_6));  // open: out_6
endmodule

module Bootstrapper (
  output out_1
);

  wire clock_1_out;

  Clock clock_1 (.out(clock_1_out));
  S_R_Flip_Flop s_r_ff_1 (.S(clock_1_out), .clk(clock_1_out), .R(1'b0), .Qn(out_1));  // open: Q, preset, reset, en
endmodule
