// Logisim project CBRLABminesweeper.circ as structural Verilog: 7 circuits, main circuit main
module main (
);

  wire F_2_out, F_3_out, F_4_out, F_5_out, F_6_out, F_7_out, F_8_out, F_9_out, F_10_out, F_11_out, F_12_out,
       F_13_out, F_14_out, F_15_out, F_16_out, F_17_out, F_18_out, F_19_out, F_20_out, F_21_out, F_22_out,
       F_23_out, F_24_out, F_25_out, F_26_out, F_27_out, F_28_out, F_29_out, F_30_out, F_31_out, F_32_out,
       F_33_out, F_34_out, F_35_out, F_36_out, F_out, O_2_out, O_3_out, O_4_out, O_5_out, O_6_out, O_7_out,
       O_8_out, O_9_out, O_10_out, O_11_out, O_12_out, O_13_out, O_14_out, O_15_out, O_16_out, O_17_out,
       O_18_out, O_19_out, O_20_out, O_21_out, O_22_out, O_23_out, O_24_out, O_25_out, O_26_out, O_27_out,
       O_28_out, O_29_out, O_30_out, O_31_out, O_32_out, O_33_out, O_34_out, O_35_out, O_36_out, O_out;
  wire [2:0] cell_handler_1_celldata_out, cell_handler_2_celldata_out, cell_handler_3_celldata_out,
       cell_handler_4_celldata_out, cell_handler_5_celldata_out, cell_handler_6_celldata_out,
       cell_handler_7_celldata_out, cell_handler_8_celldata_out, cell_handler_9_celldata_out,
       cell_handler_10_celldata_out, cell_handler_11_celldata_out, cell_handler_12_celldata_out,
       cell_handler_13_celldata_out, cell_handler_14_celldata_out, cell_handler_15_celldata_out,
       cell_handler_16_celldata_out, cell_handler_17_celldata_out, cell_handler_18_celldata_out,
       cell_handler_19_celldata_out, cell_handler_20_celldata_out, cell_handler_21_celldata_out,
       cell_handler_22_celldata_out, cell_handler_23_celldata_out, cell_handler_24_celldata_out,
       cell_handler_25_celldata_out, cell_handler_26_celldata_out, cell_handler_27_celldata_out,
       cell_handler_28_celldata_out, cell_handler_29_celldata_out, cell_handler_30_celldata_out,
       cell_handler_31_celldata_out, cell_handler_32_celldata_out, cell_handler_33_celldata_out,
       cell_handler_34_celldata_out, cell_handler_35_celldata_out, cell_handler_36_celldata_out;
  wire [3:0] cell_handler_1_out_4, cell_handler_1_out_5, cell_handler_2_out_4, cell_handler_2_out_5,
       cell_handler_3_out_4, cell_handler_3_out_5, cell_handler_4_out_4, cell_handler_4_out_5,
       cell_handler_5_out_4, cell_handler_5_out_5, cell_handler_6_out_4, cell_handler_6_out_5,
       cell_handler_7_out_4, cell_handler_7_out_5, cell_handler_8_out_4, cell_handler_8_out_5,
       cell_handler_9_out_4, cell_handler_9_out_5, cell_handler_10_out_4, cell_handler_10_out_5,
       cell_handler_11_out_4, cell_handler_11_out_5, cell_handler_12_out_4, cell_handler_12_out_5,
       cell_handler_13_out_4, cell_handler_13_out_5, cell_handler_14_out_4, cell_handler_14_out_5,
       cell_handler_15_out_4, cell_handler_15_out_5, cell_handler_16_out_4, cell_handler_16_out_5,
       cell_handler_17_out_4, cell_handler_17_out_5, cell_handler_18_out_4, cell_handler_18_out_5,
       cell_handler_19_out_4, cell_handler_19_out_5, cell_handler_20_out_4, cell_handler_20_out_5,
       cell_handler_21_out_4, cell_handler_21_out_5, cell_handler_22_out_4, cell_handler_22_out_5,
       cell_handler_23_out_4, cell_handler_23_out_5, cell_handler_24_out_4, cell_handler_24_out_5,
       cell_handler_25_out_4, cell_handler_25_out_5, cell_handler_26_out_4, cell_handler_26_out_5,
       cell_handler_27_out_4, cell_handler_27_out_5, cell_handler_28_out_4, cell_handler_28_out_5,
       cell_handler_29_out_4, cell_handler_29_out_5, cell_handler_30_out_4, cell_handler_30_out_5,
       cell_handler_31_out_4, cell_handler_31_out_5, cell_handler_32_out_4, cell_handler_32_out_5,
       cell_handler_33_out_4, cell_handler_33_out_5, cell_handler_34_out_4, cell_handler_34_out_5,
       cell_handler_35_out_4, cell_handler_35_out_5, cell_handler_36_out_4, cell_handler_36_out_5;
  wire [23:0] funny_merger_1_out_9, funny_merger_2_out_9, funny_merger_3_out_9, funny_merger_4_out_9,
       funny_merger_5_out_9, funny_merger_6_out_9, funny_merger_7_out_9, funny_merger_8_out_9,
       funny_merger_9_out_9, funny_merger_10_out_9, funny_merger_11_out_9, funny_merger_12_out_9,
       funny_merger_13_out_9, funny_merger_14_out_9, funny_merger_15_out_9, funny_merger_16_out_9,
       funny_merger_17_out_9, funny_merger_18_out_9, funny_merger_19_out_9, funny_merger_20_out_9,
       funny_merger_21_out_9, funny_merger_22_out_9, funny_merger_23_out_9, funny_merger_24_out_9,
       funny_merger_25_out_9, funny_merger_26_out_9, funny_merger_27_out_9, funny_merger_28_out_9,
       funny_merger_29_out_9, funny_merger_30_out_9, funny_merger_31_out_9, funny_merger_32_out_9,
       funny_merger_33_out_9, funny_merger_34_out_9, funny_merger_35_out_9, funny_merger_36_out_9;

  Button F (.out(F_out));
  Funny_Merger funny_merger_1 (
    .in_1(cell_handler_11_celldata_out), .in_2(cell_handler_5_celldata_out), .in_3(3'b000),
    .in_4(cell_handler_12_celldata_out), .in_5(3'b000), .in_6(3'b000), .in_7(cell_handler_1_celldata_out),
    .in_8(cell_handler_7_celldata_out), .out_9(funny_merger_1_out_9));
  Button O (.out(O_out));
  Button F_2 (.out(F_2_out));
  _7_Segment_Display u_7_segment_display_1 (
    .g(cell_handler_1_out_4[3]), .f(cell_handler_1_out_4[2]), .a(cell_handler_1_out_4[1]),
    .b(cell_handler_1_out_4[0]), .e(cell_handler_1_out_5[3]), .d(cell_handler_1_out_5[2]),
    .c(cell_handler_1_out_5[1]), .dp(cell_handler_1_out_5[0]));
  Funny_Merger funny_merger_2 (
    .in_1(cell_handler_12_celldata_out), .in_2(cell_handler_6_celldata_out), .in_3(3'b000),
    .in_4(cell_handler_7_celldata_out), .in_5(3'b000), .in_6(3'b000), .in_7(cell_handler_2_celldata_out),
    .in_8(cell_handler_8_celldata_out), .out_9(funny_merger_2_out_9));
  Cell_Handler cell_handler_1 (
    .Neighbour_Data(funny_merger_2_out_9), .CellData_Out(cell_handler_1_celldata_out),
    .out_4(cell_handler_1_out_4), .out_5(cell_handler_1_out_5), .Flagger(F_2_out), .Opener(O_2_out));
  Button O_2 (.out(O_2_out));
  Button F_3 (.out(F_3_out));
  _7_Segment_Display u_7_segment_display_2 (
    .g(cell_handler_2_out_4[3]), .f(cell_handler_2_out_4[2]), .a(cell_handler_2_out_4[1]),
    .b(cell_handler_2_out_4[0]), .e(cell_handler_2_out_5[3]), .d(cell_handler_2_out_5[2]),
    .c(cell_handler_2_out_5[1]), .dp(cell_handler_2_out_5[0]));
  Funny_Merger funny_merger_3 (
    .in_1(cell_handler_7_celldata_out), .in_2(cell_handler_1_celldata_out), .in_3(3'b000),
    .in_4(cell_handler_8_celldata_out), .in_5(3'b000), .in_6(3'b000), .in_7(3'b000), .in_8(3'b000),
    .out_9(funny_merger_3_out_9));
  Cell_Handler cell_handler_2 (
    .Neighbour_Data(funny_merger_3_out_9), .CellData_Out(cell_handler_2_celldata_out),
    .out_4(cell_handler_2_out_4), .out_5(cell_handler_2_out_5), .Flagger(F_3_out), .Opener(O_3_out));
  Button O_3 (.out(O_3_out));
  Button F_4 (.out(F_4_out));
  _7_Segment_Display u_7_segment_display_3 (
    .g(cell_handler_3_out_4[3]), .f(cell_handler_3_out_4[2]), .a(cell_handler_3_out_4[1]),
    .b(cell_handler_3_out_4[0]), .e(cell_handler_3_out_5[3]), .d(cell_handler_3_out_5[2]),
    .c(cell_handler_3_out_5[1]), .dp(cell_handler_3_out_5[0]));
  Funny_Merger funny_merger_4 (
    .in_1(3'b000), .in_2(3'b000), .in_3(3'b000), .in_4(cell_handler_9_celldata_out), .in_5(3'b000),
    .in_6(3'b000), .in_7(cell_handler_4_celldata_out), .in_8(cell_handler_10_celldata_out),
    .out_9(funny_merger_4_out_9));
  Cell_Handler cell_handler_3 (
    .Neighbour_Data(funny_merger_4_out_9), .CellData_Out(cell_handler_3_celldata_out),
    .out_4(cell_handler_3_out_4), .out_5(cell_handler_3_out_5), .Flagger(F_4_out), .Opener(O_4_out));
  Button O_4 (.out(O_4_out));
  Button F_5 (.out(F_5_out));
  _7_Segment_Display u_7_segment_display_4 (
    .g(cell_handler_4_out_4[3]), .f(cell_handler_4_out_4[2]), .a(cell_handler_4_out_4[1]),
    .b(cell_handler_4_out_4[0]), .e(cell_handler_4_out_5[3]), .d(cell_handler_4_out_5[2]),
    .c(cell_handler_4_out_5[1]), .dp(cell_handler_4_out_5[0]));
  Funny_Merger funny_merger_5 (
    .in_1(cell_handler_9_celldata_out), .in_2(cell_handler_3_celldata_out), .in_3(3'b000),
    .in_4(cell_handler_10_celldata_out), .in_5(3'b000), .in_6(3'b000), .in_7(cell_handler_5_celldata_out),
    .in_8(cell_handler_11_celldata_out), .out_9(funny_merger_5_out_9));
  Cell_Handler cell_handler_4 (
    .Neighbour_Data(funny_merger_5_out_9), .CellData_Out(cell_handler_4_celldata_out),
    .out_4(cell_handler_4_out_4), .out_5(cell_handler_4_out_5), .Flagger(F_5_out), .Opener(O_5_out));
  Button O_5 (.out(O_5_out));
  _7_Segment_Display u_7_segment_display_5 (
    .g(cell_handler_5_out_4[3]), .f(cell_handler_5_out_4[2]), .a(cell_handler_5_out_4[1]),
    .b(cell_handler_5_out_4[0]), .e(cell_handler_5_out_5[3]), .d(cell_handler_5_out_5[2]),
    .c(cell_handler_5_out_5[1]), .dp(cell_handler_5_out_5[0]));
  Button F_6 (.out(F_6_out));
  Funny_Merger funny_merger_6 (
    .in_1(cell_handler_10_celldata_out), .in_2(cell_handler_4_celldata_out), .in_3(3'b000),
    .in_4(cell_handler_11_celldata_out), .in_5(3'b000), .in_6(3'b000), .in_7(cell_handler_6_celldata_out),
    .in_8(cell_handler_12_celldata_out), .out_9(funny_merger_6_out_9));
  Cell_Handler cell_handler_5 (
    .Neighbour_Data(funny_merger_6_out_9), .CellData_Out(cell_handler_5_celldata_out),
    .out_4(cell_handler_5_out_4), .out_5(cell_handler_5_out_5), .Flagger(F_6_out), .Opener(O_6_out));
  Button O_6 (.out(O_6_out));
  _7_Segment_Display u_7_segment_display_6 (
    .g(cell_handler_6_out_4[3]), .f(cell_handler_6_out_4[2]), .a(cell_handler_6_out_4[1]),
    .b(cell_handler_6_out_4[0]), .e(cell_handler_6_out_5[3]), .d(cell_handler_6_out_5[2]),
    .c(cell_handler_6_out_5[1]), .dp(cell_handler_6_out_5[0]));
  Cell_Handler cell_handler_6 (
    .Neighbour_Data(funny_merger_1_out_9), .CellData_Out(cell_handler_6_celldata_out),
    .out_4(cell_handler_6_out_4), .out_5(cell_handler_6_out_5), .Flagger(F_out), .Opener(O_out));
  Funny_Merger funny_merger_7 (
    .in_1(cell_handler_15_celldata_out), .in_2(cell_handler_11_celldata_out),
    .in_3(cell_handler_5_celldata_out), .in_4(cell_handler_16_celldata_out),
    .in_5(cell_handler_6_celldata_out), .in_6(cell_handler_1_celldata_out),
    .in_7(cell_handler_7_celldata_out), .in_8(cell_handler_17_celldata_out), .out_9(funny_merger_7_out_9));
  Button F_7 (.out(F_7_out));
  Funny_Merger funny_merger_8 (
    .in_1(cell_handler_16_celldata_out), .in_2(cell_handler_12_celldata_out),
    .in_3(cell_handler_6_celldata_out), .in_4(cell_handler_17_celldata_out),
    .in_5(cell_handler_1_celldata_out), .in_6(cell_handler_2_celldata_out),
    .in_7(cell_handler_8_celldata_out), .in_8(cell_handler_13_celldata_out), .out_9(funny_merger_8_out_9));
  Cell_Handler cell_handler_7 (
    .Neighbour_Data(funny_merger_8_out_9), .CellData_Out(cell_handler_7_celldata_out),
    .out_4(cell_handler_7_out_4), .out_5(cell_handler_7_out_5), .Flagger(F_7_out), .Opener(O_7_out));
  Button O_7 (.out(O_7_out));
  Button F_8 (.out(F_8_out));
  _7_Segment_Display u_7_segment_display_7 (
    .g(cell_handler_8_out_4[3]), .f(cell_handler_8_out_4[2]), .a(cell_handler_8_out_4[1]),
    .b(cell_handler_8_out_4[0]), .e(cell_handler_8_out_5[3]), .d(cell_handler_8_out_5[2]),
    .c(cell_handler_8_out_5[1]), .dp(cell_handler_8_out_5[0]));
  Funny_Merger funny_merger_9 (
    .in_1(cell_handler_17_celldata_out), .in_2(cell_handler_7_celldata_out),
    .in_3(cell_handler_1_celldata_out), .in_4(cell_handler_13_celldata_out),
    .in_5(cell_handler_2_celldata_out), .in_6(3'b000), .in_7(3'b000), .in_8(3'b000),
    .out_9(funny_merger_9_out_9));
  Cell_Handler cell_handler_8 (
    .Neighbour_Data(funny_merger_9_out_9), .CellData_Out(cell_handler_8_celldata_out),
    .out_4(cell_handler_8_out_4), .out_5(cell_handler_8_out_5), .Flagger(F_8_out), .Opener(O_8_out));
  Button O_8 (.out(O_8_out));
  Button F_9 (.out(F_9_out));
  Funny_Merger funny_merger_10 (
    .in_1(3'b000), .in_2(3'b000), .in_3(3'b000), .in_4(cell_handler_18_celldata_out),
    .in_5(cell_handler_3_celldata_out), .in_6(cell_handler_4_celldata_out),
    .in_7(cell_handler_10_celldata_out), .in_8(cell_handler_14_celldata_out), .out_9(funny_merger_10_out_9));
  Cell_Handler cell_handler_9 (
    .Neighbour_Data(funny_merger_10_out_9), .CellData_Out(cell_handler_9_celldata_out),
    .out_4(cell_handler_9_out_4), .out_5(cell_handler_9_out_5), .Flagger(F_9_out), .Opener(O_9_out));
  Button O_9 (.out(O_9_out));
  Button F_10 (.out(F_10_out));
  _7_Segment_Display u_7_segment_display_8 (
    .g(cell_handler_10_out_4[3]), .f(cell_handler_10_out_4[2]), .a(cell_handler_10_out_4[1]),
    .b(cell_handler_10_out_4[0]), .e(cell_handler_10_out_5[3]), .d(cell_handler_10_out_5[2]),
    .c(cell_handler_10_out_5[1]), .dp(cell_handler_10_out_5[0]));
  Funny_Merger funny_merger_11 (
    .in_1(cell_handler_18_celldata_out), .in_2(cell_handler_9_celldata_out),
    .in_3(cell_handler_3_celldata_out), .in_4(cell_handler_14_celldata_out),
    .in_5(cell_handler_4_celldata_out), .in_6(cell_handler_5_celldata_out),
    .in_7(cell_handler_11_celldata_out), .in_8(cell_handler_15_celldata_out), .out_9(funny_merger_11_out_9));
  Cell_Handler cell_handler_10 (
    .Neighbour_Data(funny_merger_11_out_9), .CellData_Out(cell_handler_10_celldata_out),
    .out_4(cell_handler_10_out_4), .out_5(cell_handler_10_out_5), .Flagger(F_10_out), .Opener(O_10_out));
  Button O_10 (.out(O_10_out));
  _7_Segment_Display u_7_segment_display_9 (
    .g(cell_handler_11_out_4[3]), .f(cell_handler_11_out_4[2]), .a(cell_handler_11_out_4[1]),
    .b(cell_handler_11_out_4[0]), .e(cell_handler_11_out_5[3]), .d(cell_handler_11_out_5[2]),
    .c(cell_handler_11_out_5[1]), .dp(cell_handler_11_out_5[0]));
  Button F_11 (.out(F_11_out));
  Funny_Merger funny_merger_12 (
    .in_1(cell_handler_14_celldata_out), .in_2(cell_handler_10_celldata_out),
    .in_3(cell_handler_4_celldata_out), .in_4(cell_handler_15_celldata_out),
    .in_5(cell_handler_5_celldata_out), .in_6(cell_handler_6_celldata_out),
    .in_7(cell_handler_12_celldata_out), .in_8(cell_handler_16_celldata_out), .out_9(funny_merger_12_out_9));
  Cell_Handler cell_handler_11 (
    .Neighbour_Data(funny_merger_12_out_9), .CellData_Out(cell_handler_11_celldata_out),
    .out_4(cell_handler_11_out_4), .out_5(cell_handler_11_out_5), .Flagger(F_11_out), .Opener(O_11_out));
  Button O_11 (.out(O_11_out));
  _7_Segment_Display u_7_segment_display_10 (
    .g(cell_handler_12_out_4[3]), .f(cell_handler_12_out_4[2]), .a(cell_handler_12_out_4[1]),
    .b(cell_handler_12_out_4[0]), .e(cell_handler_12_out_5[3]), .d(cell_handler_12_out_5[2]),
    .c(cell_handler_12_out_5[1]), .dp(cell_handler_12_out_5[0]));
  Button F_12 (.out(F_12_out));
  Cell_Handler cell_handler_12 (
    .Neighbour_Data(funny_merger_7_out_9), .CellData_Out(cell_handler_12_celldata_out),
    .out_4(cell_handler_12_out_4), .out_5(cell_handler_12_out_5), .Flagger(F_12_out), .Opener(O_12_out));
  Button O_12 (.out(O_12_out));
  _7_Segment_Display u_7_segment_display_11 (
    .g(cell_handler_7_out_4[3]), .f(cell_handler_7_out_4[2]), .a(cell_handler_7_out_4[1]),
    .b(cell_handler_7_out_4[0]), .e(cell_handler_7_out_5[3]), .d(cell_handler_7_out_5[2]),
    .c(cell_handler_7_out_5[1]), .dp(cell_handler_7_out_5[0]));
  _7_Segment_Display u_7_segment_display_12 (
    .g(cell_handler_9_out_4[3]), .f(cell_handler_9_out_4[2]), .a(cell_handler_9_out_4[1]),
    .b(cell_handler_9_out_4[0]), .e(cell_handler_9_out_5[3]), .d(cell_handler_9_out_5[2]),
    .c(cell_handler_9_out_5[1]), .dp(cell_handler_9_out_5[0]));
  Button F_13 (.out(F_13_out));
  Funny_Merger funny_merger_13 (
    .in_1(cell_handler_22_celldata_out), .in_2(cell_handler_16_celldata_out),
    .in_3(cell_handler_12_celldata_out), .in_4(cell_handler_23_celldata_out),
    .in_5(cell_handler_7_celldata_out), .in_6(cell_handler_8_celldata_out),
    .in_7(cell_handler_13_celldata_out), .in_8(cell_handler_19_celldata_out), .out_9(funny_merger_13_out_9));
  Button O_13 (.out(O_13_out));
  Button F_14 (.out(F_14_out));
  _7_Segment_Display u_7_segment_display_13 (
    .g(cell_handler_13_out_4[3]), .f(cell_handler_13_out_4[2]), .a(cell_handler_13_out_4[1]),
    .b(cell_handler_13_out_4[0]), .e(cell_handler_13_out_5[3]), .d(cell_handler_13_out_5[2]),
    .c(cell_handler_13_out_5[1]), .dp(cell_handler_13_out_5[0]));
  Funny_Merger funny_merger_14 (
    .in_1(cell_handler_23_celldata_out), .in_2(cell_handler_17_celldata_out),
    .in_3(cell_handler_7_celldata_out), .in_4(cell_handler_19_celldata_out),
    .in_5(cell_handler_8_celldata_out), .in_6(3'b000), .in_7(3'b000), .in_8(3'b000),
    .out_9(funny_merger_14_out_9));
  Cell_Handler cell_handler_13 (
    .Neighbour_Data(funny_merger_14_out_9), .CellData_Out(cell_handler_13_celldata_out),
    .out_4(cell_handler_13_out_4), .out_5(cell_handler_13_out_5), .Flagger(F_14_out), .Opener(O_14_out));
  Button O_14 (.out(O_14_out));
  Button F_15 (.out(F_15_out));
  Funny_Merger funny_merger_15 (
    .in_1(3'b000), .in_2(3'b000), .in_3(3'b000), .in_4(cell_handler_24_celldata_out),
    .in_5(cell_handler_9_celldata_out), .in_6(cell_handler_10_celldata_out),
    .in_7(cell_handler_14_celldata_out), .in_8(cell_handler_20_celldata_out), .out_9(funny_merger_15_out_9));
  Button O_15 (.out(O_15_out));
  Button F_16 (.out(F_16_out));
  _7_Segment_Display u_7_segment_display_14 (
    .g(cell_handler_14_out_4[3]), .f(cell_handler_14_out_4[2]), .a(cell_handler_14_out_4[1]),
    .b(cell_handler_14_out_4[0]), .e(cell_handler_14_out_5[3]), .d(cell_handler_14_out_5[2]),
    .c(cell_handler_14_out_5[1]), .dp(cell_handler_14_out_5[0]));
  Funny_Merger funny_merger_16 (
    .in_1(cell_handler_24_celldata_out), .in_2(cell_handler_18_celldata_out),
    .in_3(cell_handler_9_celldata_out), .in_4(cell_handler_20_celldata_out),
    .in_5(cell_handler_10_celldata_out), .in_6(cell_handler_11_celldata_out),
    .in_7(cell_handler_15_celldata_out), .in_8(cell_handler_21_celldata_out), .out_9(funny_merger_16_out_9));
  Cell_Handler cell_handler_14 (
    .Neighbour_Data(funny_merger_16_out_9), .CellData_Out(cell_handler_14_celldata_out),
    .out_4(cell_handler_14_out_4), .out_5(cell_handler_14_out_5), .Flagger(F_16_out), .Opener(O_16_out));
  Button O_16 (.out(O_16_out));
  Button F_17 (.out(F_17_out));
  _7_Segment_Display u_7_segment_display_15 (
    .g(cell_handler_15_out_4[3]), .f(cell_handler_15_out_4[2]), .a(cell_handler_15_out_4[1]),
    .b(cell_handler_15_out_4[0]), .e(cell_handler_15_out_5[3]), .d(cell_handler_15_out_5[2]),
    .c(cell_handler_15_out_5[1]), .dp(cell_handler_15_out_5[0]));
  Funny_Merger funny_merger_17 (
    .in_1(cell_handler_20_celldata_out), .in_2(cell_handler_14_celldata_out),
    .in_3(cell_handler_10_celldata_out), .in_4(cell_handler_21_celldata_out),
    .in_5(cell_handler_11_celldata_out), .in_6(cell_handler_12_celldata_out),
    .in_7(cell_handler_16_celldata_out), .in_8(cell_handler_22_celldata_out), .out_9(funny_merger_17_out_9));
  Cell_Handler cell_handler_15 (
    .Neighbour_Data(funny_merger_17_out_9), .CellData_Out(cell_handler_15_celldata_out),
    .out_4(cell_handler_15_out_4), .out_5(cell_handler_15_out_5), .Flagger(F_17_out), .Opener(O_17_out));
  Button O_17 (.out(O_17_out));
  _7_Segment_Display u_7_segment_display_16 (
    .g(cell_handler_16_out_4[3]), .f(cell_handler_16_out_4[2]), .a(cell_handler_16_out_4[1]),
    .b(cell_handler_16_out_4[0]), .e(cell_handler_16_out_5[3]), .d(cell_handler_16_out_5[2]),
    .c(cell_handler_16_out_5[1]), .dp(cell_handler_16_out_5[0]));
  Button F_18 (.out(F_18_out));
  Funny_Merger funny_merger_18 (
    .in_1(cell_handler_21_celldata_out), .in_2(cell_handler_15_celldata_out),
    .in_3(cell_handler_11_celldata_out), .in_4(cell_handler_22_celldata_out),
    .in_5(cell_handler_12_celldata_out), .in_6(cell_handler_7_celldata_out),
    .in_7(cell_handler_17_celldata_out), .in_8(cell_handler_23_celldata_out), .out_9(funny_merger_18_out_9));
  Cell_Handler cell_handler_16 (
    .Neighbour_Data(funny_merger_18_out_9), .CellData_Out(cell_handler_16_celldata_out),
    .out_4(cell_handler_16_out_4), .out_5(cell_handler_16_out_5), .Flagger(F_18_out), .Opener(O_18_out));
  Button O_18 (.out(O_18_out));
  _7_Segment_Display u_7_segment_display_17 (
    .g(cell_handler_17_out_4[3]), .f(cell_handler_17_out_4[2]), .a(cell_handler_17_out_4[1]),
    .b(cell_handler_17_out_4[0]), .e(cell_handler_17_out_5[3]), .d(cell_handler_17_out_5[2]),
    .c(cell_handler_17_out_5[1]), .dp(cell_handler_17_out_5[0]));
  Cell_Handler cell_handler_17 (
    .Neighbour_Data(funny_merger_13_out_9), .CellData_Out(cell_handler_17_celldata_out),
    .out_4(cell_handler_17_out_4), .out_5(cell_handler_17_out_5), .Flagger(F_13_out), .Opener(O_13_out));
  _7_Segment_Display u_7_segment_display_18 (
    .g(cell_handler_18_out_4[3]), .f(cell_handler_18_out_4[2]), .a(cell_handler_18_out_4[1]),
    .b(cell_handler_18_out_4[0]), .e(cell_handler_18_out_5[3]), .d(cell_handler_18_out_5[2]),
    .c(cell_handler_18_out_5[1]), .dp(cell_handler_18_out_5[0]));
  Cell_Handler cell_handler_18 (
    .Neighbour_Data(funny_merger_15_out_9), .CellData_Out(cell_handler_18_celldata_out),
    .out_4(cell_handler_18_out_4), .out_5(cell_handler_18_out_5), .Flagger(F_15_out), .Opener(O_15_out));
  Funny_Merger funny_merger_19 (
    .in_1(cell_handler_26_celldata_out), .in_2(cell_handler_22_celldata_out),
    .in_3(cell_handler_16_celldata_out), .in_4(cell_handler_27_celldata_out),
    .in_5(cell_handler_17_celldata_out), .in_6(cell_handler_13_celldata_out),
    .in_7(cell_handler_19_celldata_out), .in_8(cell_handler_28_celldata_out), .out_9(funny_merger_19_out_9));
  Button F_19 (.out(F_19_out));
  Funny_Merger funny_merger_20 (
    .in_1(cell_handler_27_celldata_out), .in_2(cell_handler_23_celldata_out),
    .in_3(cell_handler_17_celldata_out), .in_4(cell_handler_28_celldata_out),
    .in_5(cell_handler_13_celldata_out), .in_6(3'b000), .in_7(3'b000), .in_8(3'b000),
    .out_9(funny_merger_20_out_9));
  Cell_Handler cell_handler_19 (
    .Neighbour_Data(funny_merger_20_out_9), .CellData_Out(cell_handler_19_celldata_out),
    .out_4(cell_handler_19_out_4), .out_5(cell_handler_19_out_5), .Flagger(F_19_out), .Opener(O_19_out));
  Button O_19 (.out(O_19_out));
  Funny_Merger funny_merger_21 (
    .in_1(3'b000), .in_2(3'b000), .in_3(3'b000), .in_4(cell_handler_29_celldata_out),
    .in_5(cell_handler_18_celldata_out), .in_6(cell_handler_14_celldata_out),
    .in_7(cell_handler_20_celldata_out), .in_8(cell_handler_30_celldata_out), .out_9(funny_merger_21_out_9));
  Button F_20 (.out(F_20_out));
  Funny_Merger funny_merger_22 (
    .in_1(cell_handler_29_celldata_out), .in_2(cell_handler_24_celldata_out),
    .in_3(cell_handler_18_celldata_out), .in_4(cell_handler_30_celldata_out),
    .in_5(cell_handler_14_celldata_out), .in_6(cell_handler_15_celldata_out),
    .in_7(cell_handler_21_celldata_out), .in_8(cell_handler_25_celldata_out), .out_9(funny_merger_22_out_9));
  Cell_Handler cell_handler_20 (
    .Neighbour_Data(funny_merger_22_out_9), .CellData_Out(cell_handler_20_celldata_out),
    .out_4(cell_handler_20_out_4), .out_5(cell_handler_20_out_5), .Flagger(F_20_out), .Opener(O_20_out));
  Button O_20 (.out(O_20_out));
  Button F_21 (.out(F_21_out));
  _7_Segment_Display u_7_segment_display_19 (
    .g(cell_handler_21_out_4[3]), .f(cell_handler_21_out_4[2]), .a(cell_handler_21_out_4[1]),
    .b(cell_handler_21_out_4[0]), .e(cell_handler_21_out_5[3]), .d(cell_handler_21_out_5[2]),
    .c(cell_handler_21_out_5[1]), .dp(cell_handler_21_out_5[0]));
  Funny_Merger funny_merger_23 (
    .in_1(cell_handler_30_celldata_out), .in_2(cell_handler_20_celldata_out),
    .in_3(cell_handler_14_celldata_out), .in_4(cell_handler_25_celldata_out),
    .in_5(cell_handler_15_celldata_out), .in_6(cell_handler_16_celldata_out),
    .in_7(cell_handler_22_celldata_out), .in_8(cell_handler_26_celldata_out), .out_9(funny_merger_23_out_9));
  Cell_Handler cell_handler_21 (
    .Neighbour_Data(funny_merger_23_out_9), .CellData_Out(cell_handler_21_celldata_out),
    .out_4(cell_handler_21_out_4), .out_5(cell_handler_21_out_5), .Flagger(F_21_out), .Opener(O_21_out));
  Button O_21 (.out(O_21_out));
  _7_Segment_Display u_7_segment_display_20 (
    .g(cell_handler_22_out_4[3]), .f(cell_handler_22_out_4[2]), .a(cell_handler_22_out_4[1]),
    .b(cell_handler_22_out_4[0]), .e(cell_handler_22_out_5[3]), .d(cell_handler_22_out_5[2]),
    .c(cell_handler_22_out_5[1]), .dp(cell_handler_22_out_5[0]));
  Button F_22 (.out(F_22_out));
  Funny_Merger funny_merger_24 (
    .in_1(cell_handler_25_celldata_out), .in_2(cell_handler_21_celldata_out),
    .in_3(cell_handler_15_celldata_out), .in_4(cell_handler_26_celldata_out),
    .in_5(cell_handler_16_celldata_out), .in_6(cell_handler_17_celldata_out),
    .in_7(cell_handler_23_celldata_out), .in_8(cell_handler_27_celldata_out), .out_9(funny_merger_24_out_9));
  Cell_Handler cell_handler_22 (
    .Neighbour_Data(funny_merger_24_out_9), .CellData_Out(cell_handler_22_celldata_out),
    .out_4(cell_handler_22_out_4), .out_5(cell_handler_22_out_5), .Flagger(F_22_out), .Opener(O_22_out));
  Button O_22 (.out(O_22_out));
  _7_Segment_Display u_7_segment_display_21 (
    .g(cell_handler_23_out_4[3]), .f(cell_handler_23_out_4[2]), .a(cell_handler_23_out_4[1]),
    .b(cell_handler_23_out_4[0]), .e(cell_handler_23_out_5[3]), .d(cell_handler_23_out_5[2]),
    .c(cell_handler_23_out_5[1]), .dp(cell_handler_23_out_5[0]));
  Button F_23 (.out(F_23_out));
  Cell_Handler cell_handler_23 (
    .Neighbour_Data(funny_merger_19_out_9), .CellData_Out(cell_handler_23_celldata_out),
    .out_4(cell_handler_23_out_4), .out_5(cell_handler_23_out_5), .Flagger(F_23_out), .Opener(O_23_out));
  Button O_23 (.out(O_23_out));
  _7_Segment_Display u_7_segment_display_22 (
    .g(cell_handler_19_out_4[3]), .f(cell_handler_19_out_4[2]), .a(cell_handler_19_out_4[1]),
    .b(cell_handler_19_out_4[0]), .e(cell_handler_19_out_5[3]), .d(cell_handler_19_out_5[2]),
    .c(cell_handler_19_out_5[1]), .dp(cell_handler_19_out_5[0]));
  Button F_24 (.out(F_24_out));
  _7_Segment_Display u_7_segment_display_23 (
    .g(cell_handler_24_out_4[3]), .f(cell_handler_24_out_4[2]), .a(cell_handler_24_out_4[1]),
    .b(cell_handler_24_out_4[0]), .e(cell_handler_24_out_5[3]), .d(cell_handler_24_out_5[2]),
    .c(cell_handler_24_out_5[1]), .dp(cell_handler_24_out_5[0]));
  Cell_Handler cell_handler_24 (
    .Neighbour_Data(funny_merger_21_out_9), .CellData_Out(cell_handler_24_celldata_out),
    .out_4(cell_handler_24_out_4), .out_5(cell_handler_24_out_5), .Flagger(F_24_out), .Opener(O_24_out));
  Button O_24 (.out(O_24_out));
  _7_Segment_Display u_7_segment_display_24 (
    .g(cell_handler_20_out_4[3]), .f(cell_handler_20_out_4[2]), .a(cell_handler_20_out_4[1]),
    .b(cell_handler_20_out_4[0]), .e(cell_handler_20_out_5[3]), .d(cell_handler_20_out_5[2]),
    .c(cell_handler_20_out_5[1]), .dp(cell_handler_20_out_5[0]));
  Button F_25 (.out(F_25_out));
  Funny_Merger funny_merger_25 (
    .in_1(cell_handler_33_celldata_out), .in_2(cell_handler_27_celldata_out),
    .in_3(cell_handler_23_celldata_out), .in_4(cell_handler_34_celldata_out),
    .in_5(cell_handler_19_celldata_out), .in_6(3'b000), .in_7(3'b000), .in_8(3'b000),
    .out_9(funny_merger_25_out_9));
  Button O_25 (.out(O_25_out));
  Button F_26 (.out(F_26_out));
  Funny_Merger funny_merger_26 (
    .in_1(cell_handler_35_celldata_out), .in_2(cell_handler_29_celldata_out),
    .in_3(cell_handler_24_celldata_out), .in_4(cell_handler_36_celldata_out),
    .in_5(cell_handler_20_celldata_out), .in_6(cell_handler_21_celldata_out),
    .in_7(cell_handler_25_celldata_out), .in_8(cell_handler_31_celldata_out), .out_9(funny_merger_26_out_9));
  Button O_26 (.out(O_26_out));
  Button F_27 (.out(F_27_out));
  _7_Segment_Display u_7_segment_display_25 (
    .g(cell_handler_25_out_4[3]), .f(cell_handler_25_out_4[2]), .a(cell_handler_25_out_4[1]),
    .b(cell_handler_25_out_4[0]), .e(cell_handler_25_out_5[3]), .d(cell_handler_25_out_5[2]),
    .c(cell_handler_25_out_5[1]), .dp(cell_handler_25_out_5[0]));
  Funny_Merger funny_merger_27 (
    .in_1(cell_handler_36_celldata_out), .in_2(cell_handler_30_celldata_out),
    .in_3(cell_handler_20_celldata_out), .in_4(cell_handler_31_celldata_out),
    .in_5(cell_handler_21_celldata_out), .in_6(cell_handler_22_celldata_out),
    .in_7(cell_handler_26_celldata_out), .in_8(cell_handler_32_celldata_out), .out_9(funny_merger_27_out_9));
  Cell_Handler cell_handler_25 (
    .Neighbour_Data(funny_merger_27_out_9), .CellData_Out(cell_handler_25_celldata_out),
    .out_4(cell_handler_25_out_4), .out_5(cell_handler_25_out_5), .Flagger(F_27_out), .Opener(O_27_out));
  Button O_27 (.out(O_27_out));
  Button F_28 (.out(F_28_out));
  _7_Segment_Display u_7_segment_display_26 (
    .g(cell_handler_26_out_4[3]), .f(cell_handler_26_out_4[2]), .a(cell_handler_26_out_4[1]),
    .b(cell_handler_26_out_4[0]), .e(cell_handler_26_out_5[3]), .d(cell_handler_26_out_5[2]),
    .c(cell_handler_26_out_5[1]), .dp(cell_handler_26_out_5[0]));
  Funny_Merger funny_merger_28 (
    .in_1(cell_handler_31_celldata_out), .in_2(cell_handler_25_celldata_out),
    .in_3(cell_handler_21_celldata_out), .in_4(cell_handler_32_celldata_out),
    .in_5(cell_handler_22_celldata_out), .in_6(cell_handler_23_celldata_out),
    .in_7(cell_handler_27_celldata_out), .in_8(cell_handler_33_celldata_out), .out_9(funny_merger_28_out_9));
  Cell_Handler cell_handler_26 (
    .Neighbour_Data(funny_merger_28_out_9), .CellData_Out(cell_handler_26_celldata_out),
    .out_4(cell_handler_26_out_4), .out_5(cell_handler_26_out_5), .Flagger(F_28_out), .Opener(O_28_out));
  Button O_28 (.out(O_28_out));
  _7_Segment_Display u_7_segment_display_27 (
    .g(cell_handler_27_out_4[3]), .f(cell_handler_27_out_4[2]), .a(cell_handler_27_out_4[1]),
    .b(cell_handler_27_out_4[0]), .e(cell_handler_27_out_5[3]), .d(cell_handler_27_out_5[2]),
    .c(cell_handler_27_out_5[1]), .dp(cell_handler_27_out_5[0]));
  Button F_29 (.out(F_29_out));
  Funny_Merger funny_merger_29 (
    .in_1(cell_handler_32_celldata_out), .in_2(cell_handler_26_celldata_out),
    .in_3(cell_handler_22_celldata_out), .in_4(cell_handler_33_celldata_out),
    .in_5(cell_handler_23_celldata_out), .in_6(cell_handler_19_celldata_out),
    .in_7(cell_handler_28_celldata_out), .in_8(cell_handler_34_celldata_out), .out_9(funny_merger_29_out_9));
  Cell_Handler cell_handler_27 (
    .Neighbour_Data(funny_merger_29_out_9), .CellData_Out(cell_handler_27_celldata_out),
    .out_4(cell_handler_27_out_4), .out_5(cell_handler_27_out_5), .Flagger(F_29_out), .Opener(O_29_out));
  Button O_29 (.out(O_29_out));
  _7_Segment_Display u_7_segment_display_28 (
    .g(cell_handler_28_out_4[3]), .f(cell_handler_28_out_4[2]), .a(cell_handler_28_out_4[1]),
    .b(cell_handler_28_out_4[0]), .e(cell_handler_28_out_5[3]), .d(cell_handler_28_out_5[2]),
    .c(cell_handler_28_out_5[1]), .dp(cell_handler_28_out_5[0]));
  Cell_Handler cell_handler_28 (
    .Neighbour_Data(funny_merger_25_out_9), .CellData_Out(cell_handler_28_celldata_out),
    .out_4(cell_handler_28_out_4), .out_5(cell_handler_28_out_5), .Flagger(F_25_out), .Opener(O_25_out));
  _7_Segment_Display u_7_segment_display_29 (
    .g(cell_handler_29_out_4[3]), .f(cell_handler_29_out_4[2]), .a(cell_handler_29_out_4[1]),
    .b(cell_handler_29_out_4[0]), .e(cell_handler_29_out_5[3]), .d(cell_handler_29_out_5[2]),
    .c(cell_handler_29_out_5[1]), .dp(cell_handler_29_out_5[0]));
  Button F_30 (.out(F_30_out));
  Funny_Merger funny_merger_30 (
    .in_1(3'b000), .in_2(3'b000), .in_3(3'b000), .in_4(cell_handler_35_celldata_out),
    .in_5(cell_handler_24_celldata_out), .in_6(cell_handler_20_celldata_out),
    .in_7(cell_handler_30_celldata_out), .in_8(cell_handler_36_celldata_out), .out_9(funny_merger_30_out_9));
  Cell_Handler cell_handler_29 (
    .Neighbour_Data(funny_merger_30_out_9), .CellData_Out(cell_handler_29_celldata_out),
    .out_4(cell_handler_29_out_4), .out_5(cell_handler_29_out_5), .Flagger(F_30_out), .Opener(O_30_out));
  Button O_30 (.out(O_30_out));
  _7_Segment_Display u_7_segment_display_30 (
    .g(cell_handler_30_out_4[3]), .f(cell_handler_30_out_4[2]), .a(cell_handler_30_out_4[1]),
    .b(cell_handler_30_out_4[0]), .e(cell_handler_30_out_5[3]), .d(cell_handler_30_out_5[2]),
    .c(cell_handler_30_out_5[1]), .dp(cell_handler_30_out_5[0]));
  Cell_Handler cell_handler_30 (
    .Neighbour_Data(funny_merger_26_out_9), .CellData_Out(cell_handler_30_celldata_out),
    .out_4(cell_handler_30_out_4), .out_5(cell_handler_30_out_5), .Flagger(F_26_out), .Opener(O_26_out));
  Funny_Merger funny_merger_31 (
    .in_1(3'b000), .in_2(cell_handler_33_celldata_out), .in_3(cell_handler_27_celldata_out), .in_4(3'b000),
    .in_5(cell_handler_28_celldata_out), .in_6(3'b000), .in_7(3'b000), .in_8(3'b000),
    .out_9(funny_merger_31_out_9));
  Funny_Merger funny_merger_32 (
    .in_1(3'b000), .in_2(cell_handler_35_celldata_out), .in_3(cell_handler_29_celldata_out), .in_4(3'b000),
    .in_5(cell_handler_30_celldata_out), .in_6(cell_handler_25_celldata_out),
    .in_7(cell_handler_31_celldata_out), .in_8(3'b000), .out_9(funny_merger_32_out_9));
  Button F_31 (.out(F_31_out));
  Funny_Merger funny_merger_33 (
    .in_1(3'b000), .in_2(cell_handler_36_celldata_out), .in_3(cell_handler_30_celldata_out), .in_4(3'b000),
    .in_5(cell_handler_25_celldata_out), .in_6(cell_handler_26_celldata_out),
    .in_7(cell_handler_32_celldata_out), .in_8(3'b000), .out_9(funny_merger_33_out_9));
  Cell_Handler cell_handler_31 (
    .Neighbour_Data(funny_merger_33_out_9), .CellData_Out(cell_handler_31_celldata_out),
    .out_4(cell_handler_31_out_4), .out_5(cell_handler_31_out_5), .Flagger(F_31_out), .Opener(O_31_out));
  Button O_31 (.out(O_31_out));
  _7_Segment_Display u_7_segment_display_31 (
    .g(cell_handler_32_out_4[3]), .f(cell_handler_32_out_4[2]), .a(cell_handler_32_out_4[1]),
    .b(cell_handler_32_out_4[0]), .e(cell_handler_32_out_5[3]), .d(cell_handler_32_out_5[2]),
    .c(cell_handler_32_out_5[1]), .dp(cell_handler_32_out_5[0]));
  Button F_32 (.out(F_32_out));
  Funny_Merger funny_merger_34 (
    .in_1(3'b000), .in_2(cell_handler_31_celldata_out), .in_3(cell_handler_25_celldata_out), .in_4(3'b000),
    .in_5(cell_handler_26_celldata_out), .in_6(cell_handler_27_celldata_out),
    .in_7(cell_handler_33_celldata_out), .in_8(3'b000), .out_9(funny_merger_34_out_9));
  Cell_Handler cell_handler_32 (
    .Neighbour_Data(funny_merger_34_out_9), .CellData_Out(cell_handler_32_celldata_out),
    .out_4(cell_handler_32_out_4), .out_5(cell_handler_32_out_5), .Flagger(F_32_out), .Opener(O_32_out));
  Button O_32 (.out(O_32_out));
  Button F_33 (.out(F_33_out));
  _7_Segment_Display u_7_segment_display_32 (
    .g(cell_handler_33_out_4[3]), .f(cell_handler_33_out_4[2]), .a(cell_handler_33_out_4[1]),
    .b(cell_handler_33_out_4[0]), .e(cell_handler_33_out_5[3]), .d(cell_handler_33_out_5[2]),
    .c(cell_handler_33_out_5[1]), .dp(cell_handler_33_out_5[0]));
  Funny_Merger funny_merger_35 (
    .in_1(3'b000), .in_2(cell_handler_32_celldata_out), .in_3(cell_handler_26_celldata_out), .in_4(3'b000),
    .in_5(cell_handler_27_celldata_out), .in_6(cell_handler_28_celldata_out),
    .in_7(cell_handler_34_celldata_out), .in_8(3'b000), .out_9(funny_merger_35_out_9));
  Cell_Handler cell_handler_33 (
    .Neighbour_Data(funny_merger_35_out_9), .CellData_Out(cell_handler_33_celldata_out),
    .out_4(cell_handler_33_out_4), .out_5(cell_handler_33_out_5), .Flagger(F_33_out), .Opener(O_33_out));
  Button O_33 (.out(O_33_out));
  Button F_34 (.out(F_34_out));
  _7_Segment_Display u_7_segment_display_33 (
    .g(cell_handler_34_out_4[3]), .f(cell_handler_34_out_4[2]), .a(cell_handler_34_out_4[1]),
    .b(cell_handler_34_out_4[0]), .e(cell_handler_34_out_5[3]), .d(cell_handler_34_out_5[2]),
    .c(cell_handler_34_out_5[1]), .dp(cell_handler_34_out_5[0]));
  Cell_Handler cell_handler_34 (
    .Neighbour_Data(funny_merger_31_out_9), .CellData_Out(cell_handler_34_celldata_out),
    .out_4(cell_handler_34_out_4), .out_5(cell_handler_34_out_5), .Flagger(F_34_out), .Opener(O_34_out));
  Button O_34 (.out(O_34_out));
  _7_Segment_Display u_7_segment_display_34 (
    .g(cell_handler_35_out_4[3]), .f(cell_handler_35_out_4[2]), .a(cell_handler_35_out_4[1]),
    .b(cell_handler_35_out_4[0]), .e(cell_handler_35_out_5[3]), .d(cell_handler_35_out_5[2]),
    .c(cell_handler_35_out_5[1]), .dp(cell_handler_35_out_5[0]));
  Button F_35 (.out(F_35_out));
  Funny_Merger funny_merger_36 (
    .in_1(3'b000), .in_2(3'b000), .in_3(3'b000), .in_4(3'b000), .in_5(cell_handler_29_celldata_out),
    .in_6(cell_handler_30_celldata_out), .in_7(cell_handler_36_celldata_out), .in_8(3'b000),
    .out_9(funny_merger_36_out_9));
  Cell_Handler cell_handler_35 (
    .Neighbour_Data(funny_merger_36_out_9), .CellData_Out(cell_handler_35_celldata_out),
    .out_4(cell_handler_35_out_4), .out_5(cell_handler_35_out_5), .Flagger(F_35_out), .Opener(O_35_out));
  Button O_35 (.out(O_35_out));
  Button F_36 (.out(F_36_out));
  _7_Segment_Display u_7_segment_display_35 (
    .g(cell_handler_36_out_4[3]), .f(cell_handler_36_out_4[2]), .a(cell_handler_36_out_4[1]),
    .b(cell_handler_36_out_4[0]), .e(cell_handler_36_out_5[3]), .d(cell_handler_36_out_5[2]),
    .c(cell_handler_36_out_5[1]), .dp(cell_handler_36_out_5[0]));
  Cell_Handler cell_handler_36 (
    .Neighbour_Data(funny_merger_32_out_9), .CellData_Out(cell_handler_36_celldata_out),
    .out_4(cell_handler_36_out_4), .out_5(cell_handler_36_out_5), .Flagger(F_36_out), .Opener(O_36_out));
  Button O_36 (.out(O_36_out));
  _7_Segment_Display u_7_segment_display_36 (
    .g(cell_handler_31_out_4[3]), .f(cell_handler_31_out_4[2]), .a(cell_handler_31_out_4[1]),
    .b(cell_handler_31_out_4[0]), .e(cell_handler_31_out_5[3]), .d(cell_handler_31_out_5[2]),
    .c(cell_handler_31_out_5[1]), .dp(cell_handler_31_out_5[0]));
endmodule

module input_counter (
  input  [7:0] in_1,
  output [3:0] out_2
);

  wire [2:0] adder_1_out, adder_2_out, adder_3_out, adder_4_out, adder_5_out, adder_6_out;

  Adder #(.width(3)) adder_1 (.a({2'b00, in_1[0]}), .b({2'b00, in_1[1]}), .out(adder_1_out));  // open: cin, cout
  Adder #(.width(3)) adder_2 (.a(adder_1_out), .b(adder_3_out), .out(adder_2_out));  // open: cin, cout
  Adder #(.width(3)) adder_3 (.a({2'b00, in_1[2]}), .b({2'b00, in_1[3]}), .out(adder_3_out));  // open: cin, cout
  Adder #(.width(3)) adder_4 (.a({2'b00, in_1[4]}), .b({2'b00, in_1[5]}), .out(adder_4_out));  // open: cin, cout
  Adder #(.width(3)) adder_5 (.a(adder_4_out), .b(adder_6_out), .out(adder_5_out));  // open: cin, cout
  Adder #(.width(3)) adder_6 (.a({2'b00, in_1[6]}), .b({2'b00, in_1[7]}), .out(adder_6_out));  // open: cin, cout
  // Probe on out_2
  Adder #(.width(4)) adder_7 (.a({1'b0, adder_2_out}), .b({1'b0, adder_5_out}), .out(out_2));  // open: cin, cout
endmodule

module Funny_Merger (
  input  [2:0] in_1,
  input  [2:0] in_2,
  input  [2:0] in_3,
  input  [2:0] in_4,
  input  [2:0] in_5,
  input  [2:0] in_6,
  input  [2:0] in_7,
  input  [2:0] in_8,
  output [23:0] out_9
);


  assign out_9 = {in_8, in_7, in_6, in_5, in_4, in_3, in_2, in_1};
endmodule

module Cell_Handler (
  input  [23:0] Neighbour_Data,
  input  Flagger,
  input  Opener,
  output [3:0] out_4,
  output [3:0] out_5,
  output [2:0] CellData_Out
);

  wire and_1_out, and_2_out, and_3_out, d_ff_2_q, nor_1_out, or_1_out, or_2_out, or_4_out;
  wire [1:0] t_ff_1_q;
  wire [2:0] random_1_out;
  wire [3:0] input_counter_1_out_2;
  wire [7:0] funny_splitter_1_out_2, funny_splitter_1_out_3, funny_splitter_1_out_4, multiplexer_1_out,
       number_decoder_1_out_2;

  or or_1 (or_1_out, funny_splitter_1_out_3[0], funny_splitter_1_out_3[1], funny_splitter_1_out_3[2], funny_splitter_1_out_3[3], funny_splitter_1_out_3[4], funny_splitter_1_out_3[5], funny_splitter_1_out_3[6], funny_splitter_1_out_3[7]);
  Random #(.width(3)) random_1 (.out(random_1_out));  // open: clk, next, clr
  Funny_Splitter funny_splitter_1 (
    .out_3(funny_splitter_1_out_3), .out_2(funny_splitter_1_out_2), .out_4(funny_splitter_1_out_4),
    .in_1(Neighbour_Data));
  D_Flip_Flop d_ff_1 (.clk(and_2_out), .D(and_2_out), .Q(CellData_Out[2]));  // open: Qn, preset, en, reset
  and and_1 (and_1_out, random_1_out[0], random_1_out[1], random_1_out[2]);
  input_counter input_counter_1 (.in_1(funny_splitter_1_out_2), .out_2(input_counter_1_out_2));
  nor nor_1 (nor_1_out, input_counter_1_out_2[0], input_counter_1_out_2[1], input_counter_1_out_2[2], input_counter_1_out_2[3]);
  and and_2 (and_2_out, nor_1_out, t_ff_1_q[1]);
  D_Flip_Flop d_ff_2 (.clk(or_2_out), .D(or_2_out), .Q(d_ff_2_q));  // open: Qn, preset, en, reset
  or or_2 (or_2_out, funny_splitter_1_out_4[0], funny_splitter_1_out_4[1], funny_splitter_1_out_4[2], funny_splitter_1_out_4[3], funny_splitter_1_out_4[4], funny_splitter_1_out_4[5], funny_splitter_1_out_4[6], funny_splitter_1_out_4[7]);
  and and_3 (and_3_out, t_ff_1_q[1], CellData_Out[0]);
  D_Flip_Flop is_mine (.Q(CellData_Out[0]), .preset(and_1_out));  // open: clk, D, Qn, en, reset
  or or_3 (CellData_Out[1], d_ff_2_q, and_3_out);
  or or_4 (or_4_out, d_ff_2_q, or_1_out, Opener);
  number_decoder number_decoder_1 (.out_2(number_decoder_1_out_2), .in_1(input_counter_1_out_2));
  Multiplexer #(.width(8), .enable("false")) multiplexer_1 (
    .in0(number_decoder_1_out_2), .in1(8'he8), .out(multiplexer_1_out), .sel(CellData_Out[0]));
  D_Flip_Flop Is_Open (.Q(t_ff_1_q[1]), .preset(or_4_out));  // open: clk, D, Qn, en, reset
  Multiplexer #(.select(2), .width(8), .enable("false")) multiplexer_2 (
    .in0({8{1'b0}}), .in1(8'h8e), .in2(multiplexer_1_out), .in3(multiplexer_1_out), .out({out_5, out_4}),
    .sel(t_ff_1_q));
  T_Flip_Flop t_ff_1 (.clk(Flagger), .T(Flagger), .Q(t_ff_1_q[0]));  // open: Qn, preset, reset, en
  _7_Segment_Display u_7_segment_display_1 (
    .g(out_4[3]), .f(out_4[2]), .a(out_4[1]), .b(out_4[0]), .e(out_5[3]), .d(out_5[2]), .c(out_5[1]),
    .dp(out_5[0]));
endmodule

module number_decoder (
  input  [3:0] in_1,
  output [7:0] out_2
);

  Multiplexer #(.select(4), .width(8), .enable("false")) multiplexer_1 (
    .in0(8'he7), .in1(8'h21), .in2(8'hcb), .in3(8'h6b), .in4(8'h2d), .in5(8'h6e), .in6(8'hee), .in7(8'h23),
    .in8(8'hef), .out(out_2), .sel(in_1));  // open: in9, in10, in11, in12, in13, in14, in15
endmodule

module One_Cell (
);

  wire F_out, O_out;
  wire [2:0] cell_handler_1_celldata_out, undriven, undriven_2, undriven_3, undriven_4, undriven_5,
       undriven_6, undriven_7, undriven_8;
  wire [3:0] cell_handler_1_out_4, cell_handler_1_out_5;
  wire [23:0] funny_merger_1_out_9;

  Funny_Merger funny_merger_1 (
    .in_1(undriven_7), .in_2(undriven_5), .in_3(undriven_3), .in_4(undriven), .in_5(undriven_2),
    .in_6(undriven_4), .in_7(undriven_6), .in_8(undriven_8), .out_9(funny_merger_1_out_9));
  Button F (.out(F_out));
  _7_Segment_Display u_7_segment_display_1 (
    .g(cell_handler_1_out_4[3]), .f(cell_handler_1_out_4[2]), .a(cell_handler_1_out_4[1]),
    .b(cell_handler_1_out_4[0]), .e(cell_handler_1_out_5[3]), .d(cell_handler_1_out_5[2]),
    .c(cell_handler_1_out_5[1]), .dp(cell_handler_1_out_5[0]));
  Cell_Handler cell_handler_1 (
    .Neighbour_Data(funny_merger_1_out_9), .CellData_Out(cell_handler_1_celldata_out),
    .out_4(cell_handler_1_out_4), .out_5(cell_handler_1_out_5), .Flagger(F_out), .Opener(O_out));
  Button O (.out(O_out));
endmodule

module Funny_Splitter (
  input  [23:0] in_1,
  output [7:0] out_2,
  output [7:0] out_3,
  output [7:0] out_4
);


  assign out_2 = {in_1[21], in_1[18], in_1[15], in_1[12], in_1[9], in_1[6], in_1[3], in_1[0]};
  assign out_3 = {in_1[2], in_1[5], in_1[8], in_1[11], in_1[14], in_1[17], in_1[20], in_1[23]};
  assign out_4 = {in_1[22], in_1[19], in_1[16], in_1[13], in_1[10], in_1[7], in_1[4], in_1[1]};
endmodule
