// Logisim project CBRLAB3.circ as structural Verilog: 1 circuit, main circuit main
module main (
  input  in_1,
  input  in_2,
  input  in_3,
  input  in_4,
  input  in_5,
  input  in_6,
  input  in_7,
  input  in_8,
  input  in_9,
  input  in_10,
  input  in_11,
  input  in_12,
  input  in_13,
  output out_14,
  output out_15,
  output out_16,
  output out_17,
  output out_18,
  output out_19,
  output out_20
);

  wire transistor_3_out, transistor_10_out, transistor_12_out, transistor_17_out;

  Transistor #(.\type ("n")) transistor_1 (.in(in_4), .out(out_14), .gate(in_1));
  Transistor transistor_2 (.in(in_9), .out(out_18), .gate(in_8));
  Transistor #(.\type ("n")) transistor_3 (.in(1'b1), .out(transistor_3_out), .gate(in_2));
  Transistor #(.\type ("n")) transistor_4 (.in(transistor_3_out), .out(out_16), .gate(in_6));
  Transistor transistor_5 (.in(1'b0), .out(out_16), .gate(in_6));
  Transistor transistor_6 (.in(1'b1), .out(out_19), .gate(in_10));
  Transistor transistor_7 (.in(1'b1), .out(out_19), .gate(in_12));
  Transistor transistor_8 (.in(1'b0), .out(out_16), .gate(in_2));
  Transistor #(.\type ("n")) transistor_9 (.in(transistor_10_out), .out(out_19), .gate(in_12));
  Transistor #(.\type ("n")) transistor_10 (.in(1'b0), .out(transistor_10_out), .gate(in_10));
  Transistor #(.\type ("n")) transistor_11 (.in(1'b1), .out(out_17), .gate(in_3));
  Transistor transistor_12 (.in(1'b1), .out(transistor_12_out), .gate(in_11));
  Transistor transistor_13 (.in(transistor_12_out), .out(out_20), .gate(in_13));
  Transistor #(.\type ("n")) transistor_14 (.in(1'b0), .out(out_20), .gate(in_13));
  Transistor #(.\type ("n")) transistor_15 (.in(1'b1), .out(out_17), .gate(in_7));
  Transistor transistor_16 (.in(transistor_17_out), .out(out_17), .gate(in_7));
  Transistor transistor_17 (.in(1'b0), .out(transistor_17_out), .gate(in_3));
  Transistor #(.\type ("n")) transistor_18 (.in(1'b0), .out(out_20), .gate(in_11));
  Transistor transistor_19 (.in(1'b1), .out(out_15), .gate(in_5));
  Transistor #(.\type ("n")) transistor_20 (.in(1'b0), .out(out_15), .gate(in_5));

  // Notes on the sheet:
  //   AND
  //   NAND
  //   OR
  //   NOR
  //   NOT
endmodule
