// Logisim project CBRLAB6pt2.circ as structural Verilog: 10 circuits, main circuit main
module main (
  input  in_1,
  input  in_2,
  input  in_3,
  input  in_4,
  input  [7:0] in_5,
  input  in_6,
  input  in_7,
  input  [7:0] in_8,
  input  in_9,
  input  [7:0] in_10,
  input  [2:0] in_11,
  input  [9:0] in_12,
  input  in_13,
  input  [2:0] in_14,
  input  [9:0] in_15,
  input  in_16,
  input  in_17,
  input  in_18,
  input  in_19,
  input  in_20,
  input  in_21,
  input  [7:0] in_22,
  input  in_23,
  input  in_24,
  output [7:0] out_25,
  output [7:0] out_26,
  output [7:0] out_27,
  output out_28,
  output [7:0] out_29,
  output out_30,
  output [7:0] out_31
);

  wire clock_1_out, multiplexer_1_out;

  Clock clock_1 (.out(clock_1_out));
  Multiplexer multiplexer_1 (.in0(clock_1_out), .in1(in_20), .out(multiplexer_1_out), .sel(in_21));  // open: en
  // Probe on out_25
  Better_Counter better_counter_1 (
    .Up_Down(in_1), .Clock(multiplexer_1_out), .Toggle(in_2), .Clear(in_3), .Write(in_4), .Output(out_25),
    .Input(in_5));
  // Probe on in_5
  Register register_1 (.in_1(in_24), .in_2(in_23), .in_3(multiplexer_1_out), .in_4(in_22), .out_5(out_31));
  // Probe on out_26
  // Probe on out_26
  // Probe on in_10
  // Probe on out_29
  Memorizing_Add_Tractor memorizing_add_tractor_1 (
    .in_1(in_7), .in_2(in_10), .out_6(out_29), .out_8(out_30), .in_3(in_16), .in_4(multiplexer_1_out),
    .in_5(in_17), .out_7(out_26));
  _8x1RAM u_8x1ram_1 (
    .in_3(in_9), .out_7(out_28), .in_1(multiplexer_1_out), .in_2(in_19), .in_6(in_11), .in_5(in_14),
    .in_4(in_6));
  _1024x8RAM u_1024x8ram_1 (
    .in_1(in_8), .out_7(out_27), .in_4(in_13), .in_2(in_18), .in_3(multiplexer_1_out), .in_6(in_12),
    .in_5(in_15));
endmodule

module Better_Counter (
  input  Up_Down,
  input  Clock,
  input  Toggle,
  input  Clear,
  input  Write,
  input  [7:0] Input,
  output [7:0] Output
);

  wire and_1_out, and_2_out, and_3_out, and_4_out, and_5_out, and_6_out, and_7_out, and_8_out, and_9_out,
       and_10_out, and_11_out, and_12_out, and_13_out, and_14_out, demultiplexer_1_out0,
       demultiplexer_1_out1, demultiplexer_2_out0, demultiplexer_2_out1, demultiplexer_3_out0,
       demultiplexer_3_out1, demultiplexer_4_out0, demultiplexer_4_out1, demultiplexer_5_out0,
       demultiplexer_5_out1, demultiplexer_6_out0, demultiplexer_6_out1, demultiplexer_7_out0,
       demultiplexer_7_out1, demultiplexer_8_out0, demultiplexer_8_out1, or_1_out, or_2_out, or_3_out,
       or_4_out, or_5_out, or_6_out, or_7_out, or_8_out, or_9_out, or_10_out, or_11_out, or_12_out,
       or_13_out, or_14_out, or_15_out, t_ff_1_qn, t_ff_2_qn, t_ff_3_qn, t_ff_4_qn, t_ff_5_qn, t_ff_6_qn,
       t_ff_7_qn;
  wire [7:0] not_1_out;

  // Probe on Output
  T_Flip_Flop t_ff_1 (
    .clk(Clock), .T(1'b1), .Q(Output[0]), .Qn(t_ff_1_qn), .preset(demultiplexer_1_out0), .reset(or_1_out),
    .en(Toggle));
  or or_1 (or_1_out, Clear, demultiplexer_1_out1);
  Demultiplexer demultiplexer_1 (
    .out0(demultiplexer_1_out0), .out1(demultiplexer_1_out1), .in(Write), .sel(not_1_out[0]));  // open: en
  and and_1 (and_1_out, Up_Down, Output[0]);
  and and_2 (and_2_out, t_ff_1_qn, ~Up_Down);  // AND_Gate
  assign not_1_out = ~Input;  // NOT_Gate not_1, 8 bits wide
  T_Flip_Flop t_ff_2 (
    .clk(Clock), .T(or_2_out), .Q(Output[1]), .Qn(t_ff_2_qn), .preset(demultiplexer_2_out0),
    .reset(or_3_out), .en(Toggle));
  or or_2 (or_2_out, and_1_out, and_2_out);
  or or_3 (or_3_out, Clear, demultiplexer_2_out1);
  Demultiplexer demultiplexer_2 (
    .out0(demultiplexer_2_out0), .out1(demultiplexer_2_out1), .in(Write), .sel(not_1_out[1]));  // open: en
  and and_3 (and_3_out, and_1_out, Output[1]);
  and and_4 (and_4_out, t_ff_2_qn, and_2_out);
  T_Flip_Flop t_ff_3 (
    .clk(Clock), .T(or_4_out), .Q(Output[2]), .Qn(t_ff_3_qn), .preset(demultiplexer_3_out0),
    .reset(or_5_out), .en(Toggle));
  or or_4 (or_4_out, and_3_out, and_4_out);
  or or_5 (or_5_out, Clear, demultiplexer_3_out1);
  Demultiplexer demultiplexer_3 (
    .out0(demultiplexer_3_out0), .out1(demultiplexer_3_out1), .in(Write), .sel(not_1_out[2]));  // open: en
  and and_5 (and_5_out, and_3_out, Output[2]);
  and and_6 (and_6_out, t_ff_3_qn, and_4_out);
  T_Flip_Flop t_ff_4 (
    .clk(Clock), .T(or_6_out), .Q(Output[3]), .Qn(t_ff_4_qn), .preset(demultiplexer_4_out0),
    .reset(or_7_out), .en(Toggle));
  or or_6 (or_6_out, and_5_out, and_6_out);
  or or_7 (or_7_out, Clear, demultiplexer_4_out1);
  Demultiplexer demultiplexer_4 (
    .out0(demultiplexer_4_out0), .out1(demultiplexer_4_out1), .in(Write), .sel(not_1_out[3]));  // open: en
  and and_7 (and_7_out, and_5_out, Output[3]);
  and and_8 (and_8_out, t_ff_4_qn, and_6_out);
  T_Flip_Flop t_ff_5 (
    .clk(Clock), .T(or_8_out), .Q(Output[4]), .Qn(t_ff_5_qn), .preset(demultiplexer_5_out0),
    .reset(or_9_out), .en(Toggle));
  or or_8 (or_8_out, and_7_out, and_8_out);
  or or_9 (or_9_out, Clear, demultiplexer_5_out1);
  Demultiplexer demultiplexer_5 (
    .out0(demultiplexer_5_out0), .out1(demultiplexer_5_out1), .in(Write), .sel(not_1_out[4]));  // open: en
  and and_9 (and_9_out, and_7_out, Output[4]);
  and and_10 (and_10_out, t_ff_5_qn, and_8_out);
  T_Flip_Flop t_ff_6 (
    .clk(Clock), .T(or_10_out), .Q(Output[5]), .Qn(t_ff_6_qn), .preset(demultiplexer_6_out0),
    .reset(or_11_out), .en(Toggle));
  or or_10 (or_10_out, and_9_out, and_10_out);
  or or_11 (or_11_out, Clear, demultiplexer_6_out1);
  Demultiplexer demultiplexer_6 (
    .out0(demultiplexer_6_out0), .out1(demultiplexer_6_out1), .in(Write), .sel(not_1_out[5]));  // open: en
  and and_11 (and_11_out, and_9_out, Output[5]);
  and and_12 (and_12_out, t_ff_6_qn, and_10_out);
  T_Flip_Flop t_ff_7 (
    .clk(Clock), .T(or_12_out), .Q(Output[6]), .Qn(t_ff_7_qn), .preset(demultiplexer_7_out0),
    .reset(or_13_out), .en(Toggle));
  or or_12 (or_12_out, and_11_out, and_12_out);
  or or_13 (or_13_out, Clear, demultiplexer_7_out1);
  Demultiplexer demultiplexer_7 (
    .out0(demultiplexer_7_out0), .out1(demultiplexer_7_out1), .in(Write), .sel(not_1_out[6]));  // open: en
  and and_13 (and_13_out, and_11_out, Output[6]);
  and and_14 (and_14_out, t_ff_7_qn, and_12_out);
  T_Flip_Flop t_ff_8 (
    .clk(Clock), .T(or_14_out), .Q(Output[7]), .preset(demultiplexer_8_out0), .reset(or_15_out), .en(Toggle));  // open: Qn
  or or_14 (or_14_out, and_13_out, and_14_out);
  or or_15 (or_15_out, Clear, demultiplexer_8_out1);
  Demultiplexer demultiplexer_8 (
    .out0(demultiplexer_8_out0), .out1(demultiplexer_8_out1), .in(Write), .sel(not_1_out[7]));  // open: en
endmodule

module Register (
  input  in_1,
  input  in_2,
  input  in_3,
  input  [7:0] in_4,
  output [7:0] out_5
);

  D_Flip_Flop d_ff_1 (.clk(in_3), .D(in_4[0]), .Q(out_5[0]), .en(in_2), .reset(in_1));  // open: Qn, preset
  D_Flip_Flop d_ff_2 (.clk(in_3), .D(in_4[1]), .Q(out_5[1]), .en(in_2), .reset(in_1));  // open: Qn, preset
  D_Flip_Flop d_ff_3 (.clk(in_3), .D(in_4[2]), .Q(out_5[2]), .en(in_2), .reset(in_1));  // open: Qn, preset
  D_Flip_Flop d_ff_4 (.clk(in_3), .D(in_4[3]), .Q(out_5[3]), .en(in_2), .reset(in_1));  // open: Qn, preset
  D_Flip_Flop d_ff_5 (.clk(in_3), .D(in_4[4]), .Q(out_5[4]), .en(in_2), .reset(in_1));  // open: Qn, preset
  D_Flip_Flop d_ff_6 (.clk(in_3), .D(in_4[5]), .Q(out_5[5]), .en(in_2), .reset(in_1));  // open: Qn, preset
  D_Flip_Flop d_ff_7 (.clk(in_3), .D(in_4[6]), .Q(out_5[6]), .en(in_2), .reset(in_1));  // open: Qn, preset
  D_Flip_Flop d_ff_8 (.clk(in_3), .D(in_4[7]), .Q(out_5[7]), .en(in_2), .reset(in_1));  // open: Qn, preset
endmodule

module Rising_Edge_Detector (
  input  in_1,
  output out_2
);

  wire not_1_out, not_2_out, not_3_out;

  not not_1 (not_1_out, not_3_out);
  not not_2 (not_2_out, in_1);
  not not_3 (not_3_out, not_2_out);
  and and_1 (out_2, not_1_out, in_1);
endmodule

module Memorizing_Adder (
  input  in_1,
  input  [7:0] in_2,
  input  in_3,
  input  in_4,
  input  in_5,
  output [7:0] out_6,
  output out_7
);

  wire [7:0] adder_1_out;

  // Probe on in_2
  Register_part register_1 (.D(adder_1_out), .en(in_3), .Q(out_6), .clk(in_4), .clr(in_5));
  Adder adder_1 (.a(out_6), .b(in_2), .out(adder_1_out), .cin(in_1), .cout(out_7));
  // Probe on out_6
endmodule

module Memorizing_Add_Tractor (
  input  in_1,
  input  [7:0] in_2,
  input  in_3,
  input  in_4,
  input  in_5,
  output [7:0] out_6,
  output [7:0] out_7,
  output out_8
);

  wire adder_1_cout;
  wire [7:0] xor_1_out;

  assign xor_1_out = {8{in_1}} ^ in_2;  // XOR_Gate xor_1, 8 bits wide
  Adder adder_1 (.a(out_7), .b(xor_1_out), .out(out_6), .cin(in_1), .cout(adder_1_cout));
  // Probe on xor_1_out
  xor xor_2 (out_8, in_1, adder_1_cout);
  // Probe on out_6
  // Probe on out_7
  Register_part register_1 (.D(out_6), .en(in_3), .Q(out_7), .clk(in_4), .clr(in_5));
endmodule

module _8x1RAM (
  input  in_1,
  input  in_2,
  input  in_3,
  input  in_4,
  input  [2:0] in_5,
  input  [2:0] in_6,
  output out_7
);

  wire d_ff_1_q, d_ff_2_q, d_ff_3_q, d_ff_4_q, d_ff_5_q, d_ff_6_q, d_ff_7_q, d_ff_8_q;
  wire [1:0] demultiplexer_1_out0, demultiplexer_1_out1, demultiplexer_1_out2, demultiplexer_1_out3,
       demultiplexer_1_out4, demultiplexer_1_out5, demultiplexer_1_out6, demultiplexer_1_out7;

  Demultiplexer #(.select(3), .width(2)) demultiplexer_1 (
    .out0(demultiplexer_1_out0), .out1(demultiplexer_1_out1), .out2(demultiplexer_1_out2),
    .out3(demultiplexer_1_out3), .out4(demultiplexer_1_out4), .out5(demultiplexer_1_out5),
    .out6(demultiplexer_1_out6), .out7(demultiplexer_1_out7), .in({in_4, in_3}), .sel(in_6));  // open: en
  D_Flip_Flop d_ff_1 (
    .clk(in_1), .D(demultiplexer_1_out0[0]), .Q(d_ff_1_q), .en(demultiplexer_1_out0[1]), .reset(in_2));  // open: Qn, preset
  D_Flip_Flop d_ff_2 (
    .clk(in_1), .D(demultiplexer_1_out1[0]), .Q(d_ff_2_q), .en(demultiplexer_1_out1[1]), .reset(in_2));  // open: Qn, preset
  D_Flip_Flop d_ff_3 (
    .clk(in_1), .D(demultiplexer_1_out2[0]), .Q(d_ff_3_q), .en(demultiplexer_1_out2[1]), .reset(in_2));  // open: Qn, preset
  D_Flip_Flop d_ff_4 (
    .clk(in_1), .D(demultiplexer_1_out3[0]), .Q(d_ff_4_q), .en(demultiplexer_1_out3[1]), .reset(in_2));  // open: Qn, preset
  D_Flip_Flop d_ff_5 (
    .clk(in_1), .D(demultiplexer_1_out4[0]), .Q(d_ff_5_q), .en(demultiplexer_1_out4[1]), .reset(in_2));  // open: Qn, preset
  D_Flip_Flop d_ff_6 (
    .clk(in_1), .D(demultiplexer_1_out5[0]), .Q(d_ff_6_q), .en(demultiplexer_1_out5[1]), .reset(in_2));  // open: Qn, preset
  D_Flip_Flop d_ff_7 (
    .clk(in_1), .D(demultiplexer_1_out6[0]), .Q(d_ff_7_q), .en(demultiplexer_1_out6[1]), .reset(in_2));  // open: Qn, preset
  D_Flip_Flop d_ff_8 (
    .clk(in_1), .D(demultiplexer_1_out7[0]), .Q(d_ff_8_q), .en(demultiplexer_1_out7[1]), .reset(in_2));  // open: Qn, preset
  Multiplexer #(.select(3)) multiplexer_1 (
    .in0(d_ff_1_q), .in1(d_ff_2_q), .in2(d_ff_3_q), .in3(d_ff_4_q), .in4(d_ff_5_q), .in5(d_ff_6_q),
    .in6(d_ff_7_q), .in7(d_ff_8_q), .out(out_7), .sel(in_5));  // open: en
endmodule

module _16x8RAM (
  input  in_1,
  input  in_2,
  input  [7:0] in_3,
  input  in_4,
  input  [3:0] in_5,
  input  [3:0] in_6,
  output [7:0] out_7
);

  wire [7:0] register_1_q, register_2_q, register_3_q, register_4_q, register_5_q, register_6_q,
       register_7_q, register_8_q, register_9_q, register_10_q, register_11_q, register_12_q, register_13_q,
       register_14_q, register_15_q, register_16_q;
  wire [8:0] demultiplexer_1_out0, demultiplexer_1_out1, demultiplexer_1_out2, demultiplexer_1_out3,
       demultiplexer_1_out4, demultiplexer_1_out5, demultiplexer_1_out6, demultiplexer_1_out7,
       demultiplexer_1_out8, demultiplexer_1_out9, demultiplexer_1_out10, demultiplexer_1_out11,
       demultiplexer_1_out12, demultiplexer_1_out13, demultiplexer_1_out14, demultiplexer_1_out15;

  Demultiplexer #(.select(4), .width(9)) demultiplexer_1 (
    .out0(demultiplexer_1_out0), .out1(demultiplexer_1_out1), .out2(demultiplexer_1_out2),
    .out3(demultiplexer_1_out3), .out4(demultiplexer_1_out4), .out5(demultiplexer_1_out5),
    .out6(demultiplexer_1_out6), .out7(demultiplexer_1_out7), .out8(demultiplexer_1_out8),
    .out9(demultiplexer_1_out9), .out10(demultiplexer_1_out10), .out11(demultiplexer_1_out11),
    .out12(demultiplexer_1_out12), .out13(demultiplexer_1_out13), .out14(demultiplexer_1_out14),
    .out15(demultiplexer_1_out15), .in({in_4, in_3}), .sel(in_6));  // open: en
  Register_part register_1 (
    .D(demultiplexer_1_out0[7:0]), .en(demultiplexer_1_out0[8]), .Q(register_1_q), .clk(in_2), .clr(in_1));
  Register_part register_2 (
    .D(demultiplexer_1_out1[7:0]), .en(demultiplexer_1_out1[8]), .Q(register_2_q), .clk(in_2), .clr(in_1));
  Register_part register_3 (
    .D(demultiplexer_1_out2[7:0]), .en(demultiplexer_1_out2[8]), .Q(register_3_q), .clk(in_2), .clr(in_1));
  Register_part register_4 (
    .D(demultiplexer_1_out3[7:0]), .en(demultiplexer_1_out3[8]), .Q(register_4_q), .clk(in_2), .clr(in_1));
  Register_part register_5 (
    .D(demultiplexer_1_out4[7:0]), .en(demultiplexer_1_out4[8]), .Q(register_5_q), .clk(in_2), .clr(in_1));
  Register_part register_6 (
    .D(demultiplexer_1_out5[7:0]), .en(demultiplexer_1_out5[8]), .Q(register_6_q), .clk(in_2), .clr(in_1));
  Register_part register_7 (
    .D(demultiplexer_1_out6[7:0]), .en(demultiplexer_1_out6[8]), .Q(register_7_q), .clk(in_2), .clr(in_1));
  Register_part register_8 (
    .D(demultiplexer_1_out7[7:0]), .en(demultiplexer_1_out7[8]), .Q(register_8_q), .clk(in_2), .clr(in_1));
  Register_part register_9 (
    .D(demultiplexer_1_out8[7:0]), .en(demultiplexer_1_out8[8]), .Q(register_9_q), .clk(in_2), .clr(in_1));
  Register_part register_10 (
    .D(demultiplexer_1_out9[7:0]), .en(demultiplexer_1_out9[8]), .Q(register_10_q), .clk(in_2), .clr(in_1));
  Register_part register_11 (
    .D(demultiplexer_1_out10[7:0]), .en(demultiplexer_1_out10[8]), .Q(register_11_q), .clk(in_2), .clr(in_1));
  Register_part register_12 (
    .D(demultiplexer_1_out11[7:0]), .en(demultiplexer_1_out11[8]), .Q(register_12_q), .clk(in_2), .clr(in_1));
  Register_part register_13 (
    .D(demultiplexer_1_out12[7:0]), .en(demultiplexer_1_out12[8]), .Q(register_13_q), .clk(in_2), .clr(in_1));
  Register_part register_14 (
    .D(demultiplexer_1_out13[7:0]), .en(demultiplexer_1_out13[8]), .Q(register_14_q), .clk(in_2), .clr(in_1));
  Register_part register_15 (
    .D(demultiplexer_1_out14[7:0]), .en(demultiplexer_1_out14[8]), .Q(register_15_q), .clk(in_2), .clr(in_1));
  Register_part register_16 (
    .D(demultiplexer_1_out15[7:0]), .en(demultiplexer_1_out15[8]), .Q(register_16_q), .clk(in_2), .clr(in_1));
  Multiplexer #(.select(4), .width(8)) multiplexer_1 (
    .in0(register_1_q), .in1(register_2_q), .in2(register_3_q), .in3(register_4_q), .in4(register_5_q),
    .in5(register_6_q), .in6(register_7_q), .in7(register_8_q), .in8(register_9_q), .in9(register_10_q),
    .in10(register_11_q), .in11(register_12_q), .in12(register_13_q), .in13(register_14_q),
    .in14(register_15_q), .in15(register_16_q), .out(out_7), .sel(in_5));  // open: en
endmodule

module _256x8RAM (
  input  in_1,
  input  in_2,
  input  [7:0] in_3,
  input  in_4,
  input  [7:0] in_5,
  input  [7:0] in_6,
  output [7:0] out_7
);

  wire [7:0] n16x8ram_1_out_7, n16x8ram_2_out_7, n16x8ram_3_out_7, n16x8ram_4_out_7, n16x8ram_5_out_7,
       n16x8ram_6_out_7, n16x8ram_7_out_7, n16x8ram_8_out_7, n16x8ram_9_out_7, n16x8ram_10_out_7,
       n16x8ram_11_out_7, n16x8ram_12_out_7, n16x8ram_13_out_7, n16x8ram_14_out_7, n16x8ram_15_out_7,
       n16x8ram_16_out_7;
  wire [8:0] demultiplexer_1_out0, demultiplexer_1_out1, demultiplexer_1_out2, demultiplexer_1_out3,
       demultiplexer_1_out4, demultiplexer_1_out5, demultiplexer_1_out6, demultiplexer_1_out7,
       demultiplexer_1_out8, demultiplexer_1_out9, demultiplexer_1_out10, demultiplexer_1_out11,
       demultiplexer_1_out12, demultiplexer_1_out13, demultiplexer_1_out14, demultiplexer_1_out15;

  Demultiplexer #(.select(4), .width(9)) demultiplexer_1 (
    .out0(demultiplexer_1_out0), .out1(demultiplexer_1_out1), .out2(demultiplexer_1_out2),
    .out3(demultiplexer_1_out3), .out4(demultiplexer_1_out4), .out5(demultiplexer_1_out5),
    .out6(demultiplexer_1_out6), .out7(demultiplexer_1_out7), .out8(demultiplexer_1_out8),
    .out9(demultiplexer_1_out9), .out10(demultiplexer_1_out10), .out11(demultiplexer_1_out11),
    .out12(demultiplexer_1_out12), .out13(demultiplexer_1_out13), .out14(demultiplexer_1_out14),
    .out15(demultiplexer_1_out15), .in({in_4, in_3}), .sel(in_6[7:4]));  // open: en
  _16x8RAM u_16x8ram_1 (
    .in_3(demultiplexer_1_out0[7:0]), .out_7(n16x8ram_1_out_7), .in_4(demultiplexer_1_out0[8]), .in_1(in_1),
    .in_2(in_2), .in_6(in_6[3:0]), .in_5(in_5[3:0]));
  _16x8RAM u_16x8ram_2 (
    .in_3(demultiplexer_1_out1[7:0]), .out_7(n16x8ram_2_out_7), .in_4(demultiplexer_1_out1[8]), .in_1(in_1),
    .in_2(in_2), .in_6(in_6[3:0]), .in_5(in_5[3:0]));
  _16x8RAM u_16x8ram_3 (
    .in_3(demultiplexer_1_out2[7:0]), .out_7(n16x8ram_3_out_7), .in_4(demultiplexer_1_out2[8]), .in_1(in_1),
    .in_2(in_2), .in_6(in_6[3:0]), .in_5(in_5[3:0]));
  _16x8RAM u_16x8ram_4 (
    .in_3(demultiplexer_1_out3[7:0]), .out_7(n16x8ram_4_out_7), .in_4(demultiplexer_1_out3[8]), .in_1(in_1),
    .in_2(in_2), .in_6(in_6[3:0]), .in_5(in_5[3:0]));
  _16x8RAM u_16x8ram_5 (
    .in_3(demultiplexer_1_out4[7:0]), .out_7(n16x8ram_5_out_7), .in_4(demultiplexer_1_out4[8]), .in_1(in_1),
    .in_2(in_2), .in_6(in_6[3:0]), .in_5(in_5[3:0]));
  _16x8RAM u_16x8ram_6 (
    .in_3(demultiplexer_1_out5[7:0]), .out_7(n16x8ram_6_out_7), .in_4(demultiplexer_1_out5[8]), .in_1(in_1),
    .in_2(in_2), .in_6(in_6[3:0]), .in_5(in_5[3:0]));
  _16x8RAM u_16x8ram_7 (
    .in_3(demultiplexer_1_out6[7:0]), .out_7(n16x8ram_7_out_7), .in_4(demultiplexer_1_out6[8]), .in_1(in_1),
    .in_2(in_2), .in_6(in_6[3:0]), .in_5(in_5[3:0]));
  _16x8RAM u_16x8ram_8 (
    .in_3(demultiplexer_1_out7[7:0]), .out_7(n16x8ram_8_out_7), .in_4(demultiplexer_1_out7[8]), .in_1(in_1),
    .in_2(in_2), .in_6(in_6[3:0]), .in_5(in_5[3:0]));
  _16x8RAM u_16x8ram_9 (
    .in_3(demultiplexer_1_out8[7:0]), .out_7(n16x8ram_9_out_7), .in_4(demultiplexer_1_out8[8]), .in_1(in_1),
    .in_2(in_2), .in_6(in_6[3:0]), .in_5(in_5[3:0]));
  _16x8RAM u_16x8ram_10 (
    .in_3(demultiplexer_1_out9[7:0]), .out_7(n16x8ram_10_out_7), .in_4(demultiplexer_1_out9[8]), .in_1(in_1),
    .in_2(in_2), .in_6(in_6[3:0]), .in_5(in_5[3:0]));
  _16x8RAM u_16x8ram_11 (
    .in_3(demultiplexer_1_out10[7:0]), .out_7(n16x8ram_11_out_7), .in_4(demultiplexer_1_out10[8]),
    .in_1(in_1), .in_2(in_2), .in_6(in_6[3:0]), .in_5(in_5[3:0]));
  _16x8RAM u_16x8ram_12 (
    .in_3(demultiplexer_1_out11[7:0]), .out_7(n16x8ram_12_out_7), .in_4(demultiplexer_1_out11[8]),
    .in_1(in_1), .in_2(in_2), .in_6(in_6[3:0]), .in_5(in_5[3:0]));
  _16x8RAM u_16x8ram_13 (
    .in_3(demultiplexer_1_out12[7:0]), .out_7(n16x8ram_13_out_7), .in_4(demultiplexer_1_out12[8]),
    .in_1(in_1), .in_2(in_2), .in_6(in_6[3:0]), .in_5(in_5[3:0]));
  _16x8RAM u_16x8ram_14 (
    .in_3(demultiplexer_1_out13[7:0]), .out_7(n16x8ram_14_out_7), .in_4(demultiplexer_1_out13[8]),
    .in_1(in_1), .in_2(in_2), .in_6(in_6[3:0]), .in_5(in_5[3:0]));
  _16x8RAM u_16x8ram_15 (
    .in_3(demultiplexer_1_out14[7:0]), .out_7(n16x8ram_15_out_7), .in_4(demultiplexer_1_out14[8]),
    .in_1(in_1), .in_2(in_2), .in_6(in_6[3:0]), .in_5(in_5[3:0]));
  _16x8RAM u_16x8ram_16 (
    .in_3(demultiplexer_1_out15[7:0]), .out_7(n16x8ram_16_out_7), .in_4(demultiplexer_1_out15[8]),
    .in_1(in_1), .in_2(in_2), .in_6(in_6[3:0]), .in_5(in_5[3:0]));
  Multiplexer #(.select(4), .width(8)) multiplexer_1 (
    .in0(n16x8ram_1_out_7), .in1(n16x8ram_2_out_7), .in2(n16x8ram_3_out_7), .in3(n16x8ram_4_out_7),
    .in4(n16x8ram_5_out_7), .in5(n16x8ram_6_out_7), .in6(n16x8ram_7_out_7), .in7(n16x8ram_8_out_7),
    .in8(n16x8ram_9_out_7), .in9(n16x8ram_10_out_7), .in10(n16x8ram_11_out_7), .in11(n16x8ram_12_out_7),
    .in12(n16x8ram_13_out_7), .in13(n16x8ram_14_out_7), .in14(n16x8ram_15_out_7), .in15(n16x8ram_16_out_7),
    .out(out_7), .sel(in_5[7:4]));  // open: en
endmodule

module _1024x8RAM (
  input  [7:0] in_1,
  input  in_2,
  input  in_3,
  input  in_4,
  input  [9:0] in_5,
  input  [9:0] in_6,
  output [7:0] out_7
);

  wire [7:0] n256x8ram_1_out_7, n256x8ram_2_out_7, n256x8ram_3_out_7, n256x8ram_4_out_7;
  wire [8:0] demultiplexer_1_out0, demultiplexer_1_out1, demultiplexer_1_out2, demultiplexer_1_out3;

  Demultiplexer #(.select(2), .width(9)) demultiplexer_1 (
    .out0(demultiplexer_1_out0), .out1(demultiplexer_1_out1), .out2(demultiplexer_1_out2),
    .out3(demultiplexer_1_out3), .in({in_4, in_1}), .sel(in_6[9:8]));  // open: en
  _256x8RAM u_256x8ram_1 (
    .in_3(demultiplexer_1_out0[7:0]), .out_7(n256x8ram_1_out_7), .in_4(demultiplexer_1_out0[8]), .in_1(in_2),
    .in_2(in_3), .in_6(in_6[7:0]), .in_5(in_5[7:0]));
  _256x8RAM u_256x8ram_2 (
    .in_3(demultiplexer_1_out1[7:0]), .out_7(n256x8ram_2_out_7), .in_4(demultiplexer_1_out1[8]), .in_1(in_2),
    .in_2(in_3), .in_6(in_6[7:0]), .in_5(in_5[7:0]));
  _256x8RAM u_256x8ram_3 (
    .in_3(demultiplexer_1_out2[7:0]), .out_7(n256x8ram_3_out_7), .in_4(demultiplexer_1_out2[8]), .in_1(in_2),
    .in_2(in_3), .in_6(in_6[7:0]), .in_5(in_5[7:0]));
  _256x8RAM u_256x8ram_4 (
    .in_3(demultiplexer_1_out3[7:0]), .out_7(n256x8ram_4_out_7), .in_4(demultiplexer_1_out3[8]), .in_1(in_2),
    .in_2(in_3), .in_6(in_6[7:0]), .in_5(in_5[7:0]));
  Multiplexer #(.select(2), .width(8)) multiplexer_1 (
    .in0(n256x8ram_1_out_7), .in1(n256x8ram_2_out_7), .in2(n256x8ram_3_out_7), .in3(n256x8ram_4_out_7),
    .out(out_7), .sel(in_5[9:8]));  // open: en
endmodule
