// Logisim project CBRLABtimer.circ as structural Verilog: 8 circuits, main circuit Rising Edge Detector
module main (
  input  in_1,
  input  in_2,
  output out_3,
  output out_4,
  output out_5,
  output out_6,
  output out_7,
  output out_8
);

  wire _0_out, button_2_out, button_3_out, button_4_out, button_out, clock_1_out, Go_out,
       input_handler_1_out_5, input_handler_1_out_6, multiplexer_1_out, or_1_out, t_ff_1_q,
       timer_core_1_out_13;
  wire [2:0] input_handler_1_out_7;
  wire [3:0] multiplexer_2_out_2, multiplexer_3_out, multiplexer_4_out_2, multiplexer_5_out_2,
       multiplexer_6_out, multiplexer_7_out_2, timer_core_1_out_7, timer_core_1_out_8, timer_core_1_out_9,
       timer_core_1_out_10, timer_core_1_out_11, timer_core_1_out_12;
  wire [3:1] multiplexer_2_out, multiplexer_3_out_2, multiplexer_4_out, multiplexer_5_out,
       multiplexer_6_out_2, multiplexer_7_out;
  wire [6:0] display_decoder_1_out_2, display_decoder_2_out_2, display_decoder_3_out_2,
       display_decoder_4_out_2, display_decoder_5_out_2, display_decoder_6_out_2;

  Clock clock_1 (.out(clock_1_out));
  Multiplexer #(.enable("false")) multiplexer_1 (.in0(clock_1_out), .in1(in_1), .out(multiplexer_1_out), .sel(in_2));
  T_Flip_Flop t_ff_1 (.clk(Go_out), .T(1'b1), .Q(t_ff_1_q), .reset(or_1_out));  // open: Qn, preset, en
  or or_1 (or_1_out, input_handler_1_out_6, input_handler_1_out_5);
  Button Go (.out(Go_out));
  Timer_Core timer_core_1 (
    .in_3(input_handler_1_out_5), .in_6(t_ff_1_q), .in_4(multiplexer_1_out), .out_7(timer_core_1_out_7),
    .in_5(_0_out), .out_8(timer_core_1_out_8), .out_9(timer_core_1_out_9), .out_10(timer_core_1_out_10),
    .out_11(timer_core_1_out_11), .out_12(timer_core_1_out_12), .in_1(input_handler_1_out_6),
    .in_2(input_handler_1_out_7), .out_13(timer_core_1_out_13));
  Input_Handler input_handler_1 (
    .in_2(button_4_out), .in_1(button_out), .in_4(button_2_out), .in_3(button_3_out),
    .out_7(input_handler_1_out_7), .out_5(input_handler_1_out_5), .out_6(input_handler_1_out_6));
  Button _0 (.out(_0_out));
  Button button (.out(button_out));
  Button button_2 (.out(button_2_out));
  Button button_3 (.out(button_3_out));
  Button button_4 (.out(button_4_out));
  Display_Decoder display_decoder_1 (.out_2(display_decoder_1_out_2), .in_1(timer_core_1_out_12));
  Multiplexer #(.width(7), .disabled(0), .enable("false")) multiplexer_2 (
    .in0(display_decoder_1_out_2), .in1({7{1'b0}}),
    .out({multiplexer_2_out[1], multiplexer_2_out[2], multiplexer_2_out[3], multiplexer_2_out_2}),
    .sel(timer_core_1_out_13));
  _7_Segment_Display u_7_segment_display_1 (
    .g(multiplexer_2_out_2[3]), .f(multiplexer_2_out_2[2]), .a(multiplexer_2_out_2[1]),
    .b(multiplexer_2_out_2[0]), .e(multiplexer_2_out[3]), .d(multiplexer_2_out[2]), .c(multiplexer_2_out[1]),
    .dp(1'b0));
  _7_Segment_Display u_7_segment_display_2 (
    .g(multiplexer_3_out[3]), .f(multiplexer_3_out[2]), .a(multiplexer_3_out[1]), .b(multiplexer_3_out[0]),
    .e(multiplexer_3_out_2[3]), .d(multiplexer_3_out_2[2]), .c(multiplexer_3_out_2[1]), .dp(1'b1));
  Demultiplexer #(.select(3), .enable("false")) demultiplexer_1 (
    .out0(out_8), .out1(out_7), .out2(out_6), .out3(out_5), .out4(out_4), .out5(out_3), .in(1'b1),
    .sel(input_handler_1_out_7));  // open: out6, out7
  Display_Decoder display_decoder_2 (.out_2(display_decoder_2_out_2), .in_1(timer_core_1_out_10));
  Display_Decoder display_decoder_3 (.out_2(display_decoder_3_out_2), .in_1(timer_core_1_out_11));
  Multiplexer #(.width(7), .disabled(0), .enable("false")) multiplexer_3 (
    .in0(display_decoder_3_out_2), .in1(7'b1111001),
    .out({multiplexer_3_out_2[1], multiplexer_3_out_2[2], multiplexer_3_out_2[3], multiplexer_3_out}),
    .sel(timer_core_1_out_13));
  Multiplexer #(.width(7), .disabled(0), .enable("false")) multiplexer_4 (
    .in0(display_decoder_2_out_2), .in1(7'b1111000),
    .out({multiplexer_4_out[1], multiplexer_4_out[2], multiplexer_4_out[3], multiplexer_4_out_2}),
    .sel(timer_core_1_out_13));
  _7_Segment_Display u_7_segment_display_3 (
    .g(multiplexer_4_out_2[3]), .f(multiplexer_4_out_2[2]), .a(multiplexer_4_out_2[1]),
    .b(multiplexer_4_out_2[0]), .e(multiplexer_4_out[3]), .d(multiplexer_4_out[2]), .c(multiplexer_4_out[1]),
    .dp(1'b0));
  Display_Decoder display_decoder_4 (.out_2(display_decoder_4_out_2), .in_1(timer_core_1_out_9));
  Multiplexer #(.width(7), .disabled(0), .enable("false")) multiplexer_5 (
    .in0(display_decoder_4_out_2), .in1(7'b1011000),
    .out({multiplexer_5_out[1], multiplexer_5_out[2], multiplexer_5_out[3], multiplexer_5_out_2}),
    .sel(timer_core_1_out_13));
  _7_Segment_Display u_7_segment_display_4 (
    .g(multiplexer_6_out[3]), .f(multiplexer_6_out[2]), .a(multiplexer_6_out[1]), .b(multiplexer_6_out[0]),
    .e(multiplexer_6_out_2[3]), .d(multiplexer_6_out_2[2]), .c(multiplexer_6_out_2[1]), .dp(1'b0));
  _7_Segment_Display u_7_segment_display_5 (
    .g(multiplexer_5_out_2[3]), .f(multiplexer_5_out_2[2]), .a(multiplexer_5_out_2[1]),
    .b(multiplexer_5_out_2[0]), .e(multiplexer_5_out[3]), .d(multiplexer_5_out[2]), .c(multiplexer_5_out[1]),
    .dp(1'b1));
  Display_Decoder display_decoder_5 (.out_2(display_decoder_5_out_2), .in_1(timer_core_1_out_7));
  Display_Decoder display_decoder_6 (.out_2(display_decoder_6_out_2), .in_1(timer_core_1_out_8));
  Multiplexer #(.width(7), .disabled(0), .enable("false")) multiplexer_6 (
    .in0(display_decoder_6_out_2), .in1(7'b0111110),
    .out({multiplexer_6_out_2[1], multiplexer_6_out_2[2], multiplexer_6_out_2[3], multiplexer_6_out}),
    .sel(timer_core_1_out_13));
  Multiplexer #(.width(7), .disabled(0), .enable("false")) multiplexer_7 (
    .in0(display_decoder_5_out_2), .in1({7{1'b0}}),
    .out({multiplexer_7_out[1], multiplexer_7_out[2], multiplexer_7_out[3], multiplexer_7_out_2}),
    .sel(timer_core_1_out_13));
  _7_Segment_Display u_7_segment_display_6 (
    .g(multiplexer_7_out_2[3]), .f(multiplexer_7_out_2[2]), .a(multiplexer_7_out_2[1]),
    .b(multiplexer_7_out_2[0]), .e(multiplexer_7_out[3]), .d(multiplexer_7_out[2]), .c(multiplexer_7_out[1]),
    .dp(1'b0));
endmodule

module Rising_Edge_Detector (
  input  in_1,
  output out_2
);

  wire not_1_out, not_2_out, not_3_out;

  not not_1 (not_1_out, in_1);
  not not_2 (not_2_out, not_1_out);
  not not_3 (not_3_out, not_2_out);
  and and_1 (out_2, not_3_out, in_1);
endmodule

module _4_Bit_Counter (
  input  Up_Down,
  input  Clock,
  input  Toggle,
  input  Clear,
  input  Write,
  input  [3:0] Input,
  output [3:0] Output
);

  wire and_1_out, and_2_out, and_3_out, and_4_out, and_5_out, and_6_out, demultiplexer_1_out0,
       demultiplexer_1_out1, demultiplexer_2_out0, demultiplexer_2_out1, demultiplexer_3_out0,
       demultiplexer_3_out1, demultiplexer_4_out0, demultiplexer_4_out1, or_1_out, or_2_out, or_3_out,
       or_4_out, or_5_out, or_6_out, or_7_out, t_ff_1_qn, t_ff_2_qn, t_ff_3_qn;
  wire [3:0] not_1_out;

  // Probe on Output
  T_Flip_Flop t_ff_1 (
    .clk(Clock), .T(1'b1), .Q(Output[0]), .Qn(t_ff_1_qn), .preset(demultiplexer_1_out0), .reset(or_1_out),
    .en(Toggle));
  or or_1 (or_1_out, Clear, demultiplexer_1_out1);
  Demultiplexer #(.enable("false")) demultiplexer_1 (
    .out0(demultiplexer_1_out0), .out1(demultiplexer_1_out1), .in(Write), .sel(not_1_out[0]));
  assign not_1_out = ~Input;  // NOT_Gate not_1, 4 bits wide
  and and_1 (and_1_out, Up_Down, Output[0]);
  and and_2 (and_2_out, t_ff_1_qn, ~Up_Down);  // AND_Gate
  T_Flip_Flop t_ff_2 (
    .clk(Clock), .T(or_2_out), .Q(Output[1]), .Qn(t_ff_2_qn), .preset(demultiplexer_2_out0),
    .reset(or_3_out), .en(Toggle));
  or or_2 (or_2_out, and_1_out, and_2_out);
  or or_3 (or_3_out, Clear, demultiplexer_2_out1);
  Demultiplexer #(.enable("false")) demultiplexer_2 (
    .out0(demultiplexer_2_out0), .out1(demultiplexer_2_out1), .in(Write), .sel(not_1_out[1]));
  and and_3 (and_3_out, and_1_out, Output[1]);
  and and_4 (and_4_out, t_ff_2_qn, and_2_out);
  T_Flip_Flop t_ff_3 (
    .clk(Clock), .T(or_4_out), .Q(Output[2]), .Qn(t_ff_3_qn), .preset(demultiplexer_3_out0),
    .reset(or_5_out), .en(Toggle));
  or or_4 (or_4_out, and_3_out, and_4_out);
  or or_5 (or_5_out, Clear, demultiplexer_3_out1);
  Demultiplexer #(.enable("false")) demultiplexer_3 (
    .out0(demultiplexer_3_out0), .out1(demultiplexer_3_out1), .in(Write), .sel(not_1_out[2]));
  and and_5 (and_5_out, and_3_out, Output[2]);
  and and_6 (and_6_out, t_ff_3_qn, and_4_out);
  T_Flip_Flop t_ff_4 (
    .clk(Clock), .T(or_6_out), .Q(Output[3]), .preset(demultiplexer_4_out0), .reset(or_7_out), .en(Toggle));  // open: Qn
  or or_6 (or_6_out, and_5_out, and_6_out);
  or or_7 (or_7_out, Clear, demultiplexer_4_out1);
  Demultiplexer #(.enable("false")) demultiplexer_4 (
    .out0(demultiplexer_4_out0), .out1(demultiplexer_4_out1), .in(Write), .sel(not_1_out[3]));
endmodule

module \Сomparator  (
  input  [3:0] in_1,
  input  [3:0] in_2,
  output out_3
);

  wire [3:0] xnor_1_out;

  assign xnor_1_out = ~(in_1 ^ in_2);  // XNOR_Gate xnor_1, 4 bits wide
  and and_1 (out_3, xnor_1_out[0], xnor_1_out[1], xnor_1_out[2], xnor_1_out[3]);
endmodule

module Clamped_4_Bit_Counter (
  input  in_1,
  input  [3:0] in_2,
  input  [3:0] in_3,
  input  in_4,
  input  in_5,
  input  in_6,
  input  in_7,
  input  in_8,
  output out_9,
  output out_10,
  output [3:0] out_11,
  output out_12,
  output out_13
);

  wire or_1_out, or_2_out, or_3_out, or_4_out, rising_edge_detector_1_out_2, \сomparator_1_out_3 ;
  wire [0:0] not_1_out;
  wire [3:0] adder_1_out, demultiplexer_1_out0, demultiplexer_1_out1, multiplexer_1_out;

  Rising_Edge_Detector rising_edge_detector_1 (.in_1(in_5), .out_2(rising_edge_detector_1_out_2));
  or or_1 (or_1_out, rising_edge_detector_1_out_2, in_6);
  not not_1 (not_1_out[0], in_1);
  Multiplexer #(.select(2), .width(4), .disabled(0), .enable("false")) multiplexer_1 (
    .in0(4'b0000), .in1(in_2), .in2(in_3), .in3(in_3), .out(multiplexer_1_out), .sel({in_4, not_1_out[0]}));
  or or_2 (or_2_out, in_4, or_4_out);
  or or_3 (or_3_out, in_7, in_6);
  Demultiplexer #(.width(4), .disabled(0), .enable("false")) demultiplexer_1 (
    .out0(demultiplexer_1_out0), .out1(demultiplexer_1_out1), .in(out_11), .sel(in_1));
  _4_Bit_Counter u_4_bit_counter_1 (
    .Up_Down(in_1), .Clock(or_1_out), .Toggle(or_3_out), .Clear(in_8), .Write(or_2_out), .Output(out_11),
    .Input(multiplexer_1_out));
  // Probe on out_11
  \Сomparator  \u_сomparator_1  (.in_1(demultiplexer_1_out0), .in_2(4'b0000), .out_3(\сomparator_1_out_3 ));
  \Сomparator  \u_сomparator_2  (.in_1(demultiplexer_1_out1), .in_2(in_2), .out_3(out_12));
  \Сomparator  \u_сomparator_3  (.in_1(demultiplexer_1_out0), .in_2(4'b1111), .out_3(out_9));
  and and_1 (out_10, ~in_1, \сomparator_1_out_3 );  // AND_Gate
  \Сomparator  \u_сomparator_4  (.in_1(adder_1_out), .in_2(demultiplexer_1_out1), .out_3(out_13));
  Adder #(.width(4)) adder_1 (.a(in_2), .b(4'b0001), .out(adder_1_out));  // open: cin, cout
  or or_4 (or_4_out, out_9, out_13);
endmodule

module Timer_Core (
  input  in_1,
  input  [2:0] in_2,
  input  in_3,
  input  in_4,
  input  in_5,
  input  in_6,
  output [3:0] out_7,
  output [3:0] out_8,
  output [3:0] out_9,
  output [3:0] out_10,
  output [3:0] out_11,
  output [3:0] out_12,
  output out_13
);

  wire and_1_out, and_2_out, and_3_out, and_4_out, and_5_out, and_6_out, and_7_out, and_8_out, and_9_out,
       and_10_out, clamped_4_bit_counter_1_out_10, clamped_4_bit_counter_2_out_10,
       clamped_4_bit_counter_3_out_10, clamped_4_bit_counter_4_out_10, clamped_4_bit_counter_5_out_10,
       clamped_4_bit_counter_6_out_10, demultiplexer_1_out0, demultiplexer_1_out1, demultiplexer_1_out2,
       demultiplexer_1_out3, demultiplexer_1_out4, demultiplexer_1_out5;

  // Probe on out_7
  Clamped_4_Bit_Counter clamped_4_bit_counter_1 (
    .in_2(4'b1001), .in_4(1'b0), .in_5(in_4), .out_10(clamped_4_bit_counter_1_out_10), .in_8(in_5),
    .in_1(in_3), .in_7(and_1_out), .out_11(out_7), .in_6(demultiplexer_1_out0));  // open: in_3, out_9, out_12, out_13
  and and_1 (and_1_out, in_6, ~out_13);  // AND_Gate
  Demultiplexer #(.select(3), .enable("false")) demultiplexer_1 (
    .out0(demultiplexer_1_out0), .out1(demultiplexer_1_out1), .out2(demultiplexer_1_out2),
    .out3(demultiplexer_1_out3), .out4(demultiplexer_1_out4), .out5(demultiplexer_1_out5), .in(in_1),
    .sel(in_2));  // open: out6, out7
  Clamped_4_Bit_Counter clamped_4_bit_counter_2 (
    .in_2(4'b0101), .in_4(1'b0), .in_5(in_4), .out_10(clamped_4_bit_counter_2_out_10), .in_8(in_5),
    .in_1(in_3), .in_7(and_2_out), .out_11(out_8), .in_6(demultiplexer_1_out1));  // open: in_3, out_9, out_12, out_13
  // Probe on out_8
  and and_2 (and_2_out, and_1_out, clamped_4_bit_counter_1_out_10);
  // Probe on out_9
  Clamped_4_Bit_Counter clamped_4_bit_counter_3 (
    .in_2(4'b1001), .in_4(1'b0), .in_5(in_4), .out_10(clamped_4_bit_counter_3_out_10), .in_8(in_5),
    .in_1(in_3), .in_7(and_3_out), .out_11(out_9), .in_6(demultiplexer_1_out2));  // open: in_3, out_9, out_12, out_13
  and and_3 (and_3_out, and_1_out, and_4_out);
  and and_4 (and_4_out, clamped_4_bit_counter_2_out_10, clamped_4_bit_counter_1_out_10);
  // Probe on out_10
  Clamped_4_Bit_Counter clamped_4_bit_counter_4 (
    .in_2(4'b0101), .in_4(1'b0), .in_5(in_4), .out_10(clamped_4_bit_counter_4_out_10), .in_8(in_5),
    .in_1(in_3), .in_7(and_5_out), .out_11(out_10), .in_6(demultiplexer_1_out3));  // open: in_3, out_9, out_12, out_13
  and and_5 (and_5_out, and_1_out, and_6_out);
  and and_6 (and_6_out, clamped_4_bit_counter_3_out_10, and_4_out);
  Clamped_4_Bit_Counter clamped_4_bit_counter_5 (
    .in_2(4'b1001), .in_4(1'b0), .in_5(in_4), .out_10(clamped_4_bit_counter_5_out_10), .in_8(in_5),
    .in_1(in_3), .in_7(and_7_out), .out_11(out_11), .in_6(demultiplexer_1_out4));  // open: in_3, out_9, out_12, out_13
  // Probe on out_11
  and and_7 (and_7_out, and_1_out, and_8_out);
  and and_8 (and_8_out, clamped_4_bit_counter_4_out_10, and_6_out);
  Clamped_4_Bit_Counter clamped_4_bit_counter_6 (
    .in_2(4'b1001), .in_4(1'b0), .in_5(in_4), .out_10(clamped_4_bit_counter_6_out_10), .in_8(in_5),
    .in_1(in_3), .in_7(and_9_out), .out_11(out_12), .in_6(demultiplexer_1_out5));  // open: in_3, out_9, out_12, out_13
  // Probe on out_12
  and and_9 (and_9_out, and_1_out, and_10_out);
  and and_10 (and_10_out, clamped_4_bit_counter_5_out_10, and_8_out);
  and and_11 (out_13, clamped_4_bit_counter_6_out_10, and_10_out);

  // Other names for the same wires on the sheet: AtLimit = out_13
endmodule

module Input_Handler (
  input  in_1,
  input  in_2,
  input  in_3,
  input  in_4,
  output out_5,
  output out_6,
  output [2:0] out_7
);

  wire not_1_out, not_2_out, or_1_out;
  wire [3:3] clamped_4_bit_counter_1_out_11;

  or or_1 (or_1_out, in_3, in_4);
  not not_1 (not_1_out, or_1_out);
  not not_2 (not_2_out, not_1_out);
  Clamped_4_Bit_Counter clamped_4_bit_counter_1 (
    .in_2(4'b0101), .in_4(1'b0), .in_5(1'b0), .in_8(1'b0), .in_1(in_3), .in_7(1'b0),
    .out_11({clamped_4_bit_counter_1_out_11[3], out_7}), .in_6(not_2_out));  // open: in_3, out_9, out_10, out_12, out_13
  or or_2 (out_6, in_1, in_2);

  assign out_5 = in_1;
endmodule

module Display_Decoder (
  input  [3:0] in_1,
  output [6:0] out_2
);

  Multiplexer #(.select(4), .width(7), .disabled(0), .enable("false")) multiplexer_1 (
    .in0(7'b1110111), .in1(7'b1000001), .in2(7'b0111011), .in3(7'b1101011), .in4(7'b1001101),
    .in5(7'b1101110), .in6(7'b1111110), .in7(7'b1000011), .in8({7{1'b1}}), .in9(7'b1101111), .out(out_2),
    .sel(in_1));  // open: in10, in11, in12, in13, in14, in15
endmodule
