// Logisim project LAB1.circ as structural Verilog: 11 circuits, main circuit main
module main (
  input  in_1,
  input  in_2,
  input  in_3,
  input  in_4,
  input  in_5,
  input  in_6,
  input  in_7,
  input  in_8,
  input  in_9,
  input  in_10,
  input  in_11,
  input  in_12,
  output [1:0] out_13,
  output [1:0] out_14,
  output [1:0] out_15,
  output [1:0] out_16,
  output [1:0] out_17,
  output out_18
);

  wire clock_1_out, clock_2_out, multiplexer_1_out, multiplexer_2_out;
  wire [1:0] crossing_1_state;
  wire [2:0] platformer_jump_controller_1_state;

  Clock clock_1 (.out(clock_1_out));
  Multiplexer #(.enable("false")) multiplexer_1 (.in0(clock_1_out), .in1(in_1), .out(multiplexer_1_out), .sel(in_2));
  Clock clock_2 (.out(clock_2_out));
  Multiplexer #(.enable("false")) multiplexer_2 (.in0(clock_2_out), .in1(in_8), .out(multiplexer_2_out), .sel(in_9));
  // Probe on crossing_1_state
  crossing crossing_1 (
    .Ta(in_3), .Tb(in_4), .BTa(in_5), .BTb(in_6), .State(crossing_1_state), .Clock(multiplexer_1_out),
    .RESET(in_7));
  PJC_Decoder pjc_decoder_1 (.Gravity_Mode(out_17), .Motion_Mode(out_18), .in_1(platformer_jump_controller_1_state));
  Platformer_Jump_Controller platformer_jump_controller_1 (
    .iJ(in_10), .iF(in_11), .State(platformer_jump_controller_1_state), .Clock(multiplexer_2_out),
    .RESET(in_12));
  // Probe on platformer_jump_controller_1_state
  Crossing_Decoder crossing_decoder_1 (.in_1(crossing_1_state), .La(out_13), .Lb(out_14), .Pa(out_15), .Pb(out_16));
endmodule

module crossing (
  input  Ta,
  input  Clock,
  input  Tb,
  input  RESET,
  input  BTa,
  input  BTb,
  output [1:0] State
);

  wire [1:0] cr_s0_1_out_3, cr_s2_1_out_3, multiplexer_1_out;

  cr_s0 cr_s0_1 (.a(Ta), .b(BTa), .out_3(cr_s0_1_out_3));
  cr_s2 cr_s2_1 (.in_1(Tb), .in_2(BTb), .out_3(cr_s2_1_out_3));
  Register #(.width(2)) register_1 (.D(multiplexer_1_out), .Q(State), .clk(Clock), .clr(RESET));  // open: en
  Multiplexer #(.select(2), .width(2), .enable("false")) multiplexer_1 (
    .in0(cr_s0_1_out_3), .in1(2'b10), .in2(cr_s2_1_out_3), .in3(2'b00), .out(multiplexer_1_out), .sel(State));
endmodule

module cr_s0 (
  input  a,
  input  b,
  output [1:0] out_3
);

  wire not_1_out;

  not not_1 (not_1_out, a);
  or or_1 (out_3[0], not_1_out, b);

  assign out_3[1] = 1'b0;
endmodule

module cr_s2 (
  input  in_1,
  input  in_2,
  output [1:0] out_3
);

  wire not_1_out;

  not not_1 (not_1_out, in_1);
  or or_1 (out_3[0], not_1_out, in_2);

  assign out_3[1] = 1'b1;
endmodule

module Crossing_Decoder (
  input  [1:0] in_1,
  output [1:0] La,
  output [1:0] Lb,
  output [1:0] Pa,
  output [1:0] Pb
);

  Multiplexer #(.select(2), .width(8), .enable("false")) multiplexer_1 (
    .in0(8'h28), .in1(8'ha9), .in2(8'h82), .in3(8'ha6), .out({Pb, Pa, Lb, La}), .sel(in_1));
endmodule

module Platformer_Jump_Controller (
  input  Clock,
  input  iJ,
  input  iF,
  input  RESET,
  output [2:0] State
);

  wire [2:0] jc_s0_1_out_3, jc_s1_1_out_3, jc_s3_1_out_3, jc_s4_1_out_3, multiplexer_1_out;

  jc_s4 jc_s4_1 (.iJ(iJ), .iF(iF), .out_3(jc_s4_1_out_3));
  jc_s0 jc_s0_1 (.iJ(iJ), .iF(iF), .out_3(jc_s0_1_out_3));
  jc_s1 jc_s1_1 (.iJ(iJ), .iF(iF), .out_3(jc_s1_1_out_3));
  jc_s3 jc_s3_1 (.iJ(iJ), .iF(iF), .out_3(jc_s3_1_out_3));
  Register #(.width(3)) register_1 (.D(multiplexer_1_out), .Q(State), .clk(Clock), .clr(RESET));  // open: en
  Multiplexer #(.select(3), .width(3), .enable("false")) multiplexer_1 (
    .in0(jc_s0_1_out_3), .in1(jc_s1_1_out_3), .in2(3'b011), .in3(jc_s3_1_out_3), .in4(jc_s4_1_out_3),
    .in5(3'b000), .in6(3'b000), .in7(3'b000), .out(multiplexer_1_out), .sel(State));
endmodule

module jc_s0 (
  input  iJ,
  input  iF,
  output [2:0] out_3
);

  wire not_1_out, not_2_out;

  not not_1 (not_1_out, iJ);
  not not_2 (not_2_out, iF);
  and and_1 (out_3[0], not_1_out, not_2_out);

  assign out_3[2:1] = {1'b0, iJ};
endmodule

module jc_s1 (
  input  iJ,
  input  iF,
  output [2:0] out_3
);

  wire not_1_out, not_2_out, not_3_out;

  not not_1 (not_1_out, iF);
  not not_2 (not_2_out, iJ);
  not not_3 (not_3_out, iF);
  or or_1 (out_3[1], not_1_out, iJ);
  and and_1 (out_3[0], not_2_out, not_3_out);

  assign out_3[2] = 1'b0;
endmodule

module jc_s3 (
  input  iJ,
  input  iF,
  output [2:0] out_3
);

  wire and_2_out, and_3_out, not_1_out, not_2_out, not_3_out, not_4_out, not_5_out;

  not not_1 (not_1_out, iF);
  not not_2 (not_2_out, iJ);
  not not_3 (not_3_out, iF);
  not not_4 (not_4_out, iJ);
  not not_5 (not_5_out, iF);
  and and_1 (out_3[2], iJ, not_1_out);
  and and_2 (and_2_out, not_2_out, not_3_out);
  and and_3 (and_3_out, iJ, iF);
  and and_4 (out_3[0], not_4_out, not_5_out);
  or or_1 (out_3[1], and_2_out, and_3_out);
endmodule

module jc_s4 (
  input  iJ,
  input  iF,
  output [2:0] out_3
);

  wire not_1_out, not_2_out, not_3_out, not_4_out;

  not not_1 (not_1_out, iF);
  not not_2 (not_2_out, iJ);
  not not_3 (not_3_out, iJ);
  not not_4 (not_4_out, iF);
  and and_1 (out_3[2], iJ, not_1_out);
  or or_1 (out_3[1], not_2_out, iF);
  and and_2 (out_3[0], not_3_out, not_4_out);
endmodule

module PJC_Decoder (
  input  [2:0] in_1,
  output [1:0] Gravity_Mode,
  output Motion_Mode
);

  Multiplexer #(.select(3), .width(3), .enable("false")) multiplexer_1 (
    .in0(3'b000), .in1(3'b101), .in2(3'b101), .in3(3'b110), .in4(3'b110), .in5(3'b000), .in6(3'b000),
    .in7(3'b000), .out({Motion_Mode, Gravity_Mode}), .sel(in_1));
endmodule
